// Logisim project CPU.circ as structural Verilog: 36 circuits, main circuit CPU: ALU + RAM + ROM
module ALU_direct (
  input  [7:0] X,
  input  [7:0] Y,
  input  [4:0] ALU_Op,
  output [7:0] out_4
);

  wire [5:0] alu8_1_flags;
  wire [6:0] op_dec_1_col_0, op_dec_1_col_1, op_dec_1_col_2, op_dec_1_col_3, op_dec_1_col_4, op_dec_1_col_5,
       op_dec_1_col_6, op_dec_1_col_7, op_dec_1_col_8, op_dec_1_col_9, op_dec_1_col_10, op_dec_1_col_11,
       op_dec_1_col_12, op_dec_1_col_13;

  DotMatrix #(.matrixcols(14)) dotmatrix_1 (
    .col0(op_dec_1_col_0), .col1(op_dec_1_col_1), .col2(op_dec_1_col_2), .col3(op_dec_1_col_3),
    .col4(op_dec_1_col_4), .col5(op_dec_1_col_5), .col6(op_dec_1_col_6), .col7(op_dec_1_col_7),
    .col8(op_dec_1_col_8), .col9(op_dec_1_col_9), .col10(op_dec_1_col_10), .col11(op_dec_1_col_11),
    .col12(op_dec_1_col_12), .col13(op_dec_1_col_13));
  op_dec op_dec_1 (
    .op(ALU_Op), .col_0(op_dec_1_col_0), .col_7(op_dec_1_col_7), .col_1(op_dec_1_col_1),
    .col_8(op_dec_1_col_8), .col_2(op_dec_1_col_2), .col_9(op_dec_1_col_9), .col_3(op_dec_1_col_3),
    .col_10(op_dec_1_col_10), .col_4(op_dec_1_col_4), .col_11(op_dec_1_col_11), .col_5(op_dec_1_col_5),
    .col_12(op_dec_1_col_12), .col_6(op_dec_1_col_6), .col_13(op_dec_1_col_13));
  Hex_Digit_Display hex_digit_display_1 (.value(X[7:4]));  // open: dp
  Hex_Digit_Display hex_digit_display_2 (.value(X[3:0]));  // open: dp
  ALU8 alu8_1 (.x(X), .y(Y), .op(ALU_Op), .z(out_4), .flags(alu8_1_flags));  // open: aux_in, aux_out, aux_enabled
  Hex_Digit_Display hex_digit_display_3 (.value(Y[3:0]));  // open: dp
  Hex_Digit_Display hex_digit_display_4 (.value(Y[7:4]));  // open: dp
  // Probe on alu8_1_flags
  Hex_Digit_Display hex_digit_display_5 (.value(out_4[7:4]));  // open: dp
  Hex_Digit_Display hex_digit_display_6 (.value(out_4[3:0]));  // open: dp

  // Notes on the sheet:
  //   00000 NOP
  //   00001 XOR
  //   00010 AND
  //   00011 OR
  //   00100 NOT X
  //   00101 NOT Y
  //   00110 X
  //   00111 Y
  //   01000 ADD
  //   01001 SUB
  //   01010 INC
  //   01011 DEC
  //   01100 MUL
  //   01101 DIV
  //   01110 -X
  //   01111 X LSH Y
  //   10000 0
  //   10001 1
  //   10010 2
  //   10011 3
  //   10100 4
  //   10101 5
  //   10110 6
  //   10111 7
  //   11000 8 
  //   11001 9
  //   11001 10
  //   11011 16
  //   11100 32
  //   11101 64
  //   11110 128
  //   11111 -1
endmodule

module ALU (
  input  [7:0] X,
  input  [7:0] Y,
  input  [4:0] ALU_Op,
  output [7:0] out_4
);

  wire button_1_out;
  wire [5:0] alu8_1_flags, Flags_q;
  wire [6:0] op_dec_1_col_0, op_dec_1_col_1, op_dec_1_col_2, op_dec_1_col_3, op_dec_1_col_4, op_dec_1_col_5,
       op_dec_1_col_6, op_dec_1_col_7, op_dec_1_col_8, op_dec_1_col_9, op_dec_1_col_10, op_dec_1_col_11,
       op_dec_1_col_12, op_dec_1_col_13;
  wire [7:0] alu8_1_z, X_q, Y_q;

  Button button_1 (.out(button_1_out));
  op_dec op_dec_1 (
    .op(ALU_Op), .col_0(op_dec_1_col_0), .col_7(op_dec_1_col_7), .col_1(op_dec_1_col_1),
    .col_8(op_dec_1_col_8), .col_2(op_dec_1_col_2), .col_9(op_dec_1_col_9), .col_3(op_dec_1_col_3),
    .col_10(op_dec_1_col_10), .col_4(op_dec_1_col_4), .col_11(op_dec_1_col_11), .col_5(op_dec_1_col_5),
    .col_12(op_dec_1_col_12), .col_6(op_dec_1_col_6), .col_13(op_dec_1_col_13));
  DotMatrix #(.matrixcols(14)) dotmatrix_1 (
    .col0(op_dec_1_col_0), .col1(op_dec_1_col_1), .col2(op_dec_1_col_2), .col3(op_dec_1_col_3),
    .col4(op_dec_1_col_4), .col5(op_dec_1_col_5), .col6(op_dec_1_col_6), .col7(op_dec_1_col_7),
    .col8(op_dec_1_col_8), .col9(op_dec_1_col_9), .col10(op_dec_1_col_10), .col11(op_dec_1_col_11),
    .col12(op_dec_1_col_12), .col13(op_dec_1_col_13));
  Register #(.trigger("falling"), .Select("low")) u_Y (.D(Y), .Q(Y_q), .clk(button_1_out));  // open: en, clr
  Register #(.trigger("falling"), .Select("low")) u_X (.D(X), .Q(X_q), .clk(button_1_out));  // open: en, clr
  ALU8 alu8_1 (
    .x(X_q), .y(Y_q), .op(ALU_Op), .z(alu8_1_z), .flags(alu8_1_flags));  // open: aux_in, aux_out, aux_enabled
  Register #(.Select("low")) Z (.D(alu8_1_z), .en(1'b1), .Q(out_4), .clk(button_1_out));  // open: clr
  // Probe on Flags_q
  Register #(.width(6), .Select("low")) Flags (
    .D(alu8_1_flags), .en(1'b1), .Q(Flags_q), .clk(button_1_out));  // open: clr

  // Notes on the sheet:
  //   00000 NOP
  //   00001 XOR
  //   00010 AND
  //   00011 OR
  //   00100 NOT X
  //   00101 NOT Y
  //   00110 X
  //   00111 Y
  //   01000 ADD
  //   01001 SUB
  //   01010 INC
  //   01011 DEC
  //   01100 MUL
  //   01101 DIV
  //   01110 -X
  //   01111 X LSH Y
  //   10000 0
  //   10001 1
  //   10010 2
  //   10011 3
  //   10100 4
  //   10101 5
  //   10110 6
  //   10111 7
  //   11000 8 
  //   11001 9
  //   11001 10
  //   11011 16
  //   11100 32
  //   11101 64
  //   11110 128
  //   11111 -1
endmodule

module ALU___Reg (
  input  [3:0] X_Bus,
  input  [4:0] Y_Bus,
  input  [5:0] Z_Bus,
  input  [4:0] ALU_Op,
  input  Run
);

  wire button_1_out, clock2_1_calc, clock2_1_fetch, clock2_1_store, xy_bus_1_enable_x, xy_bus_1_enable_y,
       z_bus_1_r0_enable, z_bus_1_r1_enabel, z_bus_1_r2_enable, z_bus_1_r3_enable;
  wire [5:0] alu8_1_flags, Flags_q;
  wire [6:0] op_dec_1_col_0, op_dec_1_col_1, op_dec_1_col_2, op_dec_1_col_3, op_dec_1_col_4, op_dec_1_col_5,
       op_dec_1_col_6, op_dec_1_col_7, op_dec_1_col_8, op_dec_1_col_9, op_dec_1_col_10, op_dec_1_col_11,
       op_dec_1_col_12, op_dec_1_col_13;
  wire [7:0] alu8_1_z, R0_q, R1_q, R2_q, R3_q, X_q, xy_bus_1_x, xy_bus_1_y, Y_q, z_bus_1_r0, z_bus_1_r1,
       z_bus_1_r2, z_bus_1_r3, Z_q;

  Button button_1 (.out(button_1_out));
  Z_Bus z_bus_1 (
    .Z(Z_q), .Z_Selector(Z_Bus), .R0(z_bus_1_r0), .R0_Enable(z_bus_1_r0_enable), .R1(z_bus_1_r1),
    .R1_Enabel(z_bus_1_r1_enabel), .R2(z_bus_1_r2), .R2_Enable(z_bus_1_r2_enable), .R3(z_bus_1_r3),
    .R3_Enable(z_bus_1_r3_enable));  // open: MDR, MDR_Enable, MAR, MAR_Enable
  LED Fetch (.in(clock2_1_fetch));
  Clock2 clock2_1 (
    .Step(button_1_out), .Run(Run), .Fetch(clock2_1_fetch), .Calc(clock2_1_calc), .Store(clock2_1_store));  // open: Write, Init
  DotMatrix #(.matrixcols(14)) dotmatrix_1 (
    .col0(op_dec_1_col_0), .col1(op_dec_1_col_1), .col2(op_dec_1_col_2), .col3(op_dec_1_col_3),
    .col4(op_dec_1_col_4), .col5(op_dec_1_col_5), .col6(op_dec_1_col_6), .col7(op_dec_1_col_7),
    .col8(op_dec_1_col_8), .col9(op_dec_1_col_9), .col10(op_dec_1_col_10), .col11(op_dec_1_col_11),
    .col12(op_dec_1_col_12), .col13(op_dec_1_col_13));
  op_dec op_dec_1 (
    .op(ALU_Op), .col_0(op_dec_1_col_0), .col_7(op_dec_1_col_7), .col_1(op_dec_1_col_1),
    .col_8(op_dec_1_col_8), .col_2(op_dec_1_col_2), .col_9(op_dec_1_col_9), .col_3(op_dec_1_col_3),
    .col_10(op_dec_1_col_10), .col_4(op_dec_1_col_4), .col_11(op_dec_1_col_11), .col_5(op_dec_1_col_5),
    .col_12(op_dec_1_col_12), .col_6(op_dec_1_col_6), .col_13(op_dec_1_col_13));
  LED Calc (.in(clock2_1_calc));
  Register #(.Select("low")) R0 (.D(z_bus_1_r0), .en(z_bus_1_r0_enable), .Q(R0_q), .clk(clock2_1_store));  // open: clr
  Register #(.Select("low")) R1 (.D(z_bus_1_r1), .en(z_bus_1_r1_enabel), .Q(R1_q), .clk(clock2_1_store));  // open: clr
  Register #(.Select("low")) R2 (.D(z_bus_1_r2), .en(z_bus_1_r2_enable), .Q(R2_q), .clk(clock2_1_store));  // open: clr
  Register #(.Select("low")) R3 (.D(z_bus_1_r3), .en(z_bus_1_r3_enable), .Q(R3_q), .clk(clock2_1_store));  // open: clr
  LED Store (.in(clock2_1_store));
  XY_Bus xy_bus_1 (
    .R0(R0_q), .R1(R1_q), .R2(R2_q), .R3(R3_q), .Select_X(X_Bus), .Select_Y(Y_Bus), .X(xy_bus_1_x),
    .Y(xy_bus_1_y), .Enable_X(xy_bus_1_enable_x), .Enable_Y(xy_bus_1_enable_y));  // open: MDR
  Register #(.trigger("falling"), .Select("low")) Y (
    .D(xy_bus_1_y), .en(xy_bus_1_enable_y), .Q(Y_q), .clk(clock2_1_fetch));  // open: clr
  Register #(.trigger("falling"), .Select("low")) X (
    .D(xy_bus_1_x), .en(xy_bus_1_enable_x), .Q(X_q), .clk(clock2_1_fetch));  // open: clr
  ALU8 alu8_1 (
    .x(X_q), .y(Y_q), .aux_in(R3_q), .op(ALU_Op), .z(alu8_1_z), .flags(alu8_1_flags));  // open: aux_out, aux_enabled
  Register #(.Select("low")) Z (.D(alu8_1_z), .en(1'b1), .Q(Z_q), .clk(clock2_1_calc));  // open: clr
  // Probe on Flags_q
  Register #(.width(6), .Select("low")) Flags (
    .D(alu8_1_flags), .en(1'b1), .Q(Flags_q), .clk(clock2_1_calc));  // open: clr

  // Notes on the sheet:
  //   MDR, MAR, R3, R2, R1, R0
  //   00000 NOP
  //   00001 XOR
  //   00010 AND
  //   00011 OR
  //   00100 NOT X
  //   00101 NOT Y
  //   00110 X
  //   00111 Y
  //   01000 ADD
  //   01001 SUB
  //   01010 INC
  //   01011 DEC
  //   01100 MUL
  //   01101 DIV
  //   01110 -X
  //   01111 X LSH Y
  //   10000 0
  //   10001 1
  //   10010 2
  //   10011 3
  //   10100 4
  //   10101 5
  //   10110 6
  //   10111 7
  //   11000 8 
  //   11001 9
  //   11010 10
  //   11011 16
  //   11100 32
  //   11101 64
  //   11110 128
  //   11111 -1
endmodule

module ALU___Reg___AUX (
  input  [3:0] X_Bus,
  input  [4:0] Y_Bus,
  input  [5:0] Z_Bus,
  input  [4:0] ALU_Op,
  input  Run
);

  wire alu8_1_aux_enabled, aux_r3_1_enable, button_1_out, clock2_1_calc, clock2_1_fetch, clock2_1_store,
       clock2_1_write, xy_bus_1_enable_x, xy_bus_1_enable_y, z_bus_1_r0_enable, z_bus_1_r1_enabel,
       z_bus_1_r2_enable, z_bus_1_r3_enable;
  wire [5:0] alu8_1_flags, Flags_q;
  wire [6:0] op_dec_1_col_0, op_dec_1_col_1, op_dec_1_col_2, op_dec_1_col_3, op_dec_1_col_4, op_dec_1_col_5,
       op_dec_1_col_6, op_dec_1_col_7, op_dec_1_col_8, op_dec_1_col_9, op_dec_1_col_10, op_dec_1_col_11,
       op_dec_1_col_12, op_dec_1_col_13;
  wire [7:0] alu8_1_aux_out, alu8_1_z, aux_r3_1_r3, R0_q, R1_q, R2_q, R3_q, X_q, xy_bus_1_x, xy_bus_1_y, Y_q,
       z_bus_1_r0, z_bus_1_r1, z_bus_1_r2, z_bus_1_r3, Z_q;

  Button button_1 (.out(button_1_out));
  Z_Bus z_bus_1 (
    .Z(Z_q), .Z_Selector(Z_Bus), .R0(z_bus_1_r0), .R0_Enable(z_bus_1_r0_enable), .R1(z_bus_1_r1),
    .R1_Enabel(z_bus_1_r1_enabel), .R2(z_bus_1_r2), .R2_Enable(z_bus_1_r2_enable), .R3(z_bus_1_r3),
    .R3_Enable(z_bus_1_r3_enable));  // open: MDR, MDR_Enable, MAR, MAR_Enable
  LED Fetch (.in(clock2_1_fetch));
  Clock2 clock2_1 (
    .Step(button_1_out), .Run(Run), .Fetch(clock2_1_fetch), .Calc(clock2_1_calc), .Store(clock2_1_store),
    .Write(clock2_1_write));  // open: Init
  AUX_R3 aux_r3_1 (
    .AUX(alu8_1_aux_out), .Z(z_bus_1_r3), .Aux_Enable(alu8_1_aux_enabled), .Z_Enable(z_bus_1_r3_enable),
    .R3(aux_r3_1_r3), .Enable(aux_r3_1_enable));
  op_dec op_dec_1 (
    .op(ALU_Op), .col_0(op_dec_1_col_0), .col_7(op_dec_1_col_7), .col_1(op_dec_1_col_1),
    .col_8(op_dec_1_col_8), .col_2(op_dec_1_col_2), .col_9(op_dec_1_col_9), .col_3(op_dec_1_col_3),
    .col_10(op_dec_1_col_10), .col_4(op_dec_1_col_4), .col_11(op_dec_1_col_11), .col_5(op_dec_1_col_5),
    .col_12(op_dec_1_col_12), .col_6(op_dec_1_col_6), .col_13(op_dec_1_col_13));
  DotMatrix #(.matrixcols(14)) dotmatrix_1 (
    .col0(op_dec_1_col_0), .col1(op_dec_1_col_1), .col2(op_dec_1_col_2), .col3(op_dec_1_col_3),
    .col4(op_dec_1_col_4), .col5(op_dec_1_col_5), .col6(op_dec_1_col_6), .col7(op_dec_1_col_7),
    .col8(op_dec_1_col_8), .col9(op_dec_1_col_9), .col10(op_dec_1_col_10), .col11(op_dec_1_col_11),
    .col12(op_dec_1_col_12), .col13(op_dec_1_col_13));
  LED Calc (.in(clock2_1_calc));
  Register #(.Select("low")) R0 (.D(z_bus_1_r0), .en(z_bus_1_r0_enable), .Q(R0_q), .clk(clock2_1_store));  // open: clr
  Register #(.Select("low")) R1 (.D(z_bus_1_r1), .en(z_bus_1_r1_enabel), .Q(R1_q), .clk(clock2_1_store));  // open: clr
  Register #(.Select("low")) R2 (.D(z_bus_1_r2), .en(z_bus_1_r2_enable), .Q(R2_q), .clk(clock2_1_store));  // open: clr
  Register #(.Select("low")) R3 (.D(aux_r3_1_r3), .en(aux_r3_1_enable), .Q(R3_q), .clk(clock2_1_store));  // open: clr
  LED Store (.in(clock2_1_store));
  XY_Bus xy_bus_1 (
    .R0(R0_q), .R1(R1_q), .R2(R2_q), .R3(R3_q), .Select_X(X_Bus), .Select_Y(Y_Bus), .X(xy_bus_1_x),
    .Y(xy_bus_1_y), .Enable_X(xy_bus_1_enable_x), .Enable_Y(xy_bus_1_enable_y));  // open: MDR
  LED Write (.in(clock2_1_write));
  Register #(.trigger("falling"), .Select("low")) X (
    .D(xy_bus_1_x), .en(xy_bus_1_enable_x), .Q(X_q), .clk(clock2_1_fetch));  // open: clr
  Register #(.trigger("falling"), .Select("low")) Y (
    .D(xy_bus_1_y), .en(xy_bus_1_enable_y), .Q(Y_q), .clk(clock2_1_fetch));  // open: clr
  ALU8 alu8_1 (
    .x(X_q), .y(Y_q), .aux_in(R3_q), .op(ALU_Op), .z(alu8_1_z), .aux_out(alu8_1_aux_out),
    .flags(alu8_1_flags), .aux_enabled(alu8_1_aux_enabled));
  Register #(.Select("low")) Z (.D(alu8_1_z), .en(1'b1), .Q(Z_q), .clk(clock2_1_calc));  // open: clr
  // Probe on Flags_q
  Register #(.width(6), .Select("low")) Flags (
    .D(alu8_1_flags), .en(1'b1), .Q(Flags_q), .clk(clock2_1_calc));  // open: clr

  // Notes on the sheet:
  //   00000 NOP
  //   00001 XOR
  //   00010 AND
  //   00011 OR
  //   00100 NOT X
  //   00101 NOT Y
  //   00110 X
  //   00111 Y
  //   01000 ADD
  //   01001 SUB
  //   01010 INC
  //   01011 DEC
  //   01100 MUL
  //   01101 DIV
  //   01110 -X
  //   01111 X LSH Y
  //   10000 0
  //   10001 1
  //   10010 2
  //   10011 3
  //   10100 4
  //   10101 5
  //   10110 6
  //   10111 7
  //   11000 8 
  //   11001 9
  //   11010 10
  //   11011 16
  //   11100 32
  //   11101 64
  //   11110 128
  //   11111 -1
endmodule

module ALU___Reg___RAM (
  input  Read,
  input  Write,
  input  [3:0] X_Bus,
  input  [4:0] Y_Bus,
  input  [5:0] Z_Bus,
  input  [4:0] ALU_Op,
  input  Run
);

  wire alu8_1_aux_enabled, aux_r3_1_enable, clock2_1_calc, clock2_1_fetch, clock2_1_store, clock2_1_write,
       mdr_selector_1_clock, mdr_selector_1_mdr_en, Step_out, xy_bus_1_enable_x, xy_bus_1_enable_y,
       z_bus_1_mar_enable, z_bus_1_mdr_enable, z_bus_1_r0_enable, z_bus_1_r1_enabel, z_bus_1_r2_enable,
       z_bus_1_r3_enable;
  wire [5:0] alu8_1_flags, Flags_q;
  wire [6:0] op_dec_1_col_0, op_dec_1_col_1, op_dec_1_col_2, op_dec_1_col_3, op_dec_1_col_4, op_dec_1_col_5,
       op_dec_1_col_6, op_dec_1_col_7, op_dec_1_col_8, op_dec_1_col_9, op_dec_1_col_10, op_dec_1_col_11,
       op_dec_1_col_12, op_dec_1_col_13;
  wire [7:0] alu8_1_aux_out, alu8_1_z, aux_r3_1_r3, MAR_q, MDR_q, mdr_selector_1_mdr_d, R0_q, R1_q, R2_q,
       R3_q, ram_1_data, X_q, xy_bus_1_x, xy_bus_1_y, Y_q, z_bus_1_mar, z_bus_1_mdr, z_bus_1_r0, z_bus_1_r1,
       z_bus_1_r2, z_bus_1_r3, Z_q;

  Button Step (.out(Step_out));
  Z_Bus z_bus_1 (
    .Z(Z_q), .Z_Selector(Z_Bus), .MDR(z_bus_1_mdr), .MDR_Enable(z_bus_1_mdr_enable), .MAR(z_bus_1_mar),
    .MAR_Enable(z_bus_1_mar_enable), .R0(z_bus_1_r0), .R0_Enable(z_bus_1_r0_enable), .R1(z_bus_1_r1),
    .R1_Enabel(z_bus_1_r1_enabel), .R2(z_bus_1_r2), .R2_Enable(z_bus_1_r2_enable), .R3(z_bus_1_r3),
    .R3_Enable(z_bus_1_r3_enable));
  LED Fetch (.in(clock2_1_fetch));
  Clock2 clock2_1 (
    .Step(Step_out), .Run(Run), .Fetch(clock2_1_fetch), .Calc(clock2_1_calc), .Store(clock2_1_store),
    .Write(clock2_1_write));  // open: Init
  AUX_R3 aux_r3_1 (
    .AUX(alu8_1_aux_out), .Z(z_bus_1_r3), .Aux_Enable(alu8_1_aux_enabled), .Z_Enable(z_bus_1_r3_enable),
    .R3(aux_r3_1_r3), .Enable(aux_r3_1_enable));
  op_dec op_dec_1 (
    .op(ALU_Op), .col_0(op_dec_1_col_0), .col_7(op_dec_1_col_7), .col_1(op_dec_1_col_1),
    .col_8(op_dec_1_col_8), .col_2(op_dec_1_col_2), .col_9(op_dec_1_col_9), .col_3(op_dec_1_col_3),
    .col_10(op_dec_1_col_10), .col_4(op_dec_1_col_4), .col_11(op_dec_1_col_11), .col_5(op_dec_1_col_5),
    .col_12(op_dec_1_col_12), .col_6(op_dec_1_col_6), .col_13(op_dec_1_col_13));
  DotMatrix #(.matrixcols(14)) dotmatrix_1 (
    .col0(op_dec_1_col_0), .col1(op_dec_1_col_1), .col2(op_dec_1_col_2), .col3(op_dec_1_col_3),
    .col4(op_dec_1_col_4), .col5(op_dec_1_col_5), .col6(op_dec_1_col_6), .col7(op_dec_1_col_7),
    .col8(op_dec_1_col_8), .col9(op_dec_1_col_9), .col10(op_dec_1_col_10), .col11(op_dec_1_col_11),
    .col12(op_dec_1_col_12), .col13(op_dec_1_col_13));
  LED Calc (.in(clock2_1_calc));
  Register #(.Select("low")) R0 (.D(z_bus_1_r0), .en(z_bus_1_r0_enable), .Q(R0_q), .clk(clock2_1_store));  // open: clr
  Register #(.Select("low")) R1 (.D(z_bus_1_r1), .en(z_bus_1_r1_enabel), .Q(R1_q), .clk(clock2_1_store));  // open: clr
  Register #(.Select("low")) R2 (.D(z_bus_1_r2), .en(z_bus_1_r2_enable), .Q(R2_q), .clk(clock2_1_store));  // open: clr
  Register #(.Select("low")) R3 (.D(aux_r3_1_r3), .en(aux_r3_1_enable), .Q(R3_q), .clk(clock2_1_store));  // open: clr
  LED Store (.in(clock2_1_store));
  XY_Bus xy_bus_1 (
    .R0(R0_q), .R1(R1_q), .R2(R2_q), .R3(R3_q), .MDR(MDR_q), .Select_X(X_Bus), .Select_Y(Y_Bus),
    .X(xy_bus_1_x), .Y(xy_bus_1_y), .Enable_X(xy_bus_1_enable_x), .Enable_Y(xy_bus_1_enable_y));
  LED u_Write (.in(clock2_1_write));
  Register #(.Select("low")) MAR (
    .D(z_bus_1_mar), .en(z_bus_1_mar_enable), .Q(MAR_q), .clk(clock2_1_store));  // open: clr
  Register #(.trigger("falling"), .Select("low")) X (
    .D(xy_bus_1_x), .en(xy_bus_1_enable_x), .Q(X_q), .clk(clock2_1_fetch));  // open: clr
  Register #(.trigger("falling"), .Select("low")) Y (
    .D(xy_bus_1_y), .en(xy_bus_1_enable_y), .Q(Y_q), .clk(clock2_1_fetch));  // open: clr
  ALU8 alu8_1 (
    .x(X_q), .y(Y_q), .aux_in(R3_q), .op(ALU_Op), .z(alu8_1_z), .aux_out(alu8_1_aux_out),
    .flags(alu8_1_flags), .aux_enabled(alu8_1_aux_enabled));
  Register #(.Select("low")) Z (.D(alu8_1_z), .en(1'b1), .Q(Z_q), .clk(clock2_1_calc));  // open: clr
  // Probe on Flags_q
  Register #(.width(6), .Select("low")) Flags (
    .D(alu8_1_flags), .en(1'b1), .Q(Flags_q), .clk(clock2_1_calc));  // open: clr
  RAM #(.bus("separate"), .Select("high"), .simpleMode("false")) ram_1 (
    .addr(MAR_q), .din(MDR_q), .data(ram_1_data), .str(Write), .clk(clock2_1_write), .ld(Read));  // open: sel, clr
  MDR_Selector mdr_selector_1 (
    .RAM(ram_1_data), .Z(z_bus_1_mdr), .Read__RAM__MDR(Read), .Fetch_Phase(clock2_1_fetch),
    .Z__MDR(z_bus_1_mdr_enable), .Store_Phase(clock2_1_store), .MDR_D(mdr_selector_1_mdr_d),
    .MDR_En(mdr_selector_1_mdr_en), .Clock(mdr_selector_1_clock));
  Register #(.Select("low")) MDR (
    .D(mdr_selector_1_mdr_d), .en(mdr_selector_1_mdr_en), .Q(MDR_q), .clk(mdr_selector_1_clock));  // open: clr
  // Probe on z_bus_1_mar_enable
  // Probe on z_bus_1_mdr_enable

  // Notes on the sheet:
  //   MDR, MAR, R3, R2, R1, R0
  //   00000 NOP
  //   00001 XOR
  //   00010 AND
  //   00011 OR
  //   00100 NOT X
  //   00101 NOT Y
  //   00110 X
  //   00111 Y
  //   01000 ADD
  //   01001 SUB
  //   01010 INC
  //   01011 DEC
  //   01100 MUL
  //   01101 DIV
  //   01110 -X
  //   01111 X LSH Y
  //   10000 0
  //   10001 1
  //   10010 2
  //   10011 3
  //   10100 4
  //   10101 5
  //   10110 6
  //   10111 7
  //   11000 8 
  //   11001 9
  //   11010 10
  //   11011 16
  //   11100 32
  //   11101 64
  //   11110 128
  //   11111 -1
endmodule

module CPU__ALU___RAM___ROM (
  input  Run
);

  wire alu8_1_aux_enabled, aux_r3_1_enable, clock2_1_calc, clock2_1_fetch, clock2_1_init, clock2_1_store,
       clock2_1_write, mdr_selector_1_clock, mdr_selector_1_mdr_en, or_1_out, Step_out, xy_bus_1_enable_x,
       xy_bus_1_enable_y, z_bus_1_mar_enable, z_bus_1_mdr_enable, z_bus_1_r0_enable, z_bus_1_r1_enabel,
       z_bus_1_r2_enable, z_bus_1_r3_enable;
  wire [1:0] Control_q_6;
  wire [2:0] Control_q_5;
  wire [3:0] Control_q;
  wire [4:0] Control_q_2, Control_q_4;
  wire [5:0] Control_q_3, Control_q_7, Flags_q;
  wire [6:0] op_dec_1_col_0, op_dec_1_col_1, op_dec_1_col_2, op_dec_1_col_3, op_dec_1_col_4, op_dec_1_col_5,
       op_dec_1_col_6, op_dec_1_col_7, op_dec_1_col_8, op_dec_1_col_9, op_dec_1_col_10, op_dec_1_col_11,
       op_dec_1_col_12, op_dec_1_col_13;
  wire [7:0] address_calculator_1_ncar, alu8_1_aux_out, alu8_1_z, aux_r3_1_r3, CAR_q, COP_q, MAR_q, MDR_q,
       mdr_selector_1_mdr_d, R0_q, R1_q, R2_q, R3_q, ram_1_data, X_q, xy_bus_1_x, xy_bus_1_y, Y_q,
       z_bus_1_mar, z_bus_1_mdr, z_bus_1_r0, z_bus_1_r1, z_bus_1_r2, z_bus_1_r3, Z_q;
  wire [31:0] rom_1_data;
  wire [31:31] Control_q_8;

  Button Step (.out(Step_out));
  Z_Bus z_bus_1 (
    .Z(Z_q), .Z_Selector(Control_q_3), .MDR(z_bus_1_mdr), .MDR_Enable(z_bus_1_mdr_enable), .MAR(z_bus_1_mar),
    .MAR_Enable(z_bus_1_mar_enable), .R0(z_bus_1_r0), .R0_Enable(z_bus_1_r0_enable), .R1(z_bus_1_r1),
    .R1_Enabel(z_bus_1_r1_enabel), .R2(z_bus_1_r2), .R2_Enable(z_bus_1_r2_enable), .R3(z_bus_1_r3),
    .R3_Enable(z_bus_1_r3_enable));
  LED Fetch (.in(clock2_1_fetch));
  Clock2 clock2_1 (
    .Step(Step_out), .Run(Run), .Fetch(clock2_1_fetch), .Calc(clock2_1_calc), .Store(clock2_1_store),
    .Write(clock2_1_write), .Init(clock2_1_init));
  AUX_R3 aux_r3_1 (
    .AUX(alu8_1_aux_out), .Z(z_bus_1_r3), .Aux_Enable(alu8_1_aux_enabled), .Z_Enable(z_bus_1_r3_enable),
    .R3(aux_r3_1_r3), .Enable(aux_r3_1_enable));
  DotMatrix #(.matrixcols(14)) dotmatrix_1 (
    .col0(op_dec_1_col_0), .col1(op_dec_1_col_1), .col2(op_dec_1_col_2), .col3(op_dec_1_col_3),
    .col4(op_dec_1_col_4), .col5(op_dec_1_col_5), .col6(op_dec_1_col_6), .col7(op_dec_1_col_7),
    .col8(op_dec_1_col_8), .col9(op_dec_1_col_9), .col10(op_dec_1_col_10), .col11(op_dec_1_col_11),
    .col12(op_dec_1_col_12), .col13(op_dec_1_col_13));
  op_dec op_dec_1 (
    .op(Control_q_4), .col_0(op_dec_1_col_0), .col_7(op_dec_1_col_7), .col_1(op_dec_1_col_1),
    .col_8(op_dec_1_col_8), .col_2(op_dec_1_col_2), .col_9(op_dec_1_col_9), .col_3(op_dec_1_col_3),
    .col_10(op_dec_1_col_10), .col_4(op_dec_1_col_4), .col_11(op_dec_1_col_11), .col_5(op_dec_1_col_5),
    .col_12(op_dec_1_col_12), .col_6(op_dec_1_col_6), .col_13(op_dec_1_col_13));
  LED Calc (.in(clock2_1_calc));
  Register #(.Select("low")) R0 (.D(z_bus_1_r0), .en(z_bus_1_r0_enable), .Q(R0_q), .clk(clock2_1_store));  // open: clr
  Register #(.Select("low")) R1 (.D(z_bus_1_r1), .en(z_bus_1_r1_enabel), .Q(R1_q), .clk(clock2_1_store));  // open: clr
  Register #(.Select("low")) R2 (.D(z_bus_1_r2), .en(z_bus_1_r2_enable), .Q(R2_q), .clk(clock2_1_store));  // open: clr
  Register #(.Select("low")) R3 (.D(aux_r3_1_r3), .en(aux_r3_1_enable), .Q(R3_q), .clk(clock2_1_store));  // open: clr
  LED Store (.in(clock2_1_store));
  XY_Bus xy_bus_1 (
    .R0(R0_q), .R1(R1_q), .R2(R2_q), .R3(R3_q), .MDR(MDR_q), .Select_X(Control_q), .Select_Y(Control_q_2),
    .X(xy_bus_1_x), .Y(xy_bus_1_y), .Enable_X(xy_bus_1_enable_x), .Enable_Y(xy_bus_1_enable_y));
  LED Write (.in(clock2_1_write));
  Register #(.Select("low")) MAR (
    .D(z_bus_1_mar), .en(z_bus_1_mar_enable), .Q(MAR_q), .clk(clock2_1_store));  // open: clr
  Register #(.trigger("falling"), .Select("low")) X (
    .D(xy_bus_1_x), .en(xy_bus_1_enable_x), .Q(X_q), .clk(clock2_1_fetch));  // open: clr
  Register #(.trigger("falling"), .Select("low")) Y (
    .D(xy_bus_1_y), .en(xy_bus_1_enable_y), .Q(Y_q), .clk(clock2_1_fetch));  // open: clr
  ALU8 alu8_1 (
    .x(X_q), .y(Y_q), .aux_in(R3_q), .op(Control_q_4), .z(alu8_1_z), .aux_out(alu8_1_aux_out),
    .aux_enabled(alu8_1_aux_enabled));  // open: flags
  Register #(.Select("low")) Z (.D(alu8_1_z), .en(1'b1), .Q(Z_q), .clk(clock2_1_calc));  // open: clr
  // Probe on Flags_q
  Register #(.width(6), .Select("low")) Flags (.en(1'b1), .Q(Flags_q), .clk(clock2_1_calc));  // open: D, clr
  RAM #(.bus("separate"), .Select("high"), .simpleMode("false")) ram_1 (
    .addr(MAR_q), .din(MDR_q), .data(ram_1_data), .str(Control_q_5[1]), .clk(clock2_1_write),
    .ld(Control_q_5[0]));  // open: sel, clr
  MDR_Selector mdr_selector_1 (
    .RAM(ram_1_data), .Z(z_bus_1_mdr), .Read__RAM__MDR(Control_q_5[0]), .Fetch_Phase(clock2_1_fetch),
    .Z__MDR(z_bus_1_mdr_enable), .Store_Phase(clock2_1_store), .MDR_D(mdr_selector_1_mdr_d),
    .MDR_En(mdr_selector_1_mdr_en), .Clock(mdr_selector_1_clock));
  // Probe on Control_q
  // Probe on Control_q_2
  // Probe on Control_q_3
  // Probe on Control_q_4
  Register #(.Select("low")) MDR (
    .D(mdr_selector_1_mdr_d), .en(mdr_selector_1_mdr_en), .Q(MDR_q), .clk(mdr_selector_1_clock));  // open: clr
  // Probe on Control_q_5[0]
  // Probe on Control_q_5[1]
  // Probe on Control_q_5[2]
  // Probe on z_bus_1_mar_enable
  // Probe on z_bus_1_mdr_enable
  // Probe on address_calculator_1_ncar
  Register #(.trigger("falling"), .Select("low")) COP (
    .D(MDR_q), .en(Control_q_5[2]), .Q(COP_q), .clk(clock2_1_fetch));  // open: clr
  Address_Calculator address_calculator_1 (
    .CAR(CAR_q), .CN___Maske(Control_q_7), .Flags(Flags_q), .COP(COP_q), .Mode(Control_q_6),
    .NCAR(address_calculator_1_ncar));
  Register #(.Select("low")) CAR (
    .D(address_calculator_1_ncar), .en(1'b1), .Q(CAR_q), .clk(clock2_1_write));  // open: clr
  // Probe on Control_q_6
  // Probe on Control_q_7
  Register #(.width(32), .trigger("falling"), .Select("low")) Control (
    .D(rom_1_data), .en(1'b1),
    .Q({Control_q_8[31], Control_q_7, Control_q_6, Control_q_5, Control_q_4, Control_q_3, Control_q_2, Control_q}),
    .clk(or_1_out));  // open: clr
  ROM #(.dataWidth(32), .Select("high")) rom_1 (.addr(CAR_q), .data(rom_1_data));
  or or_1 (or_1_out, clock2_1_write, clock2_1_init);

  // Notes on the sheet:
  //   00000 NOP
  //   00001 XOR
  //   00010 AND
  //   00011 OR
  //   00100 NOT X
  //   00101 NOT Y
  //   00110 X
  //   00111 Y
  //   01000 ADD
  //   01001 SUB
  //   01010 INC
  //   01011 DEC
  //   01100 MUL
  //   01101 DIV
  //   01110 -X
  //   01111 X LSH Y
  //   10000 0
  //   10001 1
  //   10010 2
  //   10011 3
  //   10100 4
  //   10101 5
  //   10110 6
  //   10111 7
  //   11000 8 
  //   11001 9
  //   11001 10
  //   11011 16
  //   11100 32
  //   11101 64
  //   11110 128
  //   11111 -1
  //   contents of rom_1 (hex, n*v repeats v):
  //   82200 28c400 2a8a000 0 32001 138900 42221 140904 42021 2a34004
endmodule

module AU8 (
  input  [7:0] x,
  input  [7:0] y,
  input  [7:0] aux_in,
  input  [2:0] op,
  output carry_out,
  output overflow,
  output [7:0] aux_out,
  output aux_enabled,
  output [7:0] z
);

  wire adder_1_cout, adder_2_cout, adder_3_cout, adder_4_cout, multiplexer_1_out, not_1_out,
       subtractor_1_bout, subtractor_2_bout, subtractor_3_bout, subtractor_4_bout;
  wire [2:0] bit_extender_1_out;
  wire [6:0] bit_extender_2_out, bit_extender_3_out;
  wire [7:0] adder_1_out, adder_2_out, divider_1_out, divider_1_rem, multiplier_1_cout, multiplier_1_out,
       negator_1_out, shifter_1_out, subtractor_1_out, subtractor_2_out;

  Hex_Digit_Display hex_digit_display_1 (.value(x[7:4]));  // open: dp
  Hex_Digit_Display hex_digit_display_2 (.value(aux_in[7:4]));  // open: dp
  Hex_Digit_Display hex_digit_display_3 (.value(x[3:0]));  // open: dp
  Hex_Digit_Display hex_digit_display_4 (.value(y[7:4]));  // open: dp
  Hex_Digit_Display hex_digit_display_5 (.value(aux_in[3:0]));  // open: dp
  Hex_Digit_Display hex_digit_display_6 (.value(y[3:0]));  // open: dp
  Bit_Extender #(.out_width(3), .\type ("zero")) bit_extender_1 (.in(y), .out(bit_extender_1_out));
  Adder adder_1 (.a(x), .b(y), .out(adder_1_out), .cout(adder_1_cout));  // open: cin
  Subtractor subtractor_1 (.a(x), .b(y), .out(subtractor_1_out), .bout(subtractor_1_bout));  // open: bin
  Adder adder_2 (.a(x), .b(8'h1), .out(adder_2_out), .cout(adder_2_cout));  // open: cin
  Subtractor subtractor_2 (.a(x), .b(8'h1), .out(subtractor_2_out), .bout(subtractor_2_bout));  // open: bin
  Multiplier multiplier_1 (.a(x), .b(y), .out(multiplier_1_out), .cout(multiplier_1_cout));  // open: cin
  Divider divider_1 (.a(x), .b(y), .out(divider_1_out), .rem(divider_1_rem));  // open: upper
  Negator negator_1 (.in(x), .out(negator_1_out));
  Shifter shifter_1 (.in(x), .\dist (bit_extender_1_out), .out(shifter_1_out));
  Bit_Extender #(.out_width(7), .\type ("zero")) bit_extender_2 (.in(x), .out(bit_extender_2_out));
  Bit_Extender #(.out_width(7), .\type ("zero")) bit_extender_3 (.in(y), .out(bit_extender_3_out));
  Adder #(.width(7)) adder_3 (.a(bit_extender_2_out), .b(bit_extender_3_out), .cout(adder_3_cout));  // open: out, cin
  Subtractor #(.width(7)) subtractor_3 (
    .a(bit_extender_2_out), .b(bit_extender_3_out), .bout(subtractor_3_bout));  // open: out, bin
  Adder #(.width(7)) adder_4 (.a(bit_extender_2_out), .b(7'b0000001), .cout(adder_4_cout));  // open: out, cin
  Subtractor #(.width(7)) subtractor_4 (
    .a(bit_extender_2_out), .b(7'b0000001), .bout(subtractor_4_bout));  // open: out, bin
  Multiplexer #(.select(2), .disabled(0)) multiplexer_1 (
    .in0(adder_3_cout), .in1(subtractor_3_bout), .in2(adder_4_cout), .in3(subtractor_4_bout),
    .out(multiplexer_1_out), .sel(op[1:0]), .en(not_1_out));
  not not_1 (not_1_out, op[2]);
  Multiplexer #(.select(2), .disabled(0)) multiplexer_2 (
    .in0(adder_1_cout), .in1(subtractor_1_bout), .in2(adder_2_cout), .in3(subtractor_2_bout),
    .out(carry_out), .sel(op[1:0]), .en(not_1_out));
  Hex_Digit_Display hex_digit_display_7 (.value(aux_out[7:4]));  // open: dp
  Multiplexer #(.width(8)) multiplexer_3 (
    .in0(multiplier_1_cout), .in1(divider_1_rem), .out(aux_out), .sel(op[0]), .en(aux_enabled));
  and and_1 (aux_enabled, ~op[1], op[2]);  // AND_Gate
  Multiplexer #(.select(3), .width(8), .enable("false")) multiplexer_4 (
    .in0(adder_1_out), .in1(subtractor_1_out), .in2(adder_2_out), .in3(subtractor_2_out),
    .in4(multiplier_1_out), .in5(divider_1_out), .in6(negator_1_out), .in7(shifter_1_out), .out(z), .sel(op));
  xor xor_1 (overflow, carry_out, multiplexer_1_out);
  Hex_Digit_Display hex_digit_display_8 (.value(aux_out[3:0]));  // open: dp
  Hex_Digit_Display hex_digit_display_9 (.value(z[7:4]));  // open: dp
  Hex_Digit_Display hex_digit_display_10 (.value(z[3:0]));  // open: dp

  // Notes on the sheet:
  //   000 ADD
  //   001 SUB
  //   010 INC
  //   011 DEC
  //   100 MUL
  //   101 DIV
  //   110 -X
  //   111 X LSH Y
endmodule

module LU8 (
  input  [7:0] x,
  input  [7:0] y,
  input  [2:0] op,
  output [7:0] z
);

  wire [7:0] and_1_out, not_1_out, not_2_out, or_1_out, undriven, xor_1_out;

  assign xor_1_out = x ^ y;  // XOR_Gate xor_1, 8 bits wide
  assign and_1_out = x & y;  // AND_Gate and_1, 8 bits wide
  assign or_1_out = x | y;  // OR_Gate or_1, 8 bits wide
  assign not_1_out = ~x;  // NOT_Gate not_1, 8 bits wide
  assign not_2_out = ~y;  // NOT_Gate not_2, 8 bits wide
  Multiplexer #(.select(3), .width(8), .enable("false")) multiplexer_1 (
    .in0(undriven), .in1(xor_1_out), .in2(and_1_out), .in3(or_1_out), .in4(not_1_out), .in5(not_2_out),
    .in6(x), .in7(y), .out(z), .sel(op));

  // Notes on the sheet:
  //   000 NOP
  //   001 XOR
  //   010 AND
  //   011 OR
  //   100 NOT X
  //   101 NOT Y
  //   110 X
  //   111 Y
  //   NOP
endmodule

module cu8_gen (
  input  op3,
  input  op2,
  input  op1,
  input  op0,
  output z7,
  output z6,
  output z5,
  output z4,
  output z3,
  output z2,
  output z1,
  output z0
);

  wire and_4_out, and_5_out, and_6_out, and_7_out, and_8_out, and_9_out, and_10_out, and_11_out, and_12_out,
       and_13_out, and_14_out, and_15_out, and_16_out, not_1_out, not_2_out, not_3_out, not_4_out, not_5_out,
       not_6_out, not_7_out, not_8_out, not_9_out, not_10_out, not_11_out, not_12_out, not_13_out;

  and and_1 (z7, op3, op2, op1);
  and and_2 (z6, op3, op2, op0);
  not not_1 (not_1_out, op1);
  not not_2 (not_2_out, op0);
  and and_3 (z4, op3, op1, op0);
  not not_3 (not_3_out, op2);
  and and_4 (and_4_out, op3, not_3_out, not_4_out);
  not not_4 (not_4_out, op1);
  not not_5 (not_5_out, op2);
  and and_5 (and_5_out, op3, not_5_out, not_6_out);
  not not_6 (not_6_out, op0);
  and and_6 (and_6_out, op3, op2, op1, op0);
  not not_7 (not_7_out, op3);
  and and_7 (and_7_out, not_7_out, op2);
  and and_8 (and_8_out, op2, op1, op0);
  not not_8 (not_8_out, op3);
  and and_9 (and_9_out, not_8_out, op1);
  not not_9 (not_9_out, op2);
  and and_10 (and_10_out, not_9_out, op1, not_10_out);
  not not_10 (not_10_out, op0);
  and and_11 (and_11_out, op2, op1, op0);
  not not_11 (not_11_out, op3);
  and and_12 (and_12_out, not_11_out, op0);
  not not_12 (not_12_out, op2);
  and and_13 (and_13_out, not_12_out, not_13_out, op0);
  not not_13 (not_13_out, op1);
  and and_14 (and_14_out, op2, op1, op0);
  and and_15 (and_15_out, op3, op2, not_1_out, not_2_out);
  or or_1 (z5, and_15_out, and_16_out);
  and and_16 (and_16_out, op3, op2, op1, op0);
  or or_2 (z3, and_4_out, and_5_out, and_6_out);
  or or_3 (z2, and_7_out, and_8_out);
  or or_4 (z1, and_9_out, and_10_out, and_11_out);
  or or_5 (z0, and_12_out, and_13_out, and_14_out);
endmodule

module CU8 (
  input  [3:0] op,
  output [7:0] z
);

  cu8_gen cu8_gen_1 (
    .op3(op[3]), .op2(op[2]), .op1(op[1]), .op0(op[0]), .z7(z[7]), .z6(z[6]), .z5(z[5]), .z4(z[4]),
    .z3(z[3]), .z2(z[2]), .z1(z[1]), .z0(z[0]));

  // Notes on the sheet:
  //   0000 0
  //   0001 1
  //   0010 2
  //   0011 3
  //   0100 4
  //   0101 5
  //   0110 6
  //   0111 7
  //   1000 8 
  //   1001 9
  //   1010 10
  //   1011 16
  //   1100 32
  //   1101 64
  //   1110 128
  //   1111 -1
endmodule

// ALU
module ALU8 (
  input  [7:0] x,
  input  [7:0] y,
  input  [7:0] aux_in,
  input  [4:0] op,
  output [7:0] z,
  output [7:0] aux_out,
  output aux_enabled,
  output [5:0] flags
);

  wire au8_1_aux_enabled;
  wire [2:0] bit_extender_1_out;
  wire [3:0] bit_extender_2_out;
  wire [7:0] au8_1_z, cu8_1_z, lu8_1_z;

  Bit_Extender #(.in_width(5), .out_width(3), .\type ("zero")) bit_extender_1 (.in(op), .out(bit_extender_1_out));
  Bit_Extender #(.in_width(5), .out_width(4), .\type ("zero")) bit_extender_2 (.in(op), .out(bit_extender_2_out));
  LU8 lu8_1 (.x(x), .y(y), .op(bit_extender_1_out), .z(lu8_1_z));
  AU8 au8_1 (
    .x(x), .y(y), .aux_in(aux_in), .op(bit_extender_1_out), .carry_out(flags[4]), .overflow(flags[3]),
    .aux_out(aux_out), .aux_enabled(au8_1_aux_enabled), .z(au8_1_z));
  CU8 cu8_1 (.op(bit_extender_2_out), .z(cu8_1_z));
  and and_1 (aux_enabled, au8_1_aux_enabled, op[3], ~op[4]);  // AND_Gate
  Multiplexer #(.select(2), .width(8), .enable("false")) multiplexer_1 (
    .in0(lu8_1_z), .in1(au8_1_z), .in2(cu8_1_z), .in3(cu8_1_z), .out(z), .sel(op[4:3]));
  xnor parity (flags[5], z[0], z[1], z[2], z[3], z[4], z[5], z[6], z[7]);
  Comparator comparator_1 (.a(z), .b({8{1'b0}}), .gt(flags[1]), .eq(flags[0]), .lt(flags[2]));

  // Notes on the sheet:
  //   00110 X
  //   00111 Y
  //   01110 -X
  //   00000 NOP
  //   00001 XOR
  //   00010 AND
  //   00011 OR
  //   00100 NOT X
  //   00101 NOT Y
  //   01000 ADD
  //   01001 SUB
  //   01010 INC
  //   01011 DEC
  //   01100 MUL
  //   01101 DIV
  //   01111 X LSH Y
  //   10000 0
  //   10001 1
  //   10010 2
  //   10011 3
  //   10100 4
  //   10101 5
  //   10110 6
  //   10111 7
  //   11000 8 
  //   11001 9
  //   11001 10
  //   11011 16
  //   11100 32
  //   11101 64
  //   11111 -1
  //   11110 128
  //   P C Of - + 0
endmodule

// Clk
module Clock (
  input  Step,
  input  Run,
  output Fetch,
  output Calc,
  output Store,
  output Store_2
);

  wire and_1_out, and_2_out, and_6_out, Clock_out, counter_2_carry, decoder_1_out0, decoder_1_out1,
       decoder_1_out2, decoder_1_out3, or_1_out;
  wire [1:0] counter_1_q;

  Clock_part Clock (.out(Clock_out));
  and and_1 (and_1_out, Step, ~Run);  // AND_Gate
  or or_1 (or_1_out, and_1_out, and_2_out);
  and and_2 (and_2_out, Run, Clock_out);
  Decoder #(.select(2), .enable("false")) decoder_1 (
    .out0(decoder_1_out0), .out1(decoder_1_out1), .out2(decoder_1_out2), .out3(decoder_1_out3),
    .sel(counter_1_q));
  Counter #(.width(2), .max('h3), .behavior("old")) counter_1 (
    .count(1'b1), .Q(counter_1_q), .clk(or_1_out));  // open: load, D, carry, clr, preset
  LED u_Fetch (.in(decoder_1_out1));
  LED u_Calc (.in(decoder_1_out2));
  LED u_Store (.in(decoder_1_out3));
  LED u_Store_2 (.in(decoder_1_out0));
  Counter #(.width(1), .max('h1), .ongoal("stay"), .trigger("falling"), .behavior("old")) counter_2 (
    .count(1'b1), .carry(counter_2_carry), .clk(decoder_1_out1));  // open: load, D, Q, clr, preset
  and and_3 (Fetch, decoder_1_out1, or_1_out);
  and and_4 (Calc, decoder_1_out2, or_1_out);
  and and_5 (Store, decoder_1_out3, or_1_out);
  and and_6 (and_6_out, decoder_1_out0, or_1_out);
  and and_7 (Store_2, and_6_out, counter_2_carry);

  // Notes on the sheet:
  //   Debounce Initial State
endmodule

// X/Y-Bus
module XY_Bus (
  input  [7:0] R0,
  input  [7:0] R1,
  input  [7:0] R2,
  input  [7:0] R3,
  input  [3:0] Select_X,
  input  [7:0] MDR,
  input  [4:0] Select_Y,
  output [7:0] X,
  output Enable_X,
  output [7:0] Y,
  output Enable_Y
);

  wire [1:0] priority_encoder_1_out;
  wire [2:0] priority_encoder_2_out;

  Priority_Encoder #(.select(2)) priority_encoder_1 (
    .in0(Select_X[0]), .in1(Select_X[1]), .in2(Select_X[2]), .in3(Select_X[3]), .out(priority_encoder_1_out),
    .gs(Enable_X));  // open: en_out, en_in
  Priority_Encoder priority_encoder_2 (
    .in0(Select_Y[0]), .in1(Select_Y[1]), .in2(Select_Y[2]), .in3(Select_Y[3]), .in4(Select_Y[4]),
    .out(priority_encoder_2_out), .gs(Enable_Y));  // open: in5, in6, in7, en_out, en_in
  Multiplexer #(.select(2), .width(8)) multiplexer_1 (
    .in0(R0), .in1(R1), .in2(R2), .in3(R3), .out(X), .sel(priority_encoder_1_out), .en(Enable_X));
  Multiplexer #(.select(3), .width(8)) multiplexer_2 (
    .in0(R0), .in1(R1), .in2(R2), .in3(R3), .in4(MDR), .out(Y), .sel(priority_encoder_2_out), .en(Enable_Y));  // open: in5, in6, in7
endmodule

module Z_Bus (
  input  [7:0] Z,
  input  [5:0] Z_Selector,
  output [7:0] MDR,
  output MDR_Enable,
  output [7:0] MAR,
  output MAR_Enable,
  output [7:0] R0,
  output R0_Enable,
  output [7:0] R1,
  output R1_Enabel,
  output [7:0] R2,
  output R2_Enable,
  output [7:0] R3,
  output R3_Enable
);

  assign R0 = Z_Selector[0] ? Z : 8'bz;  // Controlled_Buffer controlled_buffer_1
  assign R1 = Z_Selector[1] ? Z : 8'bz;  // Controlled_Buffer controlled_buffer_2
  assign R2 = Z_Selector[2] ? Z : 8'bz;  // Controlled_Buffer controlled_buffer_3
  assign MDR = Z_Selector[5] ? Z : 8'bz;  // Controlled_Buffer controlled_buffer_4
  assign MAR = Z_Selector[4] ? Z : 8'bz;  // Controlled_Buffer controlled_buffer_5
  assign R3 = Z_Selector[3] ? Z : 8'bz;  // Controlled_Buffer controlled_buffer_6

  assign MAR_Enable = Z_Selector[4];
  assign MDR_Enable = Z_Selector[5];
  assign R0_Enable = Z_Selector[0];
  assign R1_Enabel = Z_Selector[1];
  assign R2_Enable = Z_Selector[2];
  assign R3_Enable = Z_Selector[3];

  // Notes on the sheet:
  //   MDR, MAR, R3, R2, R1, R0
endmodule

// MDR Sel
module MDR_Selector (
  input  [7:0] RAM,
  input  [7:0] Z,
  input  Read__RAM__MDR,
  input  Fetch_Phase,
  input  Z__MDR,
  input  Store_Phase,
  output [7:0] MDR_D,
  output MDR_En,
  output Clock
);

  wire priority_encoder_1_out;

  or or_1 (Clock, Fetch_Phase, Store_Phase);
  Priority_Encoder #(.select(1)) priority_encoder_1 (
    .in0(Read__RAM__MDR), .in1(Z__MDR), .out(priority_encoder_1_out), .gs(MDR_En));  // open: en_out, en_in
  Multiplexer #(.width(8)) multiplexer_1 (.in0(RAM), .in1(Z), .out(MDR_D), .sel(priority_encoder_1_out), .en(MDR_En));
endmodule

// AMX
module AUX_R3 (
  input  [7:0] AUX,
  input  [7:0] Z,
  input  Aux_Enable,
  input  Z_Enable,
  output [7:0] R3,
  output Enable
);

  wire priority_encoder_1_out;

  Priority_Encoder #(.select(1)) priority_encoder_1 (
    .in0(Aux_Enable), .in1(Z_Enable), .out(priority_encoder_1_out), .gs(Enable));  // open: en_out, en_in
  Multiplexer #(.width(8), .enable("false")) multiplexer_1 (.in0(AUX), .in1(Z), .out(R3), .sel(priority_encoder_1_out));
endmodule

// AC
module Address_Calculator (
  input  [7:0] CAR,
  input  [7:0] COP,
  input  [5:0] CN___Maske,
  input  [5:0] Flags,
  input  [1:0] Mode,
  output [7:0] NCAR
);

  wire or_1_out;
  wire [5:0] and_1_out;
  wire [7:0] bit_extender_1_out, multiplexer_1_out, n1_1_out, n4_1_out, n4_2_out;

  assign bit_extender_1_out = {{2{1'b0}}, CN___Maske};  // Bit_Extender bit_extender_1
  _1 u_1_1 (.in(CAR), .out(n1_1_out));
  _4 u_4_1 (.in(bit_extender_1_out), .out(n4_1_out));
  _4 u_4_2 (.in(COP), .out(n4_2_out));
  assign and_1_out = CN___Maske & Flags;  // AND_Gate and_1, 6 bits wide
  OR or_1 (.in(and_1_out), .out(or_1_out));
  Multiplexer #(.width(8), .enable("false")) multiplexer_1 (
    .in0(n1_1_out), .in1(n4_2_out), .out(multiplexer_1_out), .sel(or_1_out));
  Multiplexer #(.select(2), .width(8), .enable("false")) multiplexer_2 (
    .in0(n1_1_out), .in1(n4_1_out), .in2(n4_2_out), .in3(multiplexer_1_out), .out(NCAR), .sel(Mode));

  // Notes on the sheet:
  //   00 CAR++
  //   01 Seg#*4
  //   10 COP
  //   11 COP IF Cond AND Flags <> 0
endmodule

// Clk2
module Clock2 (
  input  Step,
  input  Run,
  output Fetch,
  output Calc,
  output Store,
  output Write,
  output Init
);

  wire and_1_out, and_2_out, Clock_out, counter_2_q, or_1_out;
  wire [2:0] counter_1_q;

  Clock_part Clock (.out(Clock_out));
  and and_1 (and_1_out, Step, ~Run);  // AND_Gate
  or or_1 (or_1_out, and_1_out, and_2_out);
  and and_2 (and_2_out, Run, Clock_out);
  Decoder #(.select(3), .enable("false")) decoder_1 (
    .out1(Fetch), .out3(Calc), .out5(Store), .out7(Write), .sel(counter_1_q));  // open: out0, out2, out4, out6
  Counter #(.width(3), .max('h7), .behavior("old")) counter_1 (
    .count(1'b1), .Q(counter_1_q), .clk(or_1_out));  // open: load, D, carry, clr, preset
  Counter #(.width(1), .max('h1), .ongoal("stay"), .trigger("falling"), .behavior("old")) counter_2 (
    .Q(counter_2_q), .clk(Fetch));  // open: load, D, count, carry, clr, preset
  and and_3 (Init, Fetch, ~counter_2_q);  // AND_Gate
endmodule

module op_dec_col_0 (
  input  op4,
  input  op3,
  input  op2,
  input  op1,
  input  op0,
  output r0,
  output r1,
  output r2,
  output r3,
  output r4,
  output r5,
  output r6
);

  and and_1 (r1, op4, op3, op2, op1);
  and and_2 (r5, op4, op3, op2, op1, op0);
  and and_3 (r6, op4, op3, op2, op1);

  assign r0 = 1'b0;
  assign r2 = 1'b0;
  assign r3 = 1'b0;
  assign r4 = 1'b0;
endmodule

module op_dec_col_1 (
  input  op4,
  input  op3,
  input  op2,
  input  op1,
  input  op0,
  output r0,
  output r1,
  output r2,
  output r3,
  output r4,
  output r5,
  output r6
);

  wire and_3_out, and_4_out, and_7_out, and_8_out, and_9_out, and_10_out, and_11_out, and_12_out, not_1_out,
       not_2_out, not_3_out, not_4_out, not_5_out, not_6_out, not_7_out, not_8_out, not_9_out, not_10_out,
       not_11_out, not_12_out, not_13_out, not_14_out, not_15_out, not_16_out, not_17_out, not_18_out;

  not not_1 (not_1_out, op4);
  not not_2 (not_2_out, op3);
  not not_3 (not_3_out, op2);
  not not_4 (not_4_out, op0);
  not not_5 (not_5_out, op0);
  not not_6 (not_6_out, op4);
  not not_7 (not_7_out, op3);
  not not_8 (not_8_out, op2);
  not not_9 (not_9_out, op4);
  not not_10 (not_10_out, op3);
  not not_11 (not_11_out, op1);
  not not_12 (not_12_out, op4);
  not not_13 (not_13_out, op2);
  not not_14 (not_14_out, op0);
  and and_1 (r4, op4, op3, op2, op1);
  not not_15 (not_15_out, op4);
  not not_16 (not_16_out, op3);
  not not_17 (not_17_out, op2);
  not not_18 (not_18_out, op0);
  and and_2 (r6, op4, op3, op2, op1);
  and and_3 (and_3_out, not_1_out, not_2_out, not_3_out, op1, op0);
  and and_4 (and_4_out, op4, op3, op2, op1);
  and and_5 (r1, op4, op3, op2, op1, not_4_out);
  and and_6 (r2, op4, op3, op2, op1, not_5_out);
  and and_7 (and_7_out, not_6_out, not_7_out, not_8_out, op0);
  and and_8 (and_8_out, not_9_out, not_10_out, op2, not_11_out);
  and and_9 (and_9_out, not_12_out, op3, not_13_out, op1);
  and and_10 (and_10_out, op3, op2, op1, not_14_out);
  and and_11 (and_11_out, not_15_out, not_16_out, not_17_out, op0);
  and and_12 (and_12_out, op4, op3, op2, op1, not_18_out);
  or or_1 (r0, and_3_out, and_4_out);
  or or_2 (r3, and_7_out, and_8_out, and_9_out, and_10_out);
  or or_3 (r5, and_11_out, and_12_out);
endmodule

module op_dec_col_2 (
  input  op4,
  input  op3,
  input  op2,
  input  op1,
  input  op0,
  output r0,
  output r1,
  output r2,
  output r3,
  output r4,
  output r5,
  output r6
);

  wire and_3_out, and_4_out, and_5_out, and_6_out, and_7_out, and_9_out, and_10_out, and_11_out, and_12_out,
       and_13_out, and_14_out, and_15_out, not_1_out, not_2_out, not_3_out, not_4_out, not_5_out, not_6_out,
       not_7_out, not_8_out, not_9_out, not_10_out, not_11_out, not_12_out, not_13_out, not_14_out,
       not_15_out, not_16_out, not_17_out, not_18_out, not_19_out, not_20_out, not_21_out, not_22_out,
       not_23_out, not_24_out;

  not not_1 (not_1_out, op4);
  not not_2 (not_2_out, op3);
  not not_3 (not_3_out, op2);
  not not_4 (not_4_out, op4);
  not not_5 (not_5_out, op3);
  not not_6 (not_6_out, op2);
  not not_7 (not_7_out, op2);
  not not_8 (not_8_out, op1);
  not not_9 (not_9_out, op1);
  not not_10 (not_10_out, op4);
  not not_11 (not_11_out, op3);
  not not_12 (not_12_out, op2);
  not not_13 (not_13_out, op4);
  not not_14 (not_14_out, op3);
  not not_15 (not_15_out, op1);
  not not_16 (not_16_out, op4);
  not not_17 (not_17_out, op1);
  not not_18 (not_18_out, op0);
  not not_19 (not_19_out, op4);
  not not_20 (not_20_out, op1);
  and and_1 (r4, op4, op3, op2, op0);
  not not_21 (not_21_out, op4);
  not not_22 (not_22_out, op3);
  not not_23 (not_23_out, op2);
  not not_24 (not_24_out, op1);
  and and_2 (r6, op4, op3, op1);
  and and_3 (and_3_out, not_1_out, not_2_out, not_3_out, op1, op0);
  and and_4 (and_4_out, op4, op3, op2, op1, op0);
  and and_5 (and_5_out, not_4_out, not_5_out, not_6_out, op1, op0);
  and and_6 (and_6_out, op4, op3, not_7_out, op1);
  and and_7 (and_7_out, op4, op3, op2, not_8_out);
  and and_8 (r2, op4, op3, op2, not_9_out, op0);
  and and_9 (and_9_out, not_10_out, not_11_out, not_12_out, op0);
  and and_10 (and_10_out, not_13_out, not_14_out, op2, not_15_out);
  and and_11 (and_11_out, not_16_out, op2, not_17_out, not_18_out);
  and and_12 (and_12_out, not_19_out, op3, op1);
  and and_13 (and_13_out, op4, op3, op2, not_20_out, op0);
  and and_14 (and_14_out, not_21_out, not_22_out, not_23_out, op0);
  and and_15 (and_15_out, op4, op3, op2, not_24_out);
  or or_1 (r0, and_3_out, and_4_out);
  or or_2 (r1, and_5_out, and_6_out, and_7_out);
  or or_3 (r3, and_9_out, and_10_out, and_11_out, and_12_out, and_13_out);
  or or_4 (r5, and_14_out, and_15_out);
endmodule

module op_dec_col_3 (
  input  op4,
  input  op3,
  input  op2,
  input  op1,
  input  op0,
  output r0,
  output r1,
  output r2,
  output r3,
  output r4,
  output r5,
  output r6
);

  wire and_1_out, and_2_out, and_3_out, and_4_out, and_5_out, and_6_out, and_7_out, and_8_out, and_9_out,
       and_10_out, and_11_out, and_12_out, and_13_out, and_14_out, and_15_out, and_16_out, and_17_out,
       and_18_out, and_19_out, and_20_out, and_21_out, and_22_out, and_23_out, and_24_out, not_1_out,
       not_2_out, not_3_out, not_4_out, not_5_out, not_6_out, not_7_out, not_8_out, not_9_out, not_10_out,
       not_11_out, not_12_out, not_13_out, not_14_out, not_15_out, not_16_out, not_17_out, not_18_out,
       not_19_out, not_20_out, not_21_out, not_22_out, not_23_out, not_24_out, not_25_out, not_26_out,
       not_27_out, not_28_out, not_29_out, not_30_out, not_31_out, not_32_out, not_33_out, not_34_out,
       not_35_out, not_36_out, not_37_out, not_38_out;

  not not_1 (not_1_out, op1);
  not not_2 (not_2_out, op0);
  not not_3 (not_3_out, op2);
  not not_4 (not_4_out, op1);
  not not_5 (not_5_out, op4);
  not not_6 (not_6_out, op3);
  not not_7 (not_7_out, op2);
  not not_8 (not_8_out, op2);
  not not_9 (not_9_out, op0);
  not not_10 (not_10_out, op2);
  not not_11 (not_11_out, op0);
  not not_12 (not_12_out, op2);
  not not_13 (not_13_out, op4);
  not not_14 (not_14_out, op3);
  not not_15 (not_15_out, op2);
  not not_16 (not_16_out, op4);
  not not_17 (not_17_out, op3);
  not not_18 (not_18_out, op1);
  not not_19 (not_19_out, op4);
  not not_20 (not_20_out, op1);
  not not_21 (not_21_out, op0);
  not not_22 (not_22_out, op4);
  not not_23 (not_23_out, op2);
  not not_24 (not_24_out, op4);
  not not_25 (not_25_out, op2);
  not not_26 (not_26_out, op0);
  not not_27 (not_27_out, op4);
  not not_28 (not_28_out, op2);
  not not_29 (not_29_out, op4);
  not not_30 (not_30_out, op3);
  not not_31 (not_31_out, op2);
  not not_32 (not_32_out, op4);
  not not_33 (not_33_out, op2);
  not not_34 (not_34_out, op0);
  not not_35 (not_35_out, op2);
  not not_36 (not_36_out, op1);
  not not_37 (not_37_out, op0);
  not not_38 (not_38_out, op2);
  and and_1 (and_1_out, op3, op2, not_1_out, not_2_out);
  and and_2 (and_2_out, op4, op3, not_3_out, op1);
  and and_3 (and_3_out, op4, op3, op2, not_4_out);
  and and_4 (and_4_out, not_5_out, not_6_out, not_7_out, op1, op0);
  and and_5 (and_5_out, op3, not_8_out, op1, not_9_out);
  and and_6 (and_6_out, op4, op3, op1, op0);
  and and_7 (and_7_out, op3, not_10_out, op1, not_11_out);
  and and_8 (and_8_out, op3, op2, op1, op0);
  and and_9 (and_9_out, op4, op3, not_12_out, op1);
  and and_10 (and_10_out, not_13_out, not_14_out, not_15_out, op0);
  and and_11 (and_11_out, not_16_out, not_17_out, op2, not_18_out);
  and and_12 (and_12_out, not_19_out, op2, not_20_out, not_21_out);
  and and_13 (and_13_out, not_22_out, op3, op1);
  and and_14 (and_14_out, op3, not_23_out, op1);
  and and_15 (and_15_out, op4, op3, op2, op0);
  and and_16 (and_16_out, not_24_out, not_25_out, op1, not_26_out);
  and and_17 (and_17_out, not_27_out, op3, op2, op1, op0);
  and and_18 (and_18_out, op4, op3, not_28_out, op1);
  and and_19 (and_19_out, not_29_out, not_30_out, not_31_out, op0);
  and and_20 (and_20_out, not_32_out, not_33_out, op1, not_34_out);
  and and_21 (and_21_out, op4, op3, not_35_out, op1);
  and and_22 (and_22_out, op3, op2, not_36_out, not_37_out);
  and and_23 (and_23_out, op4, op3, not_38_out, op1);
  and and_24 (and_24_out, op4, op3, op2, op0);
  or or_1 (r0, and_1_out, and_2_out, and_3_out);
  or or_2 (r1, and_4_out, and_5_out, and_6_out);
  or or_3 (r2, and_7_out, and_8_out, and_9_out);
  or or_4 (r3, and_10_out, and_11_out, and_12_out, and_13_out, and_14_out, and_15_out);
  or or_5 (r4, and_16_out, and_17_out, and_18_out);
  or or_6 (r5, and_19_out, and_20_out, and_21_out);
  or or_7 (r6, and_22_out, and_23_out, and_24_out);
endmodule

module op_dec_col_4 (
  input  op4,
  input  op3,
  input  op2,
  input  op1,
  input  op0,
  output r0,
  output r1,
  output r2,
  output r3,
  output r4,
  output r5,
  output r6
);

  wire and_2_out, and_3_out, and_4_out, and_5_out, and_6_out, and_7_out, and_8_out, and_9_out, and_10_out,
       and_11_out, and_12_out, and_13_out, and_14_out, and_15_out, and_16_out, and_17_out, and_18_out,
       and_19_out, and_20_out, not_1_out, not_2_out, not_3_out, not_4_out, not_5_out, not_6_out, not_7_out,
       not_8_out, not_9_out, not_10_out, not_11_out, not_12_out, not_13_out, not_14_out, not_15_out,
       not_16_out, not_17_out, not_18_out, not_19_out, not_20_out, not_21_out, not_22_out, not_23_out,
       not_24_out, not_25_out, not_26_out, not_27_out, not_28_out, not_29_out, not_30_out, not_31_out,
       not_32_out, not_33_out, not_34_out, not_35_out, not_36_out, not_37_out, not_38_out, not_39_out,
       not_40_out, not_41_out;

  not not_1 (not_1_out, op1);
  not not_2 (not_2_out, op4);
  not not_3 (not_3_out, op3);
  not not_4 (not_4_out, op2);
  not not_5 (not_5_out, op4);
  not not_6 (not_6_out, op1);
  not not_7 (not_7_out, op0);
  not not_8 (not_8_out, op0);
  not not_9 (not_9_out, op4);
  not not_10 (not_10_out, op3);
  not not_11 (not_11_out, op2);
  not not_12 (not_12_out, op4);
  not not_13 (not_13_out, op4);
  not not_14 (not_14_out, op2);
  not not_15 (not_15_out, op4);
  not not_16 (not_16_out, op1);
  not not_17 (not_17_out, op4);
  not not_18 (not_18_out, op0);
  not not_19 (not_19_out, op1);
  not not_20 (not_20_out, op4);
  not not_21 (not_21_out, op3);
  not not_22 (not_22_out, op2);
  not not_23 (not_23_out, op0);
  not not_24 (not_24_out, op4);
  not not_25 (not_25_out, op3);
  not not_26 (not_26_out, op1);
  not not_27 (not_27_out, op4);
  not not_28 (not_28_out, op4);
  not not_29 (not_29_out, op3);
  not not_30 (not_30_out, op2);
  not not_31 (not_31_out, op4);
  not not_32 (not_32_out, op1);
  not not_33 (not_33_out, op0);
  not not_34 (not_34_out, op0);
  not not_35 (not_35_out, op4);
  not not_36 (not_36_out, op3);
  not not_37 (not_37_out, op2);
  not not_38 (not_38_out, op0);
  not not_39 (not_39_out, op2);
  not not_40 (not_40_out, op1);
  not not_41 (not_41_out, op0);
  and and_1 (r0, op4, op3, op2, not_1_out);
  and and_2 (and_2_out, not_2_out, not_3_out, not_4_out, op1);
  and and_3 (and_3_out, not_5_out, op3, op2, not_6_out, not_7_out);
  and and_4 (and_4_out, op4, op3, op2, op1, not_8_out);
  and and_5 (and_5_out, not_9_out, not_10_out, not_11_out, op1);
  and and_6 (and_6_out, not_12_out, op3, op2, op1, op0);
  and and_7 (and_7_out, not_13_out, not_14_out, op0);
  and and_8 (and_8_out, not_15_out, op2, not_16_out);
  and and_9 (and_9_out, not_17_out, op3, not_18_out);
  and and_10 (and_10_out, op3, op2, not_19_out);
  and and_11 (and_11_out, not_20_out, not_21_out, not_22_out, op1, not_23_out);
  and and_12 (and_12_out, not_24_out, not_25_out, op2, not_26_out);
  and and_13 (and_13_out, not_27_out, op3, op2, op1, op0);
  and and_14 (and_14_out, not_28_out, not_29_out, not_30_out, op0);
  and and_15 (and_15_out, not_31_out, op3, op2, not_32_out, not_33_out);
  and and_16 (and_16_out, op4, op3, op2, op1, not_34_out);
  and and_17 (and_17_out, not_35_out, not_36_out, not_37_out, op1, not_38_out);
  and and_18 (and_18_out, op4, op3, not_39_out, op1);
  and and_19 (and_19_out, op4, op3, op2, not_40_out);
  and and_20 (and_20_out, op4, op3, op2, not_41_out);
  or or_1 (r1, and_2_out, and_3_out, and_4_out);
  or or_2 (r2, and_5_out, and_6_out);
  or or_3 (r3, and_7_out, and_8_out, and_9_out, and_10_out);
  or or_4 (r4, and_11_out, and_12_out, and_13_out);
  or or_5 (r5, and_14_out, and_15_out, and_16_out);
  or or_6 (r6, and_17_out, and_18_out, and_19_out, and_20_out);
endmodule

module op_dec_col_5 (
  input  op4,
  input  op3,
  input  op2,
  input  op1,
  input  op0,
  output r0,
  output r1,
  output r2,
  output r3,
  output r4,
  output r5,
  output r6
);

  wire and_2_out, and_3_out, and_4_out, and_5_out, and_6_out, and_7_out, and_8_out, and_9_out, and_10_out,
       and_11_out, and_12_out, and_13_out, and_14_out, and_15_out, and_16_out, and_17_out, not_1_out,
       not_2_out, not_3_out, not_4_out, not_5_out, not_6_out, not_7_out, not_8_out, not_9_out, not_10_out,
       not_11_out, not_12_out, not_13_out, not_14_out, not_15_out, not_16_out, not_17_out, not_18_out,
       not_19_out, not_20_out, not_21_out, not_22_out, not_23_out, not_24_out, not_25_out, not_26_out,
       not_27_out, not_28_out, not_29_out, not_30_out;

  not not_1 (not_1_out, op4);
  not not_2 (not_2_out, op3);
  not not_3 (not_3_out, op2);
  not not_4 (not_4_out, op0);
  and and_1 (r1, op3, op2, op1, op0);
  not not_5 (not_5_out, op4);
  not not_6 (not_6_out, op3);
  not not_7 (not_7_out, op2);
  not not_8 (not_8_out, op4);
  not not_9 (not_9_out, op1);
  not not_10 (not_10_out, op0);
  not not_11 (not_11_out, op4);
  not not_12 (not_12_out, op2);
  not not_13 (not_13_out, op4);
  not not_14 (not_14_out, op2);
  not not_15 (not_15_out, op4);
  not not_16 (not_16_out, op2);
  not not_17 (not_17_out, op1);
  not not_18 (not_18_out, op4);
  not not_19 (not_19_out, op1);
  not not_20 (not_20_out, op0);
  not not_21 (not_21_out, op4);
  not not_22 (not_22_out, op0);
  not not_23 (not_23_out, op4);
  not not_24 (not_24_out, op3);
  not not_25 (not_25_out, op2);
  not not_26 (not_26_out, op4);
  not not_27 (not_27_out, op4);
  not not_28 (not_28_out, op3);
  not not_29 (not_29_out, op2);
  not not_30 (not_30_out, op0);
  and and_2 (and_2_out, not_1_out, not_2_out, not_3_out, op1, not_4_out);
  and and_3 (and_3_out, op4, op3, op2);
  and and_4 (and_4_out, not_5_out, not_6_out, not_7_out, op1, op0);
  and and_5 (and_5_out, not_8_out, op3, op2, not_9_out, not_10_out);
  and and_6 (and_6_out, op3, op2, op1, op0);
  and and_7 (and_7_out, not_11_out, not_12_out, op0);
  and and_8 (and_8_out, not_13_out, not_14_out, op1);
  and and_9 (and_9_out, not_15_out, op3, not_16_out);
  and and_10 (and_10_out, op3, op2, not_17_out);
  and and_11 (and_11_out, not_18_out, op3, op2, not_19_out, not_20_out);
  and and_12 (and_12_out, not_21_out, op3, op2, op1, op0);
  and and_13 (and_13_out, op4, op3, op2, op1, not_22_out);
  and and_14 (and_14_out, not_23_out, not_24_out, not_25_out, op0);
  and and_15 (and_15_out, not_26_out, op3, op2, op1, op0);
  and and_16 (and_16_out, not_27_out, not_28_out, not_29_out, op1, not_30_out);
  and and_17 (and_17_out, op4, op3, op2);
  or or_1 (r0, and_2_out, and_3_out);
  or or_2 (r2, and_4_out, and_5_out, and_6_out);
  or or_3 (r3, and_7_out, and_8_out, and_9_out, and_10_out);
  or or_4 (r4, and_11_out, and_12_out, and_13_out);
  or or_5 (r5, and_14_out, and_15_out);
  or or_6 (r6, and_16_out, and_17_out);
endmodule

module op_dec_col_6 (
  input  op4,
  input  op3,
  input  op2,
  input  op1,
  input  op0,
  output r0,
  output r1,
  output r2,
  output r3,
  output r4,
  output r5,
  output r6
);

  wire and_1_out, and_2_out, and_3_out, and_4_out, and_5_out, and_6_out, and_7_out, and_8_out, and_9_out,
       and_10_out, and_11_out, and_12_out, and_13_out, and_14_out, and_15_out, and_16_out, and_17_out,
       and_18_out, and_19_out, and_20_out, and_21_out, and_22_out, and_23_out, not_1_out, not_2_out,
       not_3_out, not_4_out, not_5_out, not_6_out, not_7_out, not_8_out, not_9_out, not_10_out, not_11_out,
       not_12_out, not_13_out, not_14_out, not_15_out, not_16_out, not_17_out, not_18_out, not_19_out,
       not_20_out, not_21_out, not_22_out, not_23_out, not_24_out, not_25_out, not_26_out, not_27_out,
       not_28_out, not_29_out, not_30_out, not_31_out, not_32_out, not_33_out, not_34_out, not_35_out,
       not_36_out, not_37_out, not_38_out, not_39_out, not_40_out, not_41_out, not_42_out;

  not not_1 (not_1_out, op4);
  not not_2 (not_2_out, op3);
  not not_3 (not_3_out, op2);
  not not_4 (not_4_out, op0);
  not not_5 (not_5_out, op4);
  not not_6 (not_6_out, op1);
  not not_7 (not_7_out, op0);
  not not_8 (not_8_out, op4);
  not not_9 (not_9_out, op1);
  not not_10 (not_10_out, op0);
  not not_11 (not_11_out, op1);
  not not_12 (not_12_out, op4);
  not not_13 (not_13_out, op4);
  not not_14 (not_14_out, op0);
  not not_15 (not_15_out, op4);
  not not_16 (not_16_out, op1);
  not not_17 (not_17_out, op0);
  not not_18 (not_18_out, op1);
  not not_19 (not_19_out, op0);
  not not_20 (not_20_out, op4);
  not not_21 (not_21_out, op3);
  not not_22 (not_22_out, op2);
  not not_23 (not_23_out, op4);
  not not_24 (not_24_out, op1);
  not not_25 (not_25_out, op4);
  not not_26 (not_26_out, op1);
  not not_27 (not_27_out, op0);
  not not_28 (not_28_out, op1);
  not not_29 (not_29_out, op0);
  not not_30 (not_30_out, op4);
  not not_31 (not_31_out, op3);
  not not_32 (not_32_out, op2);
  not not_33 (not_33_out, op4);
  not not_34 (not_34_out, op1);
  not not_35 (not_35_out, op0);
  not not_36 (not_36_out, op1);
  not not_37 (not_37_out, op4);
  not not_38 (not_38_out, op4);
  not not_39 (not_39_out, op3);
  not not_40 (not_40_out, op0);
  not not_41 (not_41_out, op4);
  not not_42 (not_42_out, op0);
  and and_1 (and_1_out, not_1_out, not_2_out, not_3_out, op1, not_4_out);
  and and_2 (and_2_out, not_5_out, op3, op2, not_6_out, not_7_out);
  and and_3 (and_3_out, op3, op2, op1, op0);
  and and_4 (and_4_out, op4, op3, op2, op1);
  and and_5 (and_5_out, not_8_out, op3, not_9_out, not_10_out);
  and and_6 (and_6_out, op3, op2, not_11_out);
  and and_7 (and_7_out, not_12_out, op3, op2, op0);
  and and_8 (and_8_out, not_13_out, op2, not_14_out);
  and and_9 (and_9_out, not_15_out, op3, not_16_out, not_17_out);
  and and_10 (and_10_out, op3, op2, not_18_out, not_19_out);
  and and_11 (and_11_out, op4, op3, op2, op1, op0);
  and and_12 (and_12_out, not_20_out, not_21_out, not_22_out, op1);
  and and_13 (and_13_out, not_23_out, op3, not_24_out);
  and and_14 (and_14_out, not_25_out, op3, not_26_out, not_27_out);
  and and_15 (and_15_out, op4, op3, op2, not_28_out);
  and and_16 (and_16_out, op4, op3, op2, not_29_out);
  and and_17 (and_17_out, not_30_out, not_31_out, not_32_out, op1, op0);
  and and_18 (and_18_out, not_33_out, op3, not_34_out, not_35_out);
  and and_19 (and_19_out, op3, op2, not_36_out);
  and and_20 (and_20_out, not_37_out, op3, op2, op0);
  and and_21 (and_21_out, not_38_out, not_39_out, op1, not_40_out);
  and and_22 (and_22_out, not_41_out, op2, not_42_out);
  and and_23 (and_23_out, op3, op2, op1);
  or or_1 (r0, and_1_out, and_2_out, and_3_out, and_4_out);
  or or_2 (r1, and_5_out, and_6_out, and_7_out);
  or or_3 (r2, and_8_out, and_9_out, and_10_out, and_11_out);
  or or_4 (r3, and_12_out, and_13_out);
  or or_5 (r4, and_14_out, and_15_out, and_16_out);
  or or_6 (r5, and_17_out, and_18_out, and_19_out, and_20_out);
  or or_7 (r6, and_21_out, and_22_out, and_23_out);
endmodule

module op_dec_col_7 (
  input  op4,
  input  op3,
  input  op2,
  input  op1,
  input  op0,
  output r0,
  output r1,
  output r2,
  output r3,
  output r4,
  output r5,
  output r6
);

  wire and_1_out, and_2_out, and_3_out, and_4_out, and_5_out, and_6_out, and_7_out, and_8_out, and_9_out,
       and_10_out, and_11_out, and_12_out, and_13_out, and_14_out, and_15_out, and_16_out, and_17_out,
       and_18_out, and_19_out, and_20_out, and_21_out, and_22_out, and_23_out, and_24_out, and_25_out,
       and_26_out, and_27_out, and_28_out, and_29_out, and_30_out, and_31_out, and_32_out, and_33_out,
       and_34_out, not_1_out, not_2_out, not_3_out, not_4_out, not_5_out, not_6_out, not_7_out, not_8_out,
       not_9_out, not_10_out, not_11_out, not_12_out, not_13_out, not_14_out, not_15_out, not_16_out,
       not_17_out, not_18_out, not_19_out, not_20_out, not_21_out, not_22_out, not_23_out, not_24_out,
       not_25_out, not_26_out, not_27_out, not_28_out, not_29_out, not_30_out, not_31_out, not_32_out,
       not_33_out, not_34_out, not_35_out, not_36_out, not_37_out, not_38_out, not_39_out, not_40_out,
       not_41_out, not_42_out, not_43_out, not_44_out, not_45_out, not_46_out, not_47_out, not_48_out,
       not_49_out, not_50_out, not_51_out, not_52_out, not_53_out, not_54_out, not_55_out, not_56_out,
       not_57_out, not_58_out, not_59_out, not_60_out, not_61_out, not_62_out;

  not not_1 (not_1_out, op4);
  not not_2 (not_2_out, op3);
  not not_3 (not_3_out, op2);
  not not_4 (not_4_out, op0);
  not not_5 (not_5_out, op3);
  not not_6 (not_6_out, op3);
  not not_7 (not_7_out, op1);
  not not_8 (not_8_out, op4);
  not not_9 (not_9_out, op3);
  not not_10 (not_10_out, op2);
  not not_11 (not_11_out, op3);
  not not_12 (not_12_out, op1);
  not not_13 (not_13_out, op3);
  not not_14 (not_14_out, op0);
  not not_15 (not_15_out, op0);
  not not_16 (not_16_out, op4);
  not not_17 (not_17_out, op3);
  not not_18 (not_18_out, op4);
  not not_19 (not_19_out, op0);
  not not_20 (not_20_out, op3);
  not not_21 (not_21_out, op1);
  not not_22 (not_22_out, op3);
  not not_23 (not_23_out, op0);
  not not_24 (not_24_out, op4);
  not not_25 (not_25_out, op3);
  not not_26 (not_26_out, op0);
  not not_27 (not_27_out, op3);
  not not_28 (not_28_out, op0);
  not not_29 (not_29_out, op0);
  not not_30 (not_30_out, op4);
  not not_31 (not_31_out, op1);
  not not_32 (not_32_out, op4);
  not not_33 (not_33_out, op2);
  not not_34 (not_34_out, op4);
  not not_35 (not_35_out, op3);
  not not_36 (not_36_out, op2);
  not not_37 (not_37_out, op0);
  not not_38 (not_38_out, op4);
  not not_39 (not_39_out, op1);
  not not_40 (not_40_out, op0);
  not not_41 (not_41_out, op3);
  not not_42 (not_42_out, op0);
  not not_43 (not_43_out, op2);
  not not_44 (not_44_out, op4);
  not not_45 (not_45_out, op3);
  not not_46 (not_46_out, op0);
  not not_47 (not_47_out, op4);
  not not_48 (not_48_out, op3);
  not not_49 (not_49_out, op4);
  not not_50 (not_50_out, op0);
  not not_51 (not_51_out, op3);
  not not_52 (not_52_out, op0);
  not not_53 (not_53_out, op2);
  not not_54 (not_54_out, op2);
  not not_55 (not_55_out, op4);
  not not_56 (not_56_out, op3);
  not not_57 (not_57_out, op0);
  not not_58 (not_58_out, op4);
  not not_59 (not_59_out, op3);
  not not_60 (not_60_out, op0);
  not not_61 (not_61_out, op3);
  not not_62 (not_62_out, op1);
  and and_1 (and_1_out, not_1_out, not_2_out, not_3_out, op1, not_4_out);
  and and_2 (and_2_out, not_5_out, op2, op0);
  and and_3 (and_3_out, op2, op1, op0);
  and and_4 (and_4_out, op4, not_6_out, op2, not_7_out);
  and and_5 (and_5_out, not_8_out, not_9_out, op2, op0);
  and and_6 (and_6_out, op4, not_10_out, op1, op0);
  and and_7 (and_7_out, op4, not_11_out, op2, not_12_out);
  and and_8 (and_8_out, op4, not_13_out, op2, not_14_out);
  and and_9 (and_9_out, op4, op3, op1, not_15_out);
  and and_10 (and_10_out, not_16_out, not_17_out, op2);
  and and_11 (and_11_out, not_18_out, op2, not_19_out);
  and and_12 (and_12_out, not_20_out, op2, not_21_out);
  and and_13 (and_13_out, not_22_out, op2, not_23_out);
  and and_14 (and_14_out, op4, op3, op1);
  and and_15 (and_15_out, not_24_out, not_25_out, op1, not_26_out);
  and and_16 (and_16_out, not_27_out, op2, not_28_out);
  and and_17 (and_17_out, op2, op1, not_29_out);
  and and_18 (and_18_out, not_30_out, op3, not_31_out);
  and and_19 (and_19_out, not_32_out, op3, op2);
  and and_20 (and_20_out, op4, op3, not_33_out, op1);
  and and_21 (and_21_out, not_34_out, not_35_out, not_36_out, op1, not_37_out);
  and and_22 (and_22_out, not_38_out, op3, op2, not_39_out, not_40_out);
  and and_23 (and_23_out, op4, not_41_out, op2, op1, not_42_out);
  and and_24 (and_24_out, op4, op3, not_43_out, op1);
  and and_25 (and_25_out, not_44_out, not_45_out, op2, not_46_out);
  and and_26 (and_26_out, not_47_out, not_48_out, op2, op1);
  and and_27 (and_27_out, not_49_out, op2, op1, not_50_out);
  and and_28 (and_28_out, not_51_out, op2, op1, not_52_out);
  and and_29 (and_29_out, op4, not_53_out, op1, op0);
  and and_30 (and_30_out, op4, op3, not_54_out, op1);
  and and_31 (and_31_out, not_55_out, not_56_out, op1, not_57_out);
  and and_32 (and_32_out, not_58_out, not_59_out, op2, not_60_out);
  and and_33 (and_33_out, op3, op2, op1);
  and and_34 (and_34_out, op4, not_61_out, op2, not_62_out, op0);
  or or_1 (r0, and_1_out, and_2_out, and_3_out, and_4_out);
  or or_2 (r1, and_5_out, and_6_out, and_7_out, and_8_out, and_9_out);
  or or_3 (r2, and_10_out, and_11_out, and_12_out, and_13_out, and_14_out);
  or or_4 (r3, and_15_out, and_16_out, and_17_out, and_18_out, and_19_out, and_20_out);
  or or_5 (r4, and_21_out, and_22_out, and_23_out, and_24_out);
  or or_6 (r5, and_25_out, and_26_out, and_27_out, and_28_out, and_29_out, and_30_out);
  or or_7 (r6, and_31_out, and_32_out, and_33_out, and_34_out);
endmodule

module op_dec_col_8 (
  input  op4,
  input  op3,
  input  op2,
  input  op1,
  input  op0,
  output r0,
  output r1,
  output r2,
  output r3,
  output r4,
  output r5,
  output r6
);

  wire and_1_out, and_2_out, and_3_out, and_4_out, and_5_out, and_6_out, and_7_out, and_8_out, and_9_out,
       and_10_out, and_11_out, and_12_out, and_13_out, and_14_out, and_15_out, and_16_out, and_17_out,
       and_18_out, and_19_out, and_20_out, and_21_out, and_22_out, and_23_out, and_24_out, and_25_out,
       and_26_out, and_27_out, and_28_out, and_29_out, and_30_out, and_31_out, and_32_out, and_33_out,
       and_34_out, not_1_out, not_2_out, not_3_out, not_4_out, not_5_out, not_6_out, not_7_out, not_8_out,
       not_9_out, not_10_out, not_11_out, not_12_out, not_13_out, not_14_out, not_15_out, not_16_out,
       not_17_out, not_18_out, not_19_out, not_20_out, not_21_out, not_22_out, not_23_out, not_24_out,
       not_25_out, not_26_out, not_27_out, not_28_out, not_29_out, not_30_out, not_31_out, not_32_out,
       not_33_out, not_34_out, not_35_out, not_36_out, not_37_out, not_38_out, not_39_out, not_40_out,
       not_41_out, not_42_out, not_43_out, not_44_out, not_45_out, not_46_out, not_47_out, not_48_out,
       not_49_out, not_50_out, not_51_out, not_52_out, not_53_out, not_54_out, not_55_out, not_56_out,
       not_57_out;

  not not_1 (not_1_out, op3);
  not not_2 (not_2_out, op2);
  not not_3 (not_3_out, op3);
  not not_4 (not_4_out, op2);
  not not_5 (not_5_out, op0);
  not not_6 (not_6_out, op1);
  not not_7 (not_7_out, op0);
  not not_8 (not_8_out, op2);
  not not_9 (not_9_out, op0);
  not not_10 (not_10_out, op1);
  not not_11 (not_11_out, op4);
  not not_12 (not_12_out, op3);
  not not_13 (not_13_out, op2);
  not not_14 (not_14_out, op0);
  not not_15 (not_15_out, op4);
  not not_16 (not_16_out, op2);
  not not_17 (not_17_out, op1);
  not not_18 (not_18_out, op0);
  not not_19 (not_19_out, op1);
  not not_20 (not_20_out, op2);
  not not_21 (not_21_out, op1);
  not not_22 (not_22_out, op4);
  not not_23 (not_23_out, op3);
  not not_24 (not_24_out, op0);
  not not_25 (not_25_out, op4);
  not not_26 (not_26_out, op3);
  not not_27 (not_27_out, op1);
  not not_28 (not_28_out, op0);
  not not_29 (not_29_out, op4);
  not not_30 (not_30_out, op3);
  not not_31 (not_31_out, op0);
  not not_32 (not_32_out, op4);
  not not_33 (not_33_out, op3);
  not not_34 (not_34_out, op0);
  not not_35 (not_35_out, op4);
  not not_36 (not_36_out, op0);
  not not_37 (not_37_out, op2);
  not not_38 (not_38_out, op1);
  not not_39 (not_39_out, op0);
  not not_40 (not_40_out, op3);
  not not_41 (not_41_out, op2);
  not not_42 (not_42_out, op0);
  not not_43 (not_43_out, op4);
  not not_44 (not_44_out, op0);
  not not_45 (not_45_out, op3);
  not not_46 (not_46_out, op2);
  not not_47 (not_47_out, op0);
  not not_48 (not_48_out, op1);
  not not_49 (not_49_out, op0);
  not not_50 (not_50_out, op3);
  not not_51 (not_51_out, op2);
  not not_52 (not_52_out, op0);
  not not_53 (not_53_out, op3);
  not not_54 (not_54_out, op3);
  not not_55 (not_55_out, op2);
  not not_56 (not_56_out, op1);
  not not_57 (not_57_out, op0);
  and and_1 (and_1_out, op4, op1, op0);
  and and_2 (and_2_out, op4, op2, op0);
  and and_3 (and_3_out, op4, not_1_out, op2, op1);
  and and_4 (and_4_out, op4, op3, not_2_out, op1);
  and and_5 (and_5_out, not_3_out, not_4_out, op1, not_5_out);
  and and_6 (and_6_out, op3, op2, not_6_out, not_7_out);
  and and_7 (and_7_out, op4, not_8_out, not_9_out);
  and and_8 (and_8_out, op4, op3, not_10_out);
  and and_9 (and_9_out, not_11_out, not_12_out, not_13_out, op1, not_14_out);
  and and_10 (and_10_out, not_15_out, op3, op2, op1, op0);
  and and_11 (and_11_out, op4, not_16_out, not_17_out, not_18_out);
  and and_12 (and_12_out, op4, op2, not_19_out, op0);
  and and_13 (and_13_out, op4, op3, not_20_out, not_21_out);
  and and_14 (and_14_out, not_22_out, op2);
  and and_15 (and_15_out, not_23_out, op2, not_24_out);
  and and_16 (and_16_out, not_25_out, op3);
  and and_17 (and_17_out, op3, op1, op0);
  and and_18 (and_18_out, op3, op2, op0);
  and and_19 (and_19_out, op4, not_26_out, not_27_out, not_28_out);
  and and_20 (and_20_out, not_29_out, not_30_out, op1, not_31_out);
  and and_21 (and_21_out, not_32_out, not_33_out, op2, not_34_out);
  and and_22 (and_22_out, not_35_out, op2, op1, not_36_out);
  and and_23 (and_23_out, op3, op2, op1, op0);
  and and_24 (and_24_out, op4, not_37_out, not_38_out, not_39_out);
  and and_25 (and_25_out, not_40_out, not_41_out, op1, not_42_out);
  and and_26 (and_26_out, not_43_out, op2, not_44_out);
  and and_27 (and_27_out, op4, not_45_out, not_46_out, not_47_out);
  and and_28 (and_28_out, op4, op2, op1, op0);
  and and_29 (and_29_out, op4, op3, not_48_out, not_49_out);
  and and_30 (and_30_out, not_50_out, not_51_out, op1, not_52_out);
  and and_31 (and_31_out, not_53_out, op2, op0);
  and and_32 (and_32_out, op4, not_54_out, op1);
  and and_33 (and_33_out, op4, not_55_out, op1);
  and and_34 (and_34_out, op4, op3, op2, not_56_out, not_57_out);
  or or_1 (r0, and_1_out, and_2_out, and_3_out, and_4_out);
  or or_2 (r1, and_5_out, and_6_out, and_7_out, and_8_out);
  or or_3 (r2, and_9_out, and_10_out, and_11_out, and_12_out, and_13_out);
  or or_4 (r3, and_14_out, and_15_out, and_16_out, and_17_out, and_18_out, and_19_out);
  or or_5 (r4, and_20_out, and_21_out, and_22_out, and_23_out, and_24_out);
  or or_6 (r5, and_25_out, and_26_out, and_27_out, and_28_out, and_29_out);
  or or_7 (r6, and_30_out, and_31_out, and_32_out, and_33_out, and_34_out);
endmodule

module op_dec_col_9 (
  input  op4,
  input  op3,
  input  op2,
  input  op1,
  input  op0,
  output r0,
  output r1,
  output r2,
  output r3,
  output r4,
  output r5,
  output r6
);

  wire and_1_out, and_2_out, and_3_out, and_4_out, and_5_out, and_6_out, and_7_out, and_8_out, and_9_out,
       and_10_out, and_11_out, and_12_out, and_13_out, and_14_out, and_15_out, and_16_out, and_17_out,
       and_18_out, and_19_out, and_20_out, and_21_out, and_22_out, and_23_out, and_24_out, and_25_out,
       and_26_out, and_27_out, and_28_out, and_29_out, and_30_out, and_31_out, not_1_out, not_2_out,
       not_3_out, not_4_out, not_5_out, not_6_out, not_7_out, not_8_out, not_9_out, not_10_out, not_11_out,
       not_12_out, not_13_out, not_14_out, not_15_out, not_16_out, not_17_out, not_18_out, not_19_out,
       not_20_out, not_21_out, not_22_out, not_23_out, not_24_out, not_25_out, not_26_out, not_27_out,
       not_28_out, not_29_out, not_30_out, not_31_out, not_32_out, not_33_out, not_34_out, not_35_out,
       not_36_out, not_37_out, not_38_out, not_39_out, not_40_out, not_41_out, not_42_out, not_43_out,
       not_44_out, not_45_out, not_46_out, not_47_out, not_48_out, not_49_out, not_50_out, not_51_out,
       not_52_out, not_53_out, not_54_out, not_55_out;

  not not_1 (not_1_out, op1);
  not not_2 (not_2_out, op0);
  not not_3 (not_3_out, op2);
  not not_4 (not_4_out, op0);
  not not_5 (not_5_out, op3);
  not not_6 (not_6_out, op3);
  not not_7 (not_7_out, op2);
  not not_8 (not_8_out, op4);
  not not_9 (not_9_out, op3);
  not not_10 (not_10_out, op2);
  not not_11 (not_11_out, op3);
  not not_12 (not_12_out, op2);
  not not_13 (not_13_out, op1);
  not not_14 (not_14_out, op0);
  not not_15 (not_15_out, op4);
  not not_16 (not_16_out, op3);
  not not_17 (not_17_out, op1);
  not not_18 (not_18_out, op0);
  not not_19 (not_19_out, op4);
  not not_20 (not_20_out, op3);
  not not_21 (not_21_out, op4);
  not not_22 (not_22_out, op2);
  not not_23 (not_23_out, op4);
  not not_24 (not_24_out, op1);
  not not_25 (not_25_out, op0);
  not not_26 (not_26_out, op3);
  not not_27 (not_27_out, op3);
  not not_28 (not_28_out, op0);
  not not_29 (not_29_out, op2);
  not not_30 (not_30_out, op1);
  not not_31 (not_31_out, op2);
  not not_32 (not_32_out, op1);
  not not_33 (not_33_out, op4);
  not not_34 (not_34_out, op3);
  not not_35 (not_35_out, op0);
  not not_36 (not_36_out, op4);
  not not_37 (not_37_out, op3);
  not not_38 (not_38_out, op2);
  not not_39 (not_39_out, op0);
  not not_40 (not_40_out, op3);
  not not_41 (not_41_out, op0);
  not not_42 (not_42_out, op4);
  not not_43 (not_43_out, op3);
  not not_44 (not_44_out, op2);
  not not_45 (not_45_out, op0);
  not not_46 (not_46_out, op0);
  not not_47 (not_47_out, op4);
  not not_48 (not_48_out, op3);
  not not_49 (not_49_out, op3);
  not not_50 (not_50_out, op1);
  not not_51 (not_51_out, op1);
  not not_52 (not_52_out, op0);
  not not_53 (not_53_out, op2);
  not not_54 (not_54_out, op3);
  not not_55 (not_55_out, op0);
  and and_1 (and_1_out, op3, op2, not_1_out, not_2_out);
  and and_2 (and_2_out, op4, not_3_out, not_4_out);
  and and_3 (and_3_out, op4, not_5_out, op1);
  and and_4 (and_4_out, op4, not_6_out, op2, op0);
  and and_5 (and_5_out, op4, op3, not_7_out);
  and and_6 (and_6_out, not_8_out, not_9_out, not_10_out, op0);
  and and_7 (and_7_out, op4, not_11_out, not_12_out, not_13_out);
  and and_8 (and_8_out, op4, op3, op2, op1, not_14_out);
  and and_9 (and_9_out, not_15_out, op3, op2, op1, op0);
  and and_10 (and_10_out, op4, not_16_out, op2, not_17_out, op0);
  and and_11 (and_11_out, op4, op3, op1, not_18_out);
  and and_12 (and_12_out, not_19_out, not_20_out, op2, op0);
  and and_13 (and_13_out, not_21_out, op3, not_22_out, op1);
  and and_14 (and_14_out, not_23_out, op3, op2, not_24_out, not_25_out);
  and and_15 (and_15_out, op4, not_26_out, op1, op0);
  and and_16 (and_16_out, op4, not_27_out, op2, not_28_out);
  and and_17 (and_17_out, op4, op3, not_29_out, not_30_out);
  and and_18 (and_18_out, op4, op3, not_31_out, op0);
  and and_19 (and_19_out, op4, op3, not_32_out, op0);
  and and_20 (and_20_out, not_33_out, not_34_out, op2, not_35_out);
  and and_21 (and_21_out, not_36_out, op3, op2, op1);
  and and_22 (and_22_out, op4, not_37_out, not_38_out, op1, not_39_out);
  and and_23 (and_23_out, op4, not_40_out, op2, op1, op0);
  and and_24 (and_24_out, op4, op3, op2, not_41_out);
  and and_25 (and_25_out, not_42_out, not_43_out, not_44_out, op1, not_45_out);
  and and_26 (and_26_out, op4, op3, op2, op1, not_46_out);
  and and_27 (and_27_out, not_47_out, not_48_out, op0);
  and and_28 (and_28_out, not_49_out, not_50_out, op0);
  and and_29 (and_29_out, op3, op2, not_51_out, not_52_out);
  and and_30 (and_30_out, op4, not_53_out);
  and and_31 (and_31_out, op4, not_54_out, op1, not_55_out);
  or or_1 (r0, and_1_out, and_2_out, and_3_out, and_4_out, and_5_out);
  or or_2 (r1, and_6_out, and_7_out, and_8_out);
  or or_3 (r2, and_9_out, and_10_out, and_11_out);
  or or_4 (r3, and_12_out, and_13_out, and_14_out, and_15_out, and_16_out, and_17_out, and_18_out, and_19_out);
  or or_5 (r4, and_20_out, and_21_out, and_22_out, and_23_out, and_24_out);
  or or_6 (r5, and_25_out, and_26_out);
  or or_7 (r6, and_27_out, and_28_out, and_29_out, and_30_out, and_31_out);
endmodule

module op_dec_col_10 (
  input  op4,
  input  op3,
  input  op2,
  input  op1,
  input  op0,
  output r0,
  output r1,
  output r2,
  output r3,
  output r4,
  output r5,
  output r6
);

  wire and_1_out, and_2_out, and_3_out, and_4_out, and_5_out, and_6_out, and_7_out, and_8_out, and_9_out,
       and_10_out, and_11_out, and_12_out, and_13_out, and_14_out, and_15_out, and_16_out, and_17_out,
       and_18_out, and_19_out, and_20_out, and_21_out, and_22_out, and_23_out, and_24_out, and_25_out,
       and_26_out, and_27_out, and_28_out, and_29_out, and_30_out, and_31_out, and_32_out, and_33_out,
       and_34_out, and_35_out, and_36_out, and_37_out, and_38_out, and_39_out, and_40_out, and_41_out,
       not_1_out, not_2_out, not_3_out, not_4_out, not_5_out, not_6_out, not_7_out, not_8_out, not_9_out,
       not_10_out, not_11_out, not_12_out, not_13_out, not_14_out, not_15_out, not_16_out, not_17_out,
       not_18_out, not_19_out, not_20_out, not_21_out, not_22_out, not_23_out, not_24_out, not_25_out,
       not_26_out, not_27_out, not_28_out, not_29_out, not_30_out, not_31_out, not_32_out, not_33_out,
       not_34_out, not_35_out, not_36_out, not_37_out, not_38_out, not_39_out, not_40_out, not_41_out,
       not_42_out, not_43_out, not_44_out, not_45_out, not_46_out, not_47_out, not_48_out, not_49_out,
       not_50_out, not_51_out, not_52_out, not_53_out, not_54_out, not_55_out, not_56_out, not_57_out,
       not_58_out, not_59_out, not_60_out, not_61_out, not_62_out, not_63_out, not_64_out, not_65_out,
       not_66_out, not_67_out, not_68_out, not_69_out;

  not not_1 (not_1_out, op3);
  not not_2 (not_2_out, op2);
  not not_3 (not_3_out, op2);
  not not_4 (not_4_out, op3);
  not not_5 (not_5_out, op0);
  not not_6 (not_6_out, op4);
  not not_7 (not_7_out, op3);
  not not_8 (not_8_out, op2);
  not not_9 (not_9_out, op3);
  not not_10 (not_10_out, op2);
  not not_11 (not_11_out, op1);
  not not_12 (not_12_out, op4);
  not not_13 (not_13_out, op2);
  not not_14 (not_14_out, op0);
  not not_15 (not_15_out, op4);
  not not_16 (not_16_out, op3);
  not not_17 (not_17_out, op2);
  not not_18 (not_18_out, op4);
  not not_19 (not_19_out, op2);
  not not_20 (not_20_out, op0);
  not not_21 (not_21_out, op3);
  not not_22 (not_22_out, op2);
  not not_23 (not_23_out, op1);
  not not_24 (not_24_out, op4);
  not not_25 (not_25_out, op3);
  not not_26 (not_26_out, op3);
  not not_27 (not_27_out, op2);
  not not_28 (not_28_out, op4);
  not not_29 (not_29_out, op0);
  not not_30 (not_30_out, op3);
  not not_31 (not_31_out, op0);
  not not_32 (not_32_out, op2);
  not not_33 (not_33_out, op0);
  not not_34 (not_34_out, op1);
  not not_35 (not_35_out, op2);
  not not_36 (not_36_out, op4);
  not not_37 (not_37_out, op3);
  not not_38 (not_38_out, op2);
  not not_39 (not_39_out, op4);
  not not_40 (not_40_out, op0);
  not not_41 (not_41_out, op3);
  not not_42 (not_42_out, op2);
  not not_43 (not_43_out, op0);
  not not_44 (not_44_out, op4);
  not not_45 (not_45_out, op3);
  not not_46 (not_46_out, op0);
  not not_47 (not_47_out, op4);
  not not_48 (not_48_out, op3);
  not not_49 (not_49_out, op1);
  not not_50 (not_50_out, op1);
  not not_51 (not_51_out, op0);
  not not_52 (not_52_out, op4);
  not not_53 (not_53_out, op3);
  not not_54 (not_54_out, op2);
  not not_55 (not_55_out, op4);
  not not_56 (not_56_out, op3);
  not not_57 (not_57_out, op0);
  not not_58 (not_58_out, op4);
  not not_59 (not_59_out, op0);
  not not_60 (not_60_out, op4);
  not not_61 (not_61_out, op3);
  not not_62 (not_62_out, op1);
  not not_63 (not_63_out, op4);
  not not_64 (not_64_out, op3);
  not not_65 (not_65_out, op3);
  not not_66 (not_66_out, op2);
  not not_67 (not_67_out, op2);
  not not_68 (not_68_out, op0);
  not not_69 (not_69_out, op0);
  and and_1 (and_1_out, not_1_out, not_2_out, op0);
  and and_2 (and_2_out, op4, not_3_out);
  and and_3 (and_3_out, op4, not_4_out, op0);
  and and_4 (and_4_out, op4, op1);
  and and_5 (and_5_out, op4, op3, not_5_out);
  and and_6 (and_6_out, not_6_out, not_7_out, not_8_out, op0);
  and and_7 (and_7_out, not_9_out, not_10_out, not_11_out, op0);
  and and_8 (and_8_out, not_12_out, op3, not_13_out, op1, not_14_out);
  and and_9 (and_9_out, op3, op2, op1, op0);
  and and_10 (and_10_out, op4, op2, op1, op0);
  and and_11 (and_11_out, not_15_out, not_16_out, not_17_out, op0);
  and and_12 (and_12_out, not_18_out, op3, not_19_out, op1, not_20_out);
  and and_13 (and_13_out, op3, op2, op1, op0);
  and and_14 (and_14_out, op4, not_21_out, not_22_out, not_23_out);
  and and_15 (and_15_out, op4, op2, op1, op0);
  and and_16 (and_16_out, not_24_out, not_25_out, op0);
  and and_17 (and_17_out, not_26_out, not_27_out, op0);
  and and_18 (and_18_out, not_28_out, op2, not_29_out);
  and and_19 (and_19_out, not_30_out, op2, not_31_out);
  and and_20 (and_20_out, op3, not_32_out, op1);
  and and_21 (and_21_out, op3, op1, not_33_out);
  and and_22 (and_22_out, op4, not_34_out, op0);
  and and_23 (and_23_out, op4, op3, not_35_out);
  and and_24 (and_24_out, not_36_out, not_37_out, not_38_out, op0);
  and and_25 (and_25_out, not_39_out, op1, not_40_out);
  and and_26 (and_26_out, not_41_out, not_42_out, op1, not_43_out);
  and and_27 (and_27_out, not_44_out, not_45_out, op2, not_46_out);
  and and_28 (and_28_out, not_47_out, op3, op2, op1);
  and and_29 (and_29_out, op4, not_48_out, not_49_out, op0);
  and and_30 (and_30_out, op4, op3, op2, not_50_out, not_51_out);
  and and_31 (and_31_out, not_52_out, not_53_out, not_54_out, op0);
  and and_32 (and_32_out, not_55_out, not_56_out, op2, not_57_out);
  and and_33 (and_33_out, not_58_out, op3, op1, not_59_out);
  and and_34 (and_34_out, not_60_out, op3, op2, op1);
  and and_35 (and_35_out, op4, not_61_out, not_62_out, op0);
  and and_36 (and_36_out, not_63_out, not_64_out, op0);
  and and_37 (and_37_out, not_65_out, not_66_out, op1);
  and and_38 (and_38_out, op4, not_67_out);
  and and_39 (and_39_out, op4, op1, not_68_out);
  and and_40 (and_40_out, op4, op3, not_69_out);
  and and_41 (and_41_out, op4, op3, op1);
  or or_1 (r0, and_1_out, and_2_out, and_3_out, and_4_out, and_5_out);
  or or_2 (r1, and_6_out, and_7_out, and_8_out, and_9_out, and_10_out);
  or or_3 (r2, and_11_out, and_12_out, and_13_out, and_14_out, and_15_out);
  or or_4 (r3, and_16_out, and_17_out, and_18_out, and_19_out, and_20_out, and_21_out, and_22_out, and_23_out);
  or or_5 (r4, and_24_out, and_25_out, and_26_out, and_27_out, and_28_out, and_29_out, and_30_out);
  or or_6 (r5, and_31_out, and_32_out, and_33_out, and_34_out, and_35_out);
  or or_7 (r6, and_36_out, and_37_out, and_38_out, and_39_out, and_40_out, and_41_out);
endmodule

module op_dec_col_11 (
  input  op4,
  input  op3,
  input  op2,
  input  op1,
  input  op0,
  output r0,
  output r1,
  output r2,
  output r3,
  output r4,
  output r5,
  output r6
);

  wire and_1_out, and_2_out, and_3_out, and_4_out, and_5_out, and_6_out, and_7_out, and_8_out, and_9_out,
       and_10_out, and_11_out, and_12_out, and_13_out, and_14_out, and_15_out, and_16_out, and_17_out,
       and_18_out, and_19_out, and_20_out, and_21_out, and_22_out, and_23_out, and_24_out, and_25_out,
       and_26_out, and_27_out, and_28_out, and_29_out, and_30_out, and_31_out, and_32_out, and_33_out,
       and_34_out, and_35_out, and_36_out, and_37_out, and_38_out, and_39_out, and_40_out, and_41_out,
       and_42_out, not_1_out, not_2_out, not_3_out, not_4_out, not_5_out, not_6_out, not_7_out, not_8_out,
       not_9_out, not_10_out, not_11_out, not_12_out, not_13_out, not_14_out, not_15_out, not_16_out,
       not_17_out, not_18_out, not_19_out, not_20_out, not_21_out, not_22_out, not_23_out, not_24_out,
       not_25_out, not_26_out, not_27_out, not_28_out, not_29_out, not_30_out, not_31_out, not_32_out,
       not_33_out, not_34_out, not_35_out, not_36_out, not_37_out, not_38_out, not_39_out, not_40_out,
       not_41_out, not_42_out, not_43_out, not_44_out, not_45_out, not_46_out, not_47_out, not_48_out,
       not_49_out, not_50_out, not_51_out, not_52_out, not_53_out, not_54_out, not_55_out, not_56_out,
       not_57_out, not_58_out, not_59_out, not_60_out, not_61_out, not_62_out, not_63_out, not_64_out,
       not_65_out, not_66_out, not_67_out, not_68_out, not_69_out;

  not not_1 (not_1_out, op4);
  not not_2 (not_2_out, op3);
  not not_3 (not_3_out, op4);
  not not_4 (not_4_out, op3);
  not not_5 (not_5_out, op1);
  not not_6 (not_6_out, op0);
  not not_7 (not_7_out, op2);
  not not_8 (not_8_out, op1);
  not not_9 (not_9_out, op1);
  not not_10 (not_10_out, op4);
  not not_11 (not_11_out, op3);
  not not_12 (not_12_out, op4);
  not not_13 (not_13_out, op3);
  not not_14 (not_14_out, op2);
  not not_15 (not_15_out, op2);
  not not_16 (not_16_out, op0);
  not not_17 (not_17_out, op3);
  not not_18 (not_18_out, op0);
  not not_19 (not_19_out, op1);
  not not_20 (not_20_out, op4);
  not not_21 (not_21_out, op3);
  not not_22 (not_22_out, op4);
  not not_23 (not_23_out, op0);
  not not_24 (not_24_out, op3);
  not not_25 (not_25_out, op2);
  not not_26 (not_26_out, op2);
  not not_27 (not_27_out, op0);
  not not_28 (not_28_out, op1);
  not not_29 (not_29_out, op0);
  not not_30 (not_30_out, op4);
  not not_31 (not_31_out, op3);
  not not_32 (not_32_out, op4);
  not not_33 (not_33_out, op2);
  not not_34 (not_34_out, op0);
  not not_35 (not_35_out, op2);
  not not_36 (not_36_out, op0);
  not not_37 (not_37_out, op1);
  not not_38 (not_38_out, op0);
  not not_39 (not_39_out, op1);
  not not_40 (not_40_out, op4);
  not not_41 (not_41_out, op3);
  not not_42 (not_42_out, op2);
  not not_43 (not_43_out, op3);
  not not_44 (not_44_out, op0);
  not not_45 (not_45_out, op2);
  not not_46 (not_46_out, op1);
  not not_47 (not_47_out, op4);
  not not_48 (not_48_out, op3);
  not not_49 (not_49_out, op3);
  not not_50 (not_50_out, op0);
  not not_51 (not_51_out, op4);
  not not_52 (not_52_out, op2);
  not not_53 (not_53_out, op2);
  not not_54 (not_54_out, op1);
  not not_55 (not_55_out, op4);
  not not_56 (not_56_out, op3);
  not not_57 (not_57_out, op2);
  not not_58 (not_58_out, op4);
  not not_59 (not_59_out, op3);
  not not_60 (not_60_out, op0);
  not not_61 (not_61_out, op3);
  not not_62 (not_62_out, op1);
  not not_63 (not_63_out, op0);
  not not_64 (not_64_out, op3);
  not not_65 (not_65_out, op2);
  not not_66 (not_66_out, op0);
  not not_67 (not_67_out, op2);
  not not_68 (not_68_out, op1);
  not not_69 (not_69_out, op1);
  and and_1 (and_1_out, not_1_out, not_2_out, op2, op0);
  and and_2 (and_2_out, not_3_out, op2, op1, op0);
  and and_3 (and_3_out, op4, not_4_out, not_5_out, not_6_out);
  and and_4 (and_4_out, op4, op3, not_7_out, not_8_out);
  and and_5 (and_5_out, op4, op3, not_9_out, op0);
  and and_6 (and_6_out, op4, op3, op2, op1);
  and and_7 (and_7_out, not_10_out, not_11_out, op2, op0);
  and and_8 (and_8_out, not_12_out, op2, op1, op0);
  and and_9 (and_9_out, op4, not_13_out, not_14_out, op1);
  and and_10 (and_10_out, op4, not_15_out, op1, not_16_out);
  and and_11 (and_11_out, op4, not_17_out, op2, not_18_out);
  and and_12 (and_12_out, op4, op3, op2, not_19_out);
  and and_13 (and_13_out, not_20_out, not_21_out, op2);
  and and_14 (and_14_out, not_22_out, op2, op1, not_23_out);
  and and_15 (and_15_out, op4, not_24_out, not_25_out, op1);
  and and_16 (and_16_out, op4, not_26_out, op1, not_27_out);
  and and_17 (and_17_out, op4, op2, not_28_out, not_29_out);
  and and_18 (and_18_out, op4, op3, op2, op0);
  and and_19 (and_19_out, not_30_out, not_31_out, op2);
  and and_20 (and_20_out, not_32_out, op3, not_33_out, op1);
  and and_21 (and_21_out, op3, op1, not_34_out);
  and and_22 (and_22_out, op4, not_35_out, not_36_out);
  and and_23 (and_23_out, op4, not_37_out, not_38_out);
  and and_24 (and_24_out, op4, op3, not_39_out);
  and and_25 (and_25_out, not_40_out, not_41_out, op2, op0);
  and and_26 (and_26_out, op4, not_42_out, op1, op0);
  and and_27 (and_27_out, op4, not_43_out, op2, not_44_out);
  and and_28 (and_28_out, op4, op3, not_45_out, op1);
  and and_29 (and_29_out, op4, op3, op2, not_46_out, op0);
  and and_30 (and_30_out, not_47_out, not_48_out, op2);
  and and_31 (and_31_out, not_49_out, op2, not_50_out);
  and and_32 (and_32_out, not_51_out, op2, op1);
  and and_33 (and_33_out, op4, not_52_out, op1, op0);
  and and_34 (and_34_out, op4, op3, not_53_out, op1);
  and and_35 (and_35_out, op4, op3, op2, not_54_out, op0);
  and and_36 (and_36_out, not_55_out, not_56_out, not_57_out, op0);
  and and_37 (and_37_out, not_58_out, not_59_out, op2, not_60_out);
  and and_38 (and_38_out, not_61_out, op2, not_62_out, not_63_out);
  and and_39 (and_39_out, op3, op2, op1);
  and and_40 (and_40_out, op4, not_64_out, not_65_out, not_66_out);
  and and_41 (and_41_out, op4, not_67_out, not_68_out);
  and and_42 (and_42_out, op4, op3, not_69_out);
  or or_1 (r0, and_1_out, and_2_out, and_3_out, and_4_out, and_5_out, and_6_out);
  or or_2 (r1, and_7_out, and_8_out, and_9_out, and_10_out, and_11_out, and_12_out);
  or or_3 (r2, and_13_out, and_14_out, and_15_out, and_16_out, and_17_out, and_18_out);
  or or_4 (r3, and_19_out, and_20_out, and_21_out, and_22_out, and_23_out, and_24_out);
  or or_5 (r4, and_25_out, and_26_out, and_27_out, and_28_out, and_29_out);
  or or_6 (r5, and_30_out, and_31_out, and_32_out, and_33_out, and_34_out, and_35_out);
  or or_7 (r6, and_36_out, and_37_out, and_38_out, and_39_out, and_40_out, and_41_out, and_42_out);
endmodule

module op_dec_col_12 (
  input  op4,
  input  op3,
  input  op2,
  input  op1,
  input  op0,
  output r0,
  output r1,
  output r2,
  output r3,
  output r4,
  output r5,
  output r6
);

  wire and_1_out, and_2_out, and_3_out, and_4_out, and_5_out, and_6_out, and_7_out, and_8_out, and_9_out,
       and_10_out, and_11_out, and_12_out, and_13_out, and_14_out, and_15_out, and_16_out, and_17_out,
       and_18_out, and_19_out, not_1_out, not_2_out, not_3_out, not_4_out, not_5_out, not_6_out, not_7_out,
       not_8_out, not_9_out, not_10_out, not_11_out, not_12_out, not_13_out, not_14_out, not_15_out,
       not_16_out, not_17_out, not_18_out, not_19_out, not_20_out, not_21_out, not_22_out, not_23_out,
       not_24_out, not_25_out, not_26_out, not_27_out, not_28_out, not_29_out, not_30_out, not_31_out,
       not_32_out, not_33_out, not_34_out, not_35_out, not_36_out, not_37_out;

  and and_1 (and_1_out, op3, op2, op1, op0);
  and and_2 (and_2_out, op4, op3, op2, op1);
  not not_1 (not_1_out, op2);
  not not_2 (not_2_out, op1);
  not not_3 (not_3_out, op0);
  not not_4 (not_4_out, op2);
  not not_5 (not_5_out, op1);
  not not_6 (not_6_out, op4);
  not not_7 (not_7_out, op3);
  not not_8 (not_8_out, op0);
  not not_9 (not_9_out, op4);
  not not_10 (not_10_out, op0);
  not not_11 (not_11_out, op2);
  not not_12 (not_12_out, op1);
  not not_13 (not_13_out, op0);
  not not_14 (not_14_out, op2);
  not not_15 (not_15_out, op1);
  not not_16 (not_16_out, op4);
  not not_17 (not_17_out, op2);
  not not_18 (not_18_out, op3);
  not not_19 (not_19_out, op2);
  not not_20 (not_20_out, op1);
  not not_21 (not_21_out, op0);
  not not_22 (not_22_out, op2);
  not not_23 (not_23_out, op1);
  not not_24 (not_24_out, op0);
  not not_25 (not_25_out, op2);
  not not_26 (not_26_out, op1);
  not not_27 (not_27_out, op0);
  not not_28 (not_28_out, op2);
  not not_29 (not_29_out, op1);
  not not_30 (not_30_out, op2);
  not not_31 (not_31_out, op1);
  not not_32 (not_32_out, op0);
  not not_33 (not_33_out, op2);
  not not_34 (not_34_out, op1);
  not not_35 (not_35_out, op4);
  not not_36 (not_36_out, op3);
  not not_37 (not_37_out, op0);
  or or_1 (r0, and_1_out, and_2_out);
  and and_3 (and_3_out, op4, not_1_out, not_2_out, not_3_out);
  and and_4 (and_4_out, op4, op3, not_4_out, not_5_out);
  and and_5 (and_5_out, not_6_out, not_7_out, op2, not_8_out);
  and and_6 (and_6_out, not_9_out, op2, op1, not_10_out);
  and and_7 (and_7_out, op4, not_11_out, not_12_out, not_13_out);
  and and_8 (and_8_out, op4, op3, not_14_out, not_15_out);
  and and_9 (and_9_out, op4, op3, op2, op1, op0);
  and and_10 (and_10_out, not_16_out, op3, not_17_out, op1);
  and and_11 (and_11_out, op4, not_18_out, not_19_out, not_20_out, not_21_out);
  and and_12 (and_12_out, op4, op3, not_22_out, not_23_out, op0);
  and and_13 (and_13_out, op4, op3, op2, op1, not_24_out);
  and and_14 (and_14_out, op4, not_25_out, not_26_out, not_27_out);
  and and_15 (and_15_out, op4, op3, not_28_out, not_29_out);
  and and_16 (and_16_out, op4, not_30_out, not_31_out, not_32_out);
  and and_17 (and_17_out, op4, op3, not_33_out, not_34_out);
  and and_18 (and_18_out, not_35_out, not_36_out, op2, not_37_out);
  and and_19 (and_19_out, op3, op2, op1);
  or or_2 (r1, and_3_out, and_4_out);
  or or_3 (r2, and_5_out, and_6_out, and_7_out, and_8_out, and_9_out);
  or or_4 (r3, and_10_out, and_11_out, and_12_out, and_13_out);
  or or_5 (r4, and_14_out, and_15_out);
  or or_6 (r5, and_16_out, and_17_out);
  or or_7 (r6, and_18_out, and_19_out);
endmodule

module op_dec_col_13 (
  input  op4,
  input  op3,
  input  op2,
  input  op1,
  input  op0,
  output r0,
  output r1,
  output r2,
  output r3,
  output r4,
  output r5,
  output r6
);

  wire not_1_out, not_2_out;

  and and_1 (r0, op4, op3, op2, op1, op0);
  not not_1 (not_1_out, op0);
  not not_2 (not_2_out, op0);
  and and_2 (r3, op4, op3, op2, op1, op0);
  and and_3 (r4, op4, op3, op2, op1);
  and and_4 (r5, op4, op3, op2, op1);
  and and_5 (r1, op4, op3, op2, op1, not_1_out);
  and and_6 (r2, op4, op3, op2, op1, not_2_out);

  assign r6 = 1'b0;
endmodule

// ALU Code (Disp. Driv.)
module op_dec (
  input  [4:0] op,
  output [6:0] col_0,
  output [6:0] col_7,
  output [6:0] col_1,
  output [6:0] col_8,
  output [6:0] col_2,
  output [6:0] col_9,
  output [6:0] col_3,
  output [6:0] col_10,
  output [6:0] col_4,
  output [6:0] col_11,
  output [6:0] col_5,
  output [6:0] col_12,
  output [6:0] col_6,
  output [6:0] col_13
);

  op_dec_col_0 op_dec_col_0_1 (
    .op4(op[4]), .op3(op[3]), .op2(op[2]), .op1(op[1]), .op0(op[0]), .r0(col_0[6]), .r1(col_0[5]),
    .r2(col_0[4]), .r3(col_0[3]), .r4(col_0[2]), .r5(col_0[1]), .r6(col_0[0]));
  op_dec_col_1 op_dec_col_1_1 (
    .op4(op[4]), .op3(op[3]), .op2(op[2]), .op1(op[1]), .op0(op[0]), .r0(col_1[6]), .r1(col_1[5]),
    .r2(col_1[4]), .r3(col_1[3]), .r4(col_1[2]), .r5(col_1[1]), .r6(col_1[0]));
  op_dec_col_2 op_dec_col_2_1 (
    .op4(op[4]), .op3(op[3]), .op2(op[2]), .op1(op[1]), .op0(op[0]), .r0(col_2[6]), .r1(col_2[5]),
    .r2(col_2[4]), .r3(col_2[3]), .r4(col_2[2]), .r5(col_2[1]), .r6(col_2[0]));
  op_dec_col_3 op_dec_col_3_1 (
    .op4(op[4]), .op3(op[3]), .op2(op[2]), .op1(op[1]), .op0(op[0]), .r0(col_3[6]), .r1(col_3[5]),
    .r2(col_3[4]), .r3(col_3[3]), .r4(col_3[2]), .r5(col_3[1]), .r6(col_3[0]));
  op_dec_col_4 op_dec_col_4_1 (
    .op4(op[4]), .op3(op[3]), .op2(op[2]), .op1(op[1]), .op0(op[0]), .r0(col_4[6]), .r1(col_4[5]),
    .r2(col_4[4]), .r3(col_4[3]), .r4(col_4[2]), .r5(col_4[1]), .r6(col_4[0]));
  op_dec_col_5 op_dec_col_5_1 (
    .op4(op[4]), .op3(op[3]), .op2(op[2]), .op1(op[1]), .op0(op[0]), .r0(col_5[6]), .r1(col_5[5]),
    .r2(col_5[4]), .r3(col_5[3]), .r4(col_5[2]), .r5(col_5[1]), .r6(col_5[0]));
  op_dec_col_6 op_dec_col_6_1 (
    .op4(op[4]), .op3(op[3]), .op2(op[2]), .op1(op[1]), .op0(op[0]), .r0(col_6[6]), .r1(col_6[5]),
    .r2(col_6[4]), .r3(col_6[3]), .r4(col_6[2]), .r5(col_6[1]), .r6(col_6[0]));
  op_dec_col_7 op_dec_col_7_1 (
    .op4(op[4]), .op3(op[3]), .op2(op[2]), .op1(op[1]), .op0(op[0]), .r0(col_7[6]), .r1(col_7[5]),
    .r2(col_7[4]), .r3(col_7[3]), .r4(col_7[2]), .r5(col_7[1]), .r6(col_7[0]));
  op_dec_col_8 op_dec_col_8_1 (
    .op4(op[4]), .op3(op[3]), .op2(op[2]), .op1(op[1]), .op0(op[0]), .r0(col_8[6]), .r1(col_8[5]),
    .r2(col_8[4]), .r3(col_8[3]), .r4(col_8[2]), .r5(col_8[1]), .r6(col_8[0]));
  op_dec_col_9 op_dec_col_9_1 (
    .op4(op[4]), .op3(op[3]), .op2(op[2]), .op1(op[1]), .op0(op[0]), .r0(col_9[6]), .r1(col_9[5]),
    .r2(col_9[4]), .r3(col_9[3]), .r4(col_9[2]), .r5(col_9[1]), .r6(col_9[0]));
  op_dec_col_10 op_dec_col_10_1 (
    .op4(op[4]), .op3(op[3]), .op2(op[2]), .op1(op[1]), .op0(op[0]), .r0(col_10[6]), .r1(col_10[5]),
    .r2(col_10[4]), .r3(col_10[3]), .r4(col_10[2]), .r5(col_10[1]), .r6(col_10[0]));
  op_dec_col_11 op_dec_col_11_1 (
    .op4(op[4]), .op3(op[3]), .op2(op[2]), .op1(op[1]), .op0(op[0]), .r0(col_11[6]), .r1(col_11[5]),
    .r2(col_11[4]), .r3(col_11[3]), .r4(col_11[2]), .r5(col_11[1]), .r6(col_11[0]));
  op_dec_col_12 op_dec_col_12_1 (
    .op4(op[4]), .op3(op[3]), .op2(op[2]), .op1(op[1]), .op0(op[0]), .r0(col_12[6]), .r1(col_12[5]),
    .r2(col_12[4]), .r3(col_12[3]), .r4(col_12[2]), .r5(col_12[1]), .r6(col_12[0]));
  op_dec_col_13 op_dec_col_13_1 (
    .op4(op[4]), .op3(op[3]), .op2(op[2]), .op1(op[1]), .op0(op[0]), .r0(col_13[6]), .r1(col_13[5]),
    .r2(col_13[4]), .r3(col_13[3]), .r4(col_13[2]), .r5(col_13[1]), .r6(col_13[0]));
endmodule

module OR (
  input  [5:0] in,
  output out
);

  or or_1 (out, in[0], in[1], in[2], in[3], in[4], in[5]);
endmodule

module _4 (
  input  [7:0] in,
  output [7:0] out
);

  Shifter shifter_1 (.in(in), .\dist (3'b010), .out(out));
endmodule

module _1 (
  input  [7:0] in,
  output [7:0] out
);

  Adder adder_1 (.a(in), .b(8'h1), .out(out));  // open: cin, cout
endmodule
