// Logisim project alu.circ as structural Verilog: 14 circuits, main circuit FA
module FA (
  input  cin,
  input  a,
  input  b,
  output cout,
  output s
);

  wire and_1_out, and_2_out, and_3_out, and_4_out, and_5_out, and_6_out, and_7_out, not_1_out, not_2_out,
       not_3_out, not_4_out, not_5_out, not_6_out;

  and and_1 (and_1_out, a, b);
  and and_2 (and_2_out, cin, b);
  and and_3 (and_3_out, cin, a);
  not not_1 (not_1_out, cin);
  not not_2 (not_2_out, a);
  not not_3 (not_3_out, cin);
  not not_4 (not_4_out, b);
  not not_5 (not_5_out, a);
  not not_6 (not_6_out, b);
  or or_1 (cout, and_1_out, and_2_out, and_3_out);
  and and_4 (and_4_out, not_1_out, not_2_out, b);
  and and_5 (and_5_out, not_3_out, a, not_4_out);
  and and_6 (and_6_out, cin, not_5_out, not_6_out);
  and and_7 (and_7_out, cin, a, b);
  or or_2 (s, and_4_out, and_5_out, and_6_out, and_7_out);
endmodule

module FA2 (
  input  [1:0] a,
  input  [1:0] b,
  input  cin,
  output [1:0] sum,
  output [2:0] sum___carry,
  output cout
);

  wire fa_1_cout;

  FA fa_1 (.cin(cin), .a(a[0]), .b(b[0]), .cout(fa_1_cout), .s(sum[0]));
  FA fa_2 (.cin(fa_1_cout), .a(a[1]), .b(b[1]), .cout(cout), .s(sum[1]));

  assign sum___carry = {cout, sum};
endmodule

module FA16 (
  input  in_1,
  input  in_2,
  input  in_3,
  input  in_4,
  input  in_5,
  input  in_6,
  input  in_7,
  input  in_8,
  input  in_9,
  input  in_10,
  input  in_11,
  input  in_12,
  input  in_13,
  input  in_14,
  input  in_15,
  input  in_16,
  input  in_17,
  input  in_18,
  input  in_19,
  input  in_20,
  input  in_21,
  input  in_22,
  input  in_23,
  input  in_24,
  input  in_25,
  input  in_26,
  input  in_27,
  input  in_28,
  input  in_29,
  input  in_30,
  input  in_31,
  input  in_32,
  input  in_33,
  output out_34,
  output out_35,
  output out_36,
  output out_37,
  output out_38,
  output out_39,
  output out_40,
  output out_41,
  output out_42,
  output out_43,
  output out_44,
  output out_45,
  output out_46,
  output out_47,
  output out_48,
  output out_49
);

  wire fa_1_cout, fa_2_cout, fa_3_cout, fa_4_cout, fa_5_cout, fa_6_cout, fa_7_cout, fa_8_cout, fa_9_cout,
       fa_10_cout, fa_11_cout, fa_12_cout, fa_13_cout, fa_14_cout, fa_15_cout;

  FA fa_1 (.cin(in_1), .a(in_2), .b(in_18), .cout(fa_1_cout), .s(out_34));
  FA fa_2 (.cin(fa_1_cout), .a(in_3), .b(in_19), .cout(fa_2_cout), .s(out_35));
  FA fa_3 (.cin(fa_2_cout), .a(in_4), .b(in_20), .cout(fa_3_cout), .s(out_36));
  FA fa_4 (.cin(fa_3_cout), .a(in_5), .b(in_21), .cout(fa_4_cout), .s(out_37));
  FA fa_5 (.cin(fa_4_cout), .a(in_6), .b(in_22), .cout(fa_5_cout), .s(out_38));
  FA fa_6 (.cin(fa_5_cout), .a(in_7), .b(in_23), .cout(fa_6_cout), .s(out_39));
  FA fa_7 (.cin(fa_6_cout), .a(in_8), .b(in_24), .cout(fa_7_cout), .s(out_40));
  FA fa_8 (.cin(fa_7_cout), .a(in_9), .b(in_25), .cout(fa_8_cout), .s(out_41));
  FA fa_9 (.cin(fa_8_cout), .a(in_10), .b(in_26), .cout(fa_9_cout), .s(out_42));
  FA fa_10 (.cin(fa_9_cout), .a(in_11), .b(in_27), .cout(fa_10_cout), .s(out_43));
  FA fa_11 (.cin(fa_10_cout), .a(in_12), .b(in_28), .cout(fa_11_cout), .s(out_44));
  FA fa_12 (.cin(fa_11_cout), .a(in_13), .b(in_29), .cout(fa_12_cout), .s(out_45));
  FA fa_13 (.cin(fa_12_cout), .a(in_14), .b(in_30), .cout(fa_13_cout), .s(out_46));
  FA fa_14 (.cin(fa_13_cout), .a(in_15), .b(in_31), .cout(fa_14_cout), .s(out_47));
  FA fa_15 (.cin(fa_14_cout), .a(in_16), .b(in_32), .cout(fa_15_cout), .s(out_48));
  FA fa_16 (.cin(fa_15_cout), .a(in_17), .b(in_33), .s(out_49));  // open: cout
endmodule

module CS4 (
  input  [3:0] a,
  input  cin,
  input  [3:0] b,
  output [3:0] s,
  output cout
);

  wire fa2_1_cout;
  wire [2:0] fa2_2_sum___carry, fa2_3_sum___carry;

  Hex_Digit_Display hex_digit_display_1 (.value(a));  // open: dp
  Hex_Digit_Display hex_digit_display_2 (.value(b));  // open: dp
  FA2 fa2_1 (.a(a[1:0]), .cin(cin), .b(b[1:0]), .cout(fa2_1_cout), .sum(s[1:0]));  // open: sum___carry
  FA2 fa2_2 (.a(a[3:2]), .cin(1'b0), .b(b[3:2]), .sum___carry(fa2_2_sum___carry));  // open: cout, sum
  FA2 fa2_3 (.a(a[3:2]), .cin(1'b1), .b(b[3:2]), .sum___carry(fa2_3_sum___carry));  // open: cout, sum
  Multiplexer #(.width(3), .disabled(0), .enable("false")) multiplexer_1 (
    .in0(fa2_2_sum___carry), .in1(fa2_3_sum___carry), .out({cout, s[3:2]}), .sel(fa2_1_cout));
  Hex_Digit_Display hex_digit_display_3 (.value(s));  // open: dp

  // Notes on the sheet:
  //   fixed carry 0
  //   fixed carry 1
endmodule

module CS8 (
  input  [7:0] a,
  input  cin,
  input  [7:0] b,
  output [7:0] s,
  output cout
);

  wire cs4_1_cout;
  wire [3:0] cs4_2_s, cs4_3_s;
  wire [4:4] cs4_2_cout, cs4_3_cout;

  CS4 cs4_1 (.s(s[3:0]), .cout(cs4_1_cout), .a(a[3:0]), .cin(cin), .b(b[3:0]));
  CS4 cs4_2 (.s(cs4_2_s), .cout(cs4_2_cout[4]), .a(a[7:4]), .cin(1'b0), .b(b[7:4]));
  CS4 cs4_3 (.s(cs4_3_s), .cout(cs4_3_cout[4]), .a(a[7:4]), .cin(1'b1), .b(b[7:4]));
  Multiplexer #(.width(5), .disabled(0), .enable("false")) multiplexer_1 (
    .in0({cs4_2_cout[4], cs4_2_s}), .in1({cs4_3_cout[4], cs4_3_s}), .out({cout, s[7:4]}), .sel(cs4_1_cout));
endmodule

module CS16 (
  input  [15:0] a,
  input  cin,
  input  [15:0] b,
  output [15:0] s,
  output cout
);

  wire cs8_1_cout;
  wire [7:0] cs8_2_s, cs8_3_s;
  wire [8:8] cs8_2_cout, cs8_3_cout;

  CS8 cs8_1 (.s(s[7:0]), .cout(cs8_1_cout), .a(a[7:0]), .cin(cin), .b(b[7:0]));
  CS8 cs8_2 (.s(cs8_2_s), .cout(cs8_2_cout[8]), .a(a[15:8]), .cin(1'b0), .b(b[15:8]));
  CS8 cs8_3 (.s(cs8_3_s), .cout(cs8_3_cout[8]), .a(a[15:8]), .cin(1'b1), .b(b[15:8]));
  Hex_Digit_Display hex_digit_display_1 (.value(b[11:8]));  // open: dp
  Hex_Digit_Display hex_digit_display_2 (.value(b[15:12]));  // open: dp
  Hex_Digit_Display hex_digit_display_3 (.value(a[11:8]));  // open: dp
  Hex_Digit_Display hex_digit_display_4 (.value(a[15:12]));  // open: dp
  Hex_Digit_Display hex_digit_display_5 (.value(b[3:0]));  // open: dp
  Hex_Digit_Display hex_digit_display_6 (.value(b[7:4]));  // open: dp
  Hex_Digit_Display hex_digit_display_7 (.value(a[3:0]));  // open: dp
  Hex_Digit_Display hex_digit_display_8 (.value(a[7:4]));  // open: dp
  Multiplexer #(.width(9), .disabled(0), .enable("false")) multiplexer_1 (
    .in0({cs8_2_cout[8], cs8_2_s}), .in1({cs8_3_cout[8], cs8_3_s}), .out({cout, s[15:8]}), .sel(cs8_1_cout));
  Hex_Digit_Display hex_digit_display_9 (.value(s[11:8]));  // open: dp
  Hex_Digit_Display hex_digit_display_10 (.value(s[15:12]));  // open: dp
  Hex_Digit_Display hex_digit_display_11 (.value(s[7:4]));  // open: dp
  Hex_Digit_Display hex_digit_display_12 (.value(s[3:0]));  // open: dp
endmodule

// PA
module PA__Partial_Adder (
  input  cin,
  input  a,
  input  b,
  output s,
  output g,
  output p
);

  wire and_2_out, and_3_out, and_4_out, and_5_out, and_6_out, and_7_out, not_1_out, not_2_out, not_3_out,
       not_4_out, not_5_out, not_6_out, not_7_out, not_8_out;

  not not_1 (not_1_out, cin);
  not not_2 (not_2_out, a);
  not not_3 (not_3_out, cin);
  not not_4 (not_4_out, b);
  not not_5 (not_5_out, a);
  not not_6 (not_6_out, b);
  and and_1 (g, a, b);
  not not_7 (not_7_out, a);
  not not_8 (not_8_out, b);
  and and_2 (and_2_out, not_1_out, not_2_out, b);
  and and_3 (and_3_out, not_3_out, a, not_4_out);
  and and_4 (and_4_out, cin, not_5_out, not_6_out);
  and and_5 (and_5_out, cin, a, b);
  and and_6 (and_6_out, not_7_out, b);
  and and_7 (and_7_out, a, not_8_out);
  or or_1 (s, and_2_out, and_3_out, and_4_out, and_5_out);
  or or_2 (p, and_6_out, and_7_out);
endmodule

// LCU
module LCU4 (
  input  c0in,
  input  g0,
  input  p0,
  input  g1,
  input  p1,
  input  g2,
  input  p2,
  input  g3,
  input  p3,
  output c1out,
  output c2out,
  output c3out,
  output c4out,
  output gg,
  output pg
);

  wire and_1_out, and_2_out, and_3_out, and_4_out, and_5_out, and_6_out, and_7_out, and_8_out, and_9_out,
       and_10_out, and_11_out, and_12_out, and_13_out;

  and and_1 (and_1_out, p0, c0in);
  and and_2 (and_2_out, g0, p1);
  and and_3 (and_3_out, c0in, p0, p1);
  and and_4 (and_4_out, g1, p2);
  and and_5 (and_5_out, g0, p1, p2);
  and and_6 (and_6_out, c0in, p0, p1, p2);
  and and_7 (and_7_out, g2, p3);
  and and_8 (and_8_out, g1, p2, p3);
  and and_9 (and_9_out, g0, p1, p2, p3);
  and and_10 (and_10_out, c0in, p0, p1, p2, p3);
  and and_11 (and_11_out, p3, g2);
  and and_12 (and_12_out, p3, p2, g1);
  and and_13 (and_13_out, p3, p2, p1, g0);
  and and_14 (pg, p3, p2, p1, p0);
  or or_1 (c1out, g0, and_1_out);
  or or_2 (c2out, g1, and_2_out, and_3_out);
  or or_3 (c3out, g2, and_4_out, and_5_out, and_6_out);
  or or_4 (c4out, g3, and_7_out, and_8_out, and_9_out, and_10_out);
  or or_5 (gg, g3, and_11_out, and_12_out, and_13_out);
endmodule

module CLA4 (
  input  cin,
  input  [3:0] a,
  input  [3:0] b,
  output [3:0] s0,
  output c4,
  output g,
  output p
);

  wire lcu4_1_c1out, lcu4_1_c2out, lcu4_1_c3out, pa_partial_adder_1_g, pa_partial_adder_1_p,
       pa_partial_adder_2_g, pa_partial_adder_2_p, pa_partial_adder_3_g, pa_partial_adder_3_p,
       pa_partial_adder_4_g, pa_partial_adder_4_p;

  Hex_Digit_Display hex_digit_display_1 (.value(a));  // open: dp
  Hex_Digit_Display hex_digit_display_2 (.value(b));  // open: dp
  PA__Partial_Adder pa_partial_adder_1 (
    .cin(cin), .a(a[0]), .b(b[0]), .s(s0[0]), .g(pa_partial_adder_1_g), .p(pa_partial_adder_1_p));
  PA__Partial_Adder pa_partial_adder_2 (
    .cin(lcu4_1_c1out), .a(a[1]), .b(b[1]), .s(s0[1]), .g(pa_partial_adder_2_g), .p(pa_partial_adder_2_p));
  PA__Partial_Adder pa_partial_adder_3 (
    .cin(lcu4_1_c2out), .a(a[2]), .b(b[2]), .s(s0[2]), .g(pa_partial_adder_3_g), .p(pa_partial_adder_3_p));
  PA__Partial_Adder pa_partial_adder_4 (
    .cin(lcu4_1_c3out), .a(a[3]), .b(b[3]), .s(s0[3]), .g(pa_partial_adder_4_g), .p(pa_partial_adder_4_p));
  LCU4 lcu4_1 (
    .c0in(cin), .g0(pa_partial_adder_1_g), .p0(pa_partial_adder_1_p), .g1(pa_partial_adder_2_g),
    .p1(pa_partial_adder_2_p), .g2(pa_partial_adder_3_g), .p2(pa_partial_adder_3_p),
    .g3(pa_partial_adder_4_g), .p3(pa_partial_adder_4_p), .c1out(lcu4_1_c1out), .c2out(lcu4_1_c2out),
    .c3out(lcu4_1_c3out), .c4out(c4), .gg(g), .pg(p));
  Hex_Digit_Display hex_digit_display_3 (.value(s0));  // open: dp
endmodule

module LU1 (
  input  x,
  input  y,
  input  [2:0] s,
  output out_4
);

  wire and_1_out, buffer_1_out, buffer_2_out, not_1_out, not_2_out, or_1_out;

  buf buffer_1 (buffer_1_out, x);
  buf buffer_2 (buffer_2_out, y);
  not not_1 (not_1_out, x);
  not not_2 (not_2_out, y);
  and and_1 (and_1_out, x, y);
  or or_1 (or_1_out, x, y);
  Multiplexer #(.select(3), .disabled(0), .enable("false")) multiplexer_1 (
    .in0(1'b0), .in1(1'b1), .in2(buffer_1_out), .in3(buffer_2_out), .in4(not_1_out), .in5(not_2_out),
    .in6(and_1_out), .in7(or_1_out), .out(out_4), .sel(s));

  // Notes on the sheet:
  //   0, 1, x, y, ~x, ~y, AND, OR
endmodule

// LU
module LU8 (
  input  [7:0] x,
  input  [7:0] y,
  input  [2:0] s,
  output [7:0] z
);

  LU1 lu1_1 (.s(s), .out_4(z[6]), .x(x[6]), .y(y[6]));
  LU1 lu1_2 (.s(s), .out_4(z[7]), .x(x[7]), .y(y[7]));
  LU1 lu1_3 (.s(s), .out_4(z[5]), .x(x[5]), .y(y[5]));
  LU1 lu1_4 (.s(s), .out_4(z[4]), .x(x[4]), .y(y[4]));
  LU1 lu1_5 (.s(s), .out_4(z[3]), .x(x[3]), .y(y[3]));
  LU1 lu1_6 (.s(s), .out_4(z[1]), .x(x[1]), .y(y[1]));
  LU1 lu1_7 (.s(s), .out_4(z[2]), .x(x[2]), .y(y[2]));
  LU1 lu1_8 (.s(s), .out_4(z[0]), .x(x[0]), .y(y[0]));

  // Notes on the sheet:
  //   0, 1, x, y, ~x, ~y, AND, OR
endmodule

// AU
module AU8 (
  input  [7:0] x,
  input  [7:0] y,
  input  [2:0] s,
  output [7:0] z,
  output [1:0] flags
);

  wire [3:0] bitadder_1_out;
  wire [7:0] adder_1_out, adder_2_out, bit_extender_1_out, negator_1_out, shifter_1_out, subtractor_1_out,
       subtractor_2_out;

  Hex_Digit_Display hex_digit_display_1 (.value(x[3:0]));  // open: dp
  Hex_Digit_Display hex_digit_display_2 (.value(x[7:4]));  // open: dp
  Hex_Digit_Display hex_digit_display_3 (.value(y[7:4]));  // open: dp
  Adder adder_1 (.a(x), .b(y), .out(adder_1_out));  // open: cin, cout
  Subtractor subtractor_1 (.a(x), .b(y), .out(subtractor_1_out));  // open: bin, bout
  Adder adder_2 (.a(x), .b(8'h1), .out(adder_2_out));  // open: cin, cout
  Subtractor subtractor_2 (.a(x), .b(8'h1), .out(subtractor_2_out));  // open: bin, bout
  Negator negator_1 (.in(x), .out(negator_1_out));
  Shifter shifter_1 (.in(x), .\dist (y[2:0]), .out(shifter_1_out));
  BitAdder bitadder_1 (.in0(x), .out(bitadder_1_out));
  Hex_Digit_Display hex_digit_display_4 (.value(y[3:0]));  // open: dp
  assign bit_extender_1_out = {{4{1'b0}}, bitadder_1_out};  // Bit_Extender bit_extender_1
  Hex_Digit_Display hex_digit_display_5 (.value(z[7:4]));  // open: dp
  Hex_Digit_Display hex_digit_display_6 (.value(z[3:0]));  // open: dp
  Multiplexer #(.select(3), .width(8), .disabled(0), .enable("false")) multiplexer_1 (
    .in0(8'h2), .in1(adder_1_out), .in2(subtractor_1_out), .in3(adder_2_out), .in4(subtractor_2_out),
    .in5(negator_1_out), .in6(shifter_1_out), .in7(bit_extender_1_out), .out(z), .sel(s));
  Comparator comparator_1 (.a(z), .b({8{1'b0}}), .eq(flags[0]), .lt(flags[1]));  // open: gt

  // Notes on the sheet:
  //   sign
  //   2, +, -, INC, DEC, NEG, SHL, POPCNT
  //   zero
endmodule

module ALU8 (
  input  [7:0] x,
  input  [7:0] y,
  input  [3:0] op,
  output [7:0] z
);

  wire [7:0] au8_1_z, lu8_1_z;

  Hex_Digit_Display hex_digit_display_1 (.value(x[7:4]));  // open: dp
  Hex_Digit_Display hex_digit_display_2 (.value(x[3:0]));  // open: dp
  Hex_Digit_Display hex_digit_display_3 (.value(z[7:4]));  // open: dp
  Hex_Digit_Display hex_digit_display_4 (.value(z[3:0]));  // open: dp
  LU8 lu8_1 (.s(op[2:0]), .z(lu8_1_z), .x(x), .y(y));
  Multiplexer #(.width(8), .disabled(0), .enable("false")) multiplexer_1 (
    .in0(lu8_1_z), .in1(au8_1_z), .out(z), .sel(op[3]));
  AU8 au8_1 (.z(au8_1_z), .x(x), .y(y), .s(op[2:0]));  // open: flags
  Hex_Digit_Display hex_digit_display_5 (.value(y[3:0]));  // open: dp
  Hex_Digit_Display hex_digit_display_6 (.value(y[7:4]));  // open: dp

  // Notes on the sheet:
  //   0, 1, x, y, ~x, ~y, AND, OR
  //   2, +, -, INC, DEC, NEG, SHL, POPCNT
endmodule

module KSA4 (
  input  a3,
  input  a2,
  input  a1,
  input  a0,
  input  b3,
  input  b2,
  input  b1,
  input  b0,
  output cout,
  output S3,
  output S2,
  output S1,
  output S0
);

  wire and_1_out, and_2_out, and_3_out, and_4_out, and_5_out, G00_out, G01_out, G02_out, G03_out, G10_out,
       G11_out, G12_out, G13_out, G20_out, G21_out, G22_out, P01_out, P02_out, P03_out, P12_out, P13_out;

  xor P00 (S0, a0, b0);
  and G00 (G00_out, a0, b0);
  xor P01 (P01_out, a1, b1);
  and G01 (G01_out, a1, b1);
  xor P02 (P02_out, a2, b2);
  and G02 (G02_out, a2, b2);
  xor P03 (P03_out, a3, b3);
  and G03 (G03_out, a3, b3);
  and and_1 (and_1_out, G00_out, P01_out);
  or G11 (G11_out, and_1_out, G01_out);
  and P12 (P12_out, P01_out, P02_out);
  and and_2 (and_2_out, G01_out, P02_out);
  or G12 (G12_out, and_2_out, G02_out);
  and P13 (P13_out, P02_out, P03_out);
  and and_3 (and_3_out, P03_out, G02_out);
  or G13 (G13_out, and_3_out, G03_out);
  buf G10 (G10_out, G00_out);
  and and_4 (and_4_out, G10_out, P12_out);
  and and_5 (and_5_out, G11_out, P13_out);
  buf G20 (G20_out, G10_out);
  xor xor_1 (S1, G20_out, P01_out);
  buf G21 (G21_out, G11_out);
  xor xor_2 (S2, G21_out, P02_out);
  or G22 (G22_out, and_4_out, G12_out);
  or G23 (cout, and_5_out, G13_out);
  xor xor_3 (S3, G22_out, P03_out);

  // Notes on the sheet:
  //   Leitungsdichte ist große Herausvorderung
  //   4-bit Kogge-Stone Addierer
endmodule
