// Logisim project bus.circ as structural Verilog: 7 circuits, main circuit controlled buffer
module open_collector (
  input  in_1,
  input  in_2,
  input  in_3,
  input  in_4,
  input  in_5
);

  wire pull_resistor_1_node;

  // Probe on pull_resistor_1_node
  Pull_Resistor #(.pull(1)) pull_resistor_1 (.node(pull_resistor_1_node));
  assign pull_resistor_1_node = in_1 ? 1'b0 : 1'bz;  // Controlled_Buffer controlled_buffer_1
  // Probe on pull_resistor_1_node
  assign pull_resistor_1_node = in_2 ? 1'b0 : 1'bz;  // Controlled_Buffer controlled_buffer_2
  // Probe on pull_resistor_1_node
  assign pull_resistor_1_node = in_3 ? 1'b0 : 1'bz;  // Controlled_Buffer controlled_buffer_3
  // Probe on pull_resistor_1_node
  assign pull_resistor_1_node = in_4 ? 1'b0 : 1'bz;  // Controlled_Buffer controlled_buffer_4
  // Probe on pull_resistor_1_node
  Transistor #(.\type ("n")) transistor_1 (.in(1'b0), .out(pull_resistor_1_node), .gate(in_5));
endmodule

module open_collector_with_short (
  input  in_1,
  input  in_2,
  input  in_3,
  input  in_4,
  input  in_5,
  input  in_6
);

  wire pull_resistor_1_node;

  // Probe on pull_resistor_1_node
  Pull_Resistor #(.pull(1)) pull_resistor_1 (.node(pull_resistor_1_node));
  assign pull_resistor_1_node = in_2 ? 1'b0 : 1'bz;  // Controlled_Buffer controlled_buffer_1
  // Probe on pull_resistor_1_node
  assign pull_resistor_1_node = in_3 ? 1'b0 : 1'bz;  // Controlled_Buffer controlled_buffer_2
  // Probe on pull_resistor_1_node
  assign pull_resistor_1_node = in_4 ? 1'b0 : 1'bz;  // Controlled_Buffer controlled_buffer_3
  // Probe on pull_resistor_1_node
  assign pull_resistor_1_node = in_1 ? 1'b1 : 1'bz;  // Controlled_Buffer controlled_buffer_4
  assign pull_resistor_1_node = in_5 ? 1'b0 : 1'bz;  // Controlled_Buffer controlled_buffer_5
  // Probe on pull_resistor_1_node
  Transistor #(.\type ("n")) transistor_1 (.in(1'b0), .out(pull_resistor_1_node), .gate(in_6));
endmodule

module controlled_buffer (
  input  \input ,
  input  enable,
  output \output 
);

  assign \output  = enable ? \input  : 1'bz;  // Controlled_Buffer controlled_buffer_1
endmodule

module dual_input (
  input  \input ,
  input  enable,
  input  input_2,
  input  enable_2,
  output \output 
);

  assign \output  = enable ? \input  : 1'bz;  // Controlled_Buffer controlled_buffer_1
  assign \output  = enable_2 ? input_2 : 1'bz;  // Controlled_Buffer controlled_buffer_2
endmodule

module bus (
  input  phase_1,
  input  phase_2
);

  wire [7:0] controlled_buffer_1_out, controlled_buffer_2_out, register_1_q, register_2_q;

  Register #(.trigger("high"), .Select("low")) register_1 (.en(1'b1), .Q(register_1_q), .clk(1'b1));  // open: D, clr
  assign controlled_buffer_1_out = phase_1 ? register_1_q : 8'bz;  // Controlled_Buffer controlled_buffer_1
  Register #(.trigger("high"), .Select("low")) register_2 (
    .D(controlled_buffer_1_out), .en(phase_1), .Q(register_2_q), .clk(phase_1));  // open: clr
  assign controlled_buffer_2_out = phase_2 ? register_2_q : 8'bz;  // Controlled_Buffer controlled_buffer_2
  Register #(.trigger("high"), .Select("low")) register_3 (
    .D(controlled_buffer_2_out), .en(phase_2), .clk(phase_2));  // open: Q, clr
endmodule

module phased_controlled_buffer (
  input  [7:0] \input ,
  input  phase,
  input  enable,
  output [7:0] \output 
);

  wire and_1_out;

  and and_1 (and_1_out, phase, enable);
  assign \output  = and_1_out ? \input  : 8'bz;  // Controlled_Buffer controlled_buffer_1
endmodule

module multi_bus (
  input  X_en,
  input  Z1_en,
  input  Y_en,
  input  Z2_en,
  input  phase_1,
  input  phase_2
);

  wire [7:0] ALU_q, phased_controlled_buffer_1_output, phased_controlled_buffer_3_output,
       phased_controlled_buffer_4_output, X_q, Y_q;

  Register #(.trigger("high"), .Select("low")) X (.en(1'b1), .Q(X_q), .clk(1'b1));  // open: D, clr
  Register #(.trigger("high"), .Select("low")) Y (.en(1'b1), .Q(Y_q), .clk(1'b1));  // open: D, clr
  phased_controlled_buffer phased_controlled_buffer_1 (
    .\input (Y_q), .enable(Y_en), .\output (phased_controlled_buffer_1_output), .phase(phase_1));
  phased_controlled_buffer phased_controlled_buffer_2 (
    .\input (X_q), .enable(X_en), .\output (phased_controlled_buffer_1_output), .phase(phase_1));
  Register #(.trigger("high"), .Select("low")) ALU (
    .D(phased_controlled_buffer_1_output), .en(phase_1), .Q(ALU_q), .clk(phase_1));  // open: clr
  phased_controlled_buffer phased_controlled_buffer_3 (
    .\input (ALU_q), .enable(Z1_en), .\output (phased_controlled_buffer_3_output), .phase(phase_2));
  phased_controlled_buffer phased_controlled_buffer_4 (
    .\input (ALU_q), .enable(Z2_en), .\output (phased_controlled_buffer_4_output), .phase(phase_2));
  Register #(.trigger("high"), .Select("low")) Z1 (
    .D(phased_controlled_buffer_3_output), .en(phase_2), .clk(phase_2));  // open: Q, clr
  Register #(.trigger("high"), .Select("low")) Z2 (
    .D(phased_controlled_buffer_4_output), .en(phase_2), .clk(phase_2));  // open: Q, clr
endmodule
