// Logisim project 2InputMulitplexer.circ as structural Verilog
module MUX2 (
  input  d0,
  input  d1,
  input  s0,
  output out_4
);

  wire and_1_out, and_2_out, not_1_out;

  not not_1 (not_1_out, s0);
  and and_1 (and_1_out, d0, not_1_out);
  and and_2 (and_2_out, d1, s0);
  or or_1 (out_4, and_1_out, and_2_out);
endmodule

module _5_2_1Bit_Volladdierer (
  input  c_in,
  input  x,
  input  y,
  output s,
  output c_out
);

  wire and_1_out, and_2_out, xor_1_out;

  xor xor_1 (xor_1_out, x, y);
  xor xor_2 (s, xor_1_out, c_in);
  and and_1 (and_1_out, x, y);
  and and_2 (and_2_out, c_in, xor_1_out);
  or or_1 (c_out, and_1_out, and_2_out);
endmodule

module LogicUnit1 (
  input  a,
  input  b,
  input  s0,
  input  s1,
  output out_5
);

  wire [1:1] undriven;
  wire [3:0] and_1_out, not_1_out, or_1_out, xor_1_out;
  wire [3:1] multiplexer_1_out;

  and and_1 (and_1_out[0], a, b);
  or or_1 (or_1_out[0], a, b);
  not not_1 (not_1_out[0], a);
  xor xor_1 (xor_1_out[0], a, b);
  Multiplexer #(.select(2), .width(4), .enable("false")) multiplexer_1 (
    .in0(and_1_out), .in1(or_1_out), .in2(not_1_out), .in3(xor_1_out), .out({multiplexer_1_out, out_5}),
    .sel({undriven[1], s0}));
  // Pins of 1 and 4 bits meet at xor_1_out
  // Pins of 1 and 4 bits meet at and_1_out
  // Pins of 1 and 4 bits meet at or_1_out
  // Pins of 1 and 4 bits meet at not_1_out
  // Pins of 1 and 4 bits meet at {multiplexer_1_out, out_5}
  // Pins of 1 and 2 bits meet at {undriven[1], s0}

  // Notes on the sheet:
  //   4bit MUX einfügen
endmodule

module MUX4 (
  input  d0,
  input  d1,
  input  d2,
  input  d3,
  input  s0,
  input  s1,
  output out_7
);

  wire mux2_1_out_4, mux2_2_out_4, not_1_out;

  MUX2 mux2_1 (.d0(d0), .d1(d1), .s0(s0), .out_4(mux2_1_out_4));
  MUX2 mux2_2 (.d0(d2), .d1(d3), .s0(not_1_out), .out_4(mux2_2_out_4));
  not not_1 (not_1_out, s0);
  MUX2 mux2_3 (.d0(mux2_1_out_4), .d1(mux2_2_out_4), .s0(s1), .out_4(out_7));
endmodule
