// Logisim project ALU.circ as structural Verilog
module LU1 (
  input  a,
  input  b,
  input  [1:0] s1__s0,
  output f
);

  wire and_1_out, not_1_out, or_1_out, xor_1_out;

  and and_1 (and_1_out, a, b);
  or or_1 (or_1_out, a, b);
  not not_1 (not_1_out, a);
  xor xor_1 (xor_1_out, a, b);
  MUX4 mux4_1 (.a(and_1_out), .b(or_1_out), .c(not_1_out), .d(xor_1_out), .out_6(f), .in_1(s1__s0));
endmodule

module MUX2 (
  input  a,
  input  c,
  input  b,
  output out_4
);

  wire and_1_out, and_2_out, not_1_out;

  and and_1 (and_1_out, a, not_1_out);
  not not_1 (not_1_out, c);
  and and_2 (and_2_out, c, b);
  or or_1 (out_4, and_1_out, and_2_out);
endmodule

module MUX4 (
  input  [1:0] in_1,
  input  a,
  input  b,
  input  c,
  input  d,
  output out_6
);

  wire mux2_1_out_4, mux2_2_out_4;

  MUX2 mux2_1 (.a(a), .c(in_1[0]), .b(b), .out_4(mux2_1_out_4));
  MUX2 mux2_2 (.a(c), .c(in_1[0]), .b(d), .out_4(mux2_2_out_4));
  MUX2 mux2_3 (.a(mux2_1_out_4), .c(in_1[1]), .b(mux2_2_out_4), .out_4(out_6));
endmodule

module \xor  (
  input  a,
  input  b,
  output out_3
);

  wire and_1_out, and_2_out, not_1_out, not_2_out;

  and and_1 (and_1_out, a, not_1_out);
  not not_1 (not_1_out, b);
  and and_2 (and_2_out, b, not_2_out);
  not not_2 (not_2_out, a);
  or or_1 (out_3, and_1_out, and_2_out);
endmodule

module LU1_eff (
  input  in_1,
  input  a,
  input  in_3,
  input  b,
  output out_5
);

  wire and_1_out, and_2_out, and_3_out, and_4_out, not_1_out, not_2_out, not_3_out, not_4_out, not_5_out;

  not not_1 (not_1_out, b);
  not not_2 (not_2_out, in_3);
  not not_3 (not_3_out, a);
  not not_4 (not_4_out, in_3);
  not not_5 (not_5_out, in_1);
  and and_1 (and_1_out, a, in_3, not_1_out);
  and and_2 (and_2_out, not_2_out, a, b);
  and and_3 (and_3_out, not_3_out, in_1, not_4_out);
  and and_4 (and_4_out, not_5_out, in_3, b);
  or or_1 (out_5, and_1_out, and_2_out, and_3_out, and_4_out);

  // Notes on the sheet:
  //   s1   s0
endmodule

module C_GEN (
  input  s1,
  input  s0,
  output c__1
);

  xor xor_1 (c__1, s0, s1);
endmodule

module Y_Gen (
  input  s1,
  input  s0,
  input  b,
  output y
);

  wire not_1_out;

  not not_1 (not_1_out, b);
  MUX4 mux4_1 (.a(b), .b(not_1_out), .c(1'b0), .d(1'b1), .out_6(y), .in_1({s1, s0}));
endmodule

module FA (
  input  x,
  input  y,
  input  cin,
  output sum,
  output cout
);

  wire and_1_out, and_2_out, xor_1_out;

  xor xor_1 (xor_1_out, x, y);
  xor xor_2 (sum, cin, y, x);
  and and_1 (and_1_out, xor_1_out, cin);
  and and_2 (and_2_out, x, y);
  or or_1 (cout, and_1_out, and_2_out);
endmodule

module AU1 (
  input  a,
  input  b,
  input  s1,
  input  s0,
  input  cin,
  output cout,
  output sum
);

  wire y_gen_1_y;

  FA fa_1 (.sum(sum), .cout(cout), .x(a), .y(y_gen_1_y), .cin(cin));
  Y_Gen y_gen_1 (.y(y_gen_1_y), .b(b), .s1(s1), .s0(s0));
endmodule

module ALU1 (
  input  s2,
  input  s1,
  input  s0,
  input  a,
  input  b,
  input  cin,
  output f,
  output cout
);

  wire au1_1_sum, lu1_eff_1_out_5;

  LU1_eff lu1_eff_1 (.out_5(lu1_eff_1_out_5), .in_1(s1), .a(s0), .in_3(a), .b(b));
  MUX2 mux2_1 (.a(au1_1_sum), .c(s2), .b(lu1_eff_1_out_5), .out_4(f));
  AU1 au1_1 (.s1(s1), .s0(s0), .cin(cin), .a(a), .b(b), .cout(cout), .sum(au1_1_sum));
endmodule

module _4bit_ALU (
  input  [3:0] a,
  input  [3:0] b,
  input  s2,
  input  s1,
  input  s0,
  output c_flag,
  output [3:0] out_7
);

  wire alu1_2_cout, alu1_3_cout, alu1_4_cout, c_gen_1_c__1;

  ALU1 alu1_1 (.a(a[3]), .b(b[3]), .cin(alu1_2_cout), .s2(s2), .s1(s1), .s0(s0), .f(out_7[3]), .cout(c_flag));
  Hex_Digit_Display hex_digit_display_1 (.value(a));  // open: dp
  ALU1 alu1_2 (.a(a[2]), .b(b[2]), .cin(alu1_3_cout), .s2(s2), .s1(s1), .s0(s0), .f(out_7[2]), .cout(alu1_2_cout));
  ALU1 alu1_3 (.a(a[1]), .b(b[1]), .cin(alu1_4_cout), .s2(s2), .s1(s1), .s0(s0), .f(out_7[1]), .cout(alu1_3_cout));
  ALU1 alu1_4 (.a(a[0]), .b(b[0]), .cin(c_gen_1_c__1), .s2(s2), .s1(s1), .s0(s0), .f(out_7[0]), .cout(alu1_4_cout));
  Hex_Digit_Display hex_digit_display_2 (.value(out_7));  // open: dp
  Hex_Digit_Display hex_digit_display_3 (.value(b));  // open: dp
  C_GEN c_gen_1 (.c__1(c_gen_1_c__1), .s1(s1), .s0(s0));
endmodule

module Automaten (
  input  s,
  input  q1,
  input  q0,
  output d1,
  output d0
);

  wire and_1_out, and_2_out, and_3_out, not_1_out, not_2_out;

  not not_1 (not_1_out, q1);
  not not_2 (not_2_out, q1);
  and and_1 (and_1_out, not_1_out, q0);
  and and_2 (and_2_out, s, not_2_out);
  and and_3 (and_3_out, s, q0);
  or or_1 (d0, and_1_out, and_2_out, and_3_out);

  assign d1 = q0;
endmodule
