// Logisim project memory.circ as structural Verilog: 19 circuits, main circuit RS_Latch
module intro (
  input  \input ,
  input  in_2,
  input  [3:0] multi_bit_input,
  output \output ,
  output [3:0] multi_bit_output
);

  // AND_Gate gate is placed but not wired

  assign multi_bit_output = multi_bit_input;

  // Notes on the sheet:
  //   splitter
  //   logic true/1/high
  //   logic false/0/low
  //   floating/undefined
  //   splitter
  //   mulit-bit line
endmodule

module NAND (
  input  A,
  input  B,
  input  in_3,
  input  in_4,
  output Y,
  output out_6
);

  wire transistor_4_out;

  Transistor transistor_1 (.in(1'b1), .out(Y), .gate(A));
  Transistor transistor_2 (.in(1'b1), .out(Y), .gate(B));
  Transistor #(.\type ("n")) transistor_3 (.in(transistor_4_out), .out(Y), .gate(A));
  Transistor #(.\type ("n")) transistor_4 (.in(1'b0), .out(transistor_4_out), .gate(B));
  nand nand_1 (out_6, in_3, in_4);

  // Notes on the sheet:
  //   CMOS NAND
  //   - / GND
  //   + / Vdd
  //   A B | A * B | ~(A * B)
  //   0 0 |     0    |    1
  //   0 1 |     0    |    1
  //   1 0 |     0    |    1
  //   1 1 |     1    |    0
  //   abstrahiertes Boolsches NAND
  //   Spannungsversorgnung wird hier weg gelassen
endmodule

module AND__NAND___NOT (
  input  A,
  input  B,
  output Y
);

  wire transistor_1_out, transistor_4_out;

  Transistor transistor_1 (.in(1'b1), .out(transistor_1_out), .gate(A));
  Transistor transistor_2 (.in(1'b1), .out(transistor_1_out), .gate(B));
  Transistor #(.\type ("n")) transistor_3 (.in(transistor_4_out), .out(transistor_1_out), .gate(A));
  Transistor #(.\type ("n")) transistor_4 (.in(1'b0), .out(transistor_4_out), .gate(B));
  Transistor transistor_5 (.in(1'b1), .out(Y), .gate(transistor_1_out));
  Transistor #(.\type ("n")) transistor_6 (.in(1'b0), .out(Y), .gate(transistor_1_out));

  // Notes on the sheet:
  //   CMOS
  //   - / GND
  //   + / Vdd
endmodule

module RS_Latches (
  input  set,
  input  nuke,
  input  reset,
  input  not_set,
  input  not_reset,
  output not_q,
  output not_q_2,
  output q,
  output q_2,
  output q_3,
  output not_q_3
);

  nor nor_1 (not_q_2, set, q_2);
  nor nor_2 (q_2, not_q_2, reset);
  nand nand_1 (q_3, not_set, not_q_3);
  nand nand_2 (not_q_3, q_3, not_reset);
  nor nor_3 (not_q, nuke, q);
  nor nor_4 (q, not_q, nuke);

  // Notes on the sheet:
  //   RS latch from NAND gates
  //   RS latch from NOR gates
  //   problematic oscillation
endmodule

module RS_Latch (
  input  set,
  input  reset,
  output not_q,
  output q
);

  nor nor_1 (not_q, set, q);
  nor nor_2 (q, not_q, reset);

  // Notes on the sheet:
  //   RS latch from NOR gates
endmodule

module D_Latch (
  input  enable,
  input  data,
  output not_q,
  output q
);

  wire and_1_out, and_2_out, not_1_out;

  and and_1 (and_1_out, enable, data);
  and and_2 (and_2_out, enable, not_1_out);
  not not_1 (not_1_out, data);
  RS_Latch rs_latch_1 (.not_q(not_q), .reset(and_2_out), .set(and_1_out), .q(q));

  // Notes on the sheet:
  //   data -> set,      not data -> reset
endmodule

module D_FlipFlop (
  input  data,
  output not_q,
  output q
);

  wire clock_out, d_latch_1_q, not_1_out;

  Clock clock (.out(clock_out));
  not not_1 (not_1_out, clock_out);
  D_Latch d_latch_1 (.data(data), .enable(not_1_out), .q(d_latch_1_q));  // open: not_q
  D_Latch d_latch_2 (.not_q(not_q), .data(d_latch_1_q), .enable(clock_out), .q(q));

  // Notes on the sheet:
  //   "Schleuse" ist nie komplett durchlässig
endmodule

module mux_4 (
  input  [1:0] in0,
  input  [1:0] in1,
  input  [1:0] in2,
  input  [1:0] in3,
  input  [1:0] select,
  output [1:0] out_6
);

  Hex_Digit_Display hex_digit_display_1 (.value({2'b00, select}));  // open: dp
  Multiplexer #(.select(2), .width(2), .enable("false")) multiplexer_1 (
    .in0(in0), .in1(in1), .in2(in2), .in3(in3), .out(out_6), .sel(select));

  // Notes on the sheet:
  //   Multiplexer schaltet$einen von mehreren$Eingängen durch
endmodule

module dec_2_4 (
  input  [1:0] address,
  input  enable,
  input  [1:0] address_2,
  output out_0,
  output out_1,
  output out_2,
  output out_3,
  output out_0_2,
  output out_1_2,
  output out_2_2,
  output out_3_2
);

  Decoder #(.select(2), .enable("false")) decoder_1 (
    .out0(out_0), .out1(out_1), .out2(out_2), .out3(out_3), .sel(address));
  Decoder #(.select(2)) decoder_2 (
    .out0(out_0_2), .out1(out_1_2), .out2(out_2_2), .out3(out_3_2), .sel(address_2), .en(enable));

  // Notes on the sheet:
  //   Dekoder "dekodiert"$binrären Input auf$einzelne Leitungen
  //   Dekoder mit "enable"$Eingang
endmodule

module mem_cell (
  input  sel,
  input  data,
  input  write_read,
  output out
);

  wire and_1_out, and_2_out, rs_latch_1_q;

  and and_1 (and_1_out, sel, data, write_read);
  and and_2 (and_2_out, sel, ~data, write_read);  // AND_Gate
  RS_Latch rs_latch_1 (.reset(and_2_out), .set(and_1_out), .q(rs_latch_1_q));  // open: not_q
  and and_3 (out, sel, rs_latch_1_q);

  // Notes on the sheet:
  //   1-bit addressierbare Speicherzelle
  //   z.B. mit RS-Latch$oder auch mit$dynamischem Speicher$aus Kondensator
endmodule

// register
module register_4 (
  input  [3:0] data_in,
  input  sel,
  input  write_read,
  output [3:0] data_out
);

  mem_cell mem_cell_1 (.sel(sel), .data(data_in[3]), .write_read(write_read), .out(data_out[3]));
  mem_cell mem_cell_2 (.sel(sel), .data(data_in[2]), .write_read(write_read), .out(data_out[2]));
  mem_cell mem_cell_3 (.sel(sel), .data(data_in[1]), .write_read(write_read), .out(data_out[1]));
  mem_cell mem_cell_4 (.sel(sel), .data(data_in[0]), .write_read(write_read), .out(data_out[0]));
  Hex_Digit_Display hex_digit_display_1 (.value(data_in));  // open: dp
  Hex_Digit_Display hex_digit_display_2 (.value(data_out));  // open: dp

  // Notes on the sheet:
  //   4-bit Speicherzelle
endmodule

// MEM 4x4
module register_file (
  input  [3:0] data_in,
  input  [1:0] adr,
  input  write_read,
  output [3:0] data_out
);

  wire decoder_1_out0, decoder_1_out1, decoder_1_out2, decoder_1_out3;
  wire [3:0] register_4_1_data_out, register_4_2_data_out, register_4_3_data_out, register_4_4_data_out;

  Hex_Digit_Display hex_digit_display_1 (.value(data_in));  // open: dp
  Decoder #(.select(2), .enable("false")) decoder_1 (
    .out0(decoder_1_out0), .out1(decoder_1_out1), .out2(decoder_1_out2), .out3(decoder_1_out3), .sel(adr));
  register_4 register_4_1 (
    .sel(decoder_1_out3), .write_read(write_read), .data_in(data_in), .data_out(register_4_1_data_out));
  register_4 register_4_2 (
    .sel(decoder_1_out2), .write_read(write_read), .data_in(data_in), .data_out(register_4_2_data_out));
  register_4 register_4_3 (
    .sel(decoder_1_out1), .write_read(write_read), .data_in(data_in), .data_out(register_4_3_data_out));
  register_4 register_4_4 (
    .sel(decoder_1_out0), .write_read(write_read), .data_in(data_in), .data_out(register_4_4_data_out));
  Hex_Digit_Display hex_digit_display_2 (.value(data_out));  // open: dp
  Multiplexer #(.select(2), .width(4), .enable("false")) multiplexer_1 (
    .in0(register_4_4_data_out), .in1(register_4_3_data_out), .in2(register_4_2_data_out),
    .in3(register_4_1_data_out), .out(data_out), .sel(adr));

  // Notes on the sheet:
  //   4x 4-bit Speicherzelle
  //   bestehend aus eigenen 4-bit Speicherzellen
endmodule

module register_file_2 (
  input  [3:0] data_in,
  input  [1:0] adr,
  input  write_read,
  output [3:0] data_out
);

  wire decoder_1_out0, decoder_1_out1, decoder_1_out2, decoder_1_out3;
  wire [3:0] register_1_q, register_2_q, register_3_q, register_4_q;

  Hex_Digit_Display hex_digit_display_1 (.value(data_in));  // open: dp
  Decoder #(.select(2), .enable("false")) decoder_1 (
    .out0(decoder_1_out0), .out1(decoder_1_out1), .out2(decoder_1_out2), .out3(decoder_1_out3), .sel(adr));
  Register #(.width(4), .trigger("high"), .Select("low")) register_1 (
    .D(data_in), .en(decoder_1_out0), .Q(register_1_q), .clk(write_read));  // open: clr
  Register #(.width(4), .trigger("high"), .Select("low")) register_2 (
    .D(data_in), .en(decoder_1_out1), .Q(register_2_q), .clk(write_read));  // open: clr
  Register #(.width(4), .trigger("high"), .Select("low")) register_3 (
    .D(data_in), .en(decoder_1_out2), .Q(register_3_q), .clk(write_read));  // open: clr
  Register #(.width(4), .trigger("high"), .Select("low")) register_4 (
    .D(data_in), .en(decoder_1_out3), .Q(register_4_q), .clk(write_read));  // open: clr
  Hex_Digit_Display hex_digit_display_2 (.value(data_out));  // open: dp
  Multiplexer #(.select(2), .width(4), .enable("false")) multiplexer_1 (
    .in0(register_1_q), .in1(register_2_q), .in2(register_3_q), .in3(register_4_q), .out(data_out), .sel(adr));

  // Notes on the sheet:
  //   4x 4-bit Speicherzelle
  //   bestehend aus LogiSim 4-bit Speicherzellen
endmodule

module mem (
  input  [1:0] adr,
  input  adr_w,
  input  [3:0] data_in,
  input  write_read,
  input  memory_select,
  input  mdr_write,
  output [3:0] data_out
);

  wire [1:0] MAR_data_out;
  wire [3:0] multiplexer_1_out, register_file_1_data_out;
  wire [3:2] MAR_data_out_2;

  Hex_Digit_Display hex_digit_display_1 (.value({MAR_data_out_2, MAR_data_out}));  // open: dp
  register_4 MAR (.sel(1'b1), .write_read(adr_w), .data_in({2'b00, adr}), .data_out({MAR_data_out_2, MAR_data_out}));
  register_file register_file_1 (
    .write_read(write_read), .data_in(data_out), .adr(MAR_data_out), .data_out(register_file_1_data_out));
  Multiplexer #(.width(4), .enable("false")) multiplexer_1 (
    .in0(data_in), .in1(register_file_1_data_out), .out(multiplexer_1_out), .sel(memory_select));
  register_4 register_4_1 (.sel(1'b1), .write_read(mdr_write), .data_in(multiplexer_1_out), .data_out(data_out));
  Hex_Digit_Display hex_digit_display_2 (.value(register_file_1_data_out));  // open: dp
  Hex_Digit_Display hex_digit_display_3 (.value(data_out));  // open: dp

  // Notes on the sheet:
  //   Memory Address
  //   Memory Data
endmodule

module mem_2 (
  input  write,
  input  read
);

  wire [3:0] MAR_q, MDR_q, RAM_data;

  Register #(.width(4), .trigger("high"), .Select("low")) MAR (.Q(MAR_q));  // open: D, en, clk, clr
  RAM #(.addrWidth(4), .dataWidth(4), .bus("separate"), .Select("high"), .simpleMode("false")) RAM (
    .addr(MAR_q), .din(MDR_q), .data(RAM_data), .str(write), .clk(write), .ld(read));  // open: sel, clr
  Register #(.width(4), .trigger("high"), .Select("low")) MDR (.D(RAM_data), .Q(MDR_q), .clk(1'b1));  // open: en, clr

  // Notes on the sheet:
  //   Mode
endmodule

module RAM___MAR___MDR (
  input  in_1,
  input  Write,
  input  Read,
  input  clock
);

  wire [7:0] ram_1_data, register_1_q, register_2_q;

  Register #(.trigger("high"), .Select("low")) register_1 (.en(1'b1), .Q(register_1_q), .clk(1'b1));  // open: D, clr
  Register #(.trigger("high"), .Select("low")) register_2 (
    .D(ram_1_data), .en(1'b1), .Q(register_2_q), .clk(in_1));  // open: clr
  RAM #(.bus("separate"), .Select("high"), .simpleMode("false")) ram_1 (
    .addr(register_1_q), .din(register_2_q), .data(ram_1_data), .str(Write), .clk(clock), .ld(Read));  // open: sel, clr

  // Notes on the sheet:
  //   MAR
  //   MDR
endmodule

module RS_NAND__no_sim (
  input  not_set,
  input  not_reset,
  output not_Q,
  output Q
);

  wire transistor_3_out, transistor_6_out;

  Transistor transistor_1 (.in(1'b1), .out(not_Q), .gate(not_set));
  Transistor #(.\type ("n")) transistor_2 (.in(transistor_3_out), .out(not_Q), .gate(not_set));
  Transistor #(.\type ("n")) transistor_3 (.in(1'b0), .out(transistor_3_out), .gate(Q));
  Transistor transistor_4 (.in(1'b1), .out(Q), .gate(not_Q));
  Transistor #(.\type ("n")) transistor_5 (.in(transistor_6_out), .out(Q), .gate(not_Q));
  Transistor #(.\type ("n")) transistor_6 (.in(1'b0), .out(transistor_6_out), .gate(not_reset));
  Transistor transistor_7 (.in(1'b1), .out(not_Q), .gate(Q));
  Transistor transistor_8 (.in(1'b1), .out(Q), .gate(not_reset));
endmodule

module inverted_CMOS_OR (
  input  A,
  input  B,
  output Y
);

  wire transistor_4_out;

  Transistor #(.\type ("n")) transistor_1 (.in(1'b1), .out(Y), .gate(A));
  Transistor #(.\type ("n")) transistor_2 (.in(1'b1), .out(Y), .gate(B));
  Transistor transistor_3 (.in(transistor_4_out), .out(Y), .gate(A));
  Transistor transistor_4 (.in(1'b0), .out(transistor_4_out), .gate(B));

  // Notes on the sheet:
  //   CMOS
  //   - / GND
  //   + / Vdd
  //   theoretisch möglich$aber praktisch zu $hohe Verluste
endmodule

module mem_cell_CMOS__osc (
  input  Write_Line,
  input  Inv_Bit_Line,
  input  Bit_Line,
  output out_4,
  output out_5
);

  wire transistor_1_out, transistor_3_out, transistor_4_out;

  Transistor #(.\type ("n")) transistor_1 (.in(Inv_Bit_Line), .out(transistor_1_out), .gate(Write_Line));
  Transistor #(.gate("br")) transistor_2 (.in(1'b1), .out(transistor_1_out), .gate(transistor_4_out));
  Transistor #(.\type ("n"), .gate("br")) transistor_3 (
    .in(transistor_1_out), .out(transistor_3_out), .gate(transistor_4_out));
  Transistor transistor_4 (.in(1'b1), .out(transistor_4_out), .gate(transistor_1_out));
  Transistor #(.\type ("n")) transistor_5 (.in(Bit_Line), .out(transistor_4_out), .gate(Write_Line));
  Transistor #(.\type ("n")) transistor_6 (.in(transistor_4_out), .out(transistor_3_out), .gate(transistor_1_out));

  assign out_4 = Inv_Bit_Line;
  assign out_5 = Bit_Line;
  // also tied to GND on the sheet: transistor_3_out
endmodule
