// Logisim project Übung6 (1).circ as structural Verilog
module MUX2 (
  input  D0,
  input  D1,
  input  s,
  output out_4
);

  wire and_1_out, and_2_out, not_1_out;

  not not_1 (not_1_out, s);
  and and_1 (and_1_out, D0, not_1_out);
  and and_2 (and_2_out, D1, s);
  or or_1 (out_4, and_1_out, and_2_out);
endmodule

module MUX4 (
  input  D0,
  input  D1,
  input  D2,
  input  D3,
  input  s0,
  input  s1,
  output y
);

  wire and_1_out, and_2_out, and_3_out, and_4_out, not_1_out, not_2_out, not_3_out, not_4_out;

  not not_1 (not_1_out, s0);
  not not_2 (not_2_out, s1);
  not not_3 (not_3_out, s0);
  not not_4 (not_4_out, s1);
  and and_1 (and_1_out, D0, not_1_out, not_4_out);
  and and_2 (and_2_out, D1, s0, not_2_out);
  and and_3 (and_3_out, D2, not_3_out, s1);
  and and_4 (and_4_out, D3, s0, s1);
  or or_1 (y, and_1_out, and_2_out, and_3_out, and_4_out);
endmodule

module FA (
  input  Cin,
  input  x,
  input  y,
  output Cout,
  output s
);

  wire and_1_out, and_2_out, xor_1_out;

  xor xor_1 (xor_1_out, x, y);
  and and_1 (and_1_out, x, y);
  and and_2 (and_2_out, xor_1_out, Cin);
  or or_1 (Cout, and_1_out, and_2_out);
  xor xor_2 (s, xor_1_out, Cin);
endmodule

module MUX4B (
  input  D0,
  input  D1,
  input  D2,
  input  D3,
  input  s0,
  input  s1,
  output y
);

  wire mux2_1_out_4, mux2_2_out_4;

  MUX2 mux2_1 (.D0(D0), .D1(D1), .s(s0), .out_4(mux2_1_out_4));
  MUX2 mux2_2 (.D0(D2), .D1(D3), .s(s0), .out_4(mux2_2_out_4));
  MUX2 mux2_3 (.D0(mux2_1_out_4), .D1(mux2_2_out_4), .s(s1), .out_4(y));
endmodule

module ADD4 (
  input  x3,
  input  x2,
  input  x1,
  input  x0,
  input  y3,
  input  y2,
  input  y1,
  input  y0,
  output c3,
  output s3,
  output s2,
  output s1,
  output s0
);

  wire fa_2_cout, fa_3_cout, fa_4_cout;

  FA fa_1 (.Cout(c3), .Cin(fa_3_cout), .x(x3), .y(y3), .s(s3));
  FA fa_2 (.Cout(fa_2_cout), .Cin(fa_4_cout), .x(x1), .y(y1), .s(s1));
  FA fa_3 (.Cout(fa_3_cout), .Cin(fa_2_cout), .x(x2), .y(y2), .s(s2));
  FA fa_4 (.Cout(fa_4_cout), .Cin(1'b0), .x(x0), .y(y0), .s(s0));
endmodule

module Add4New_4Bit (
  input  [3:0] x,
  input  [3:0] y,
  output c3,
  output [3:0] out_4
);

  wire fa_2_cout, fa_3_cout, fa_4_cout;

  Hex_Digit_Display hex_digit_display_1 (.value(x));  // open: dp
  FA fa_1 (.Cout(c3), .Cin(fa_2_cout), .x(x[3]), .y(y[3]), .s(out_4[3]));
  FA fa_2 (.Cout(fa_2_cout), .Cin(fa_3_cout), .x(x[2]), .y(y[2]), .s(out_4[2]));
  FA fa_3 (.Cout(fa_3_cout), .Cin(fa_4_cout), .x(x[1]), .y(y[1]), .s(out_4[1]));
  Hex_Digit_Display hex_digit_display_2 (.value(y));  // open: dp
  FA fa_4 (.Cout(fa_4_cout), .Cin(1'b0), .x(x[0]), .y(y[0]), .s(out_4[0]));
  Hex_Digit_Display hex_digit_display_3 (.value(out_4));  // open: dp
endmodule

module LU1 (
  input  a,
  input  b,
  input  s1,
  input  s0,
  output f
);

  wire and_1_out, not_1_out, or_1_out, xor_1_out;

  and and_1 (and_1_out, a, b);
  or or_1 (or_1_out, a, b);
  not not_1 (not_1_out, a);
  xor xor_1 (xor_1_out, a, b);
  MUX4 mux4_1 (.D0(and_1_out), .D1(or_1_out), .D2(not_1_out), .D3(xor_1_out), .s0(s0), .s1(s1), .y(f));
endmodule

module LU (
  input  s0,
  input  a,
  input  b,
  input  s1
);
endmodule
