// Logisim project 4bitRegister+4bitAdder.circ as structural Verilog
module RS_Latch (
  input  S,
  input  R,
  output out_3
);

  wire nor_1_out;

  nor nor_1 (nor_1_out, S, out_3);
  nor nor_2 (out_3, nor_1_out, R);
endmodule

module D_Latch (
  input  D,
  input  c,
  output out_3
);

  wire and_1_out, and_2_out, nor_1_out, not_1_out;

  and and_1 (and_1_out, D, c);
  not not_1 (not_1_out, D);
  and and_2 (and_2_out, c, not_1_out);
  nor nor_1 (nor_1_out, and_1_out, out_3);
  nor nor_2 (out_3, nor_1_out, and_2_out);
endmodule

module D_FlipFlop (
  input  C,
  input  D,
  output out_3
);

  wire d_latch_1_out_3, not_1_out;

  D_Latch d_latch_1 (.D(D), .c(C), .out_3(d_latch_1_out_3));
  not not_1 (not_1_out, C);
  D_Latch d_latch_2 (.D(d_latch_1_out_3), .c(not_1_out), .out_3(out_3));

  // Notes on the sheet:
  //   D-Flip-Flop:
endmodule

module MUX2 (
  input  c,
  input  a,
  input  b,
  output out_4
);

  wire and_1_out, and_2_out, not_1_out;

  and and_1 (and_1_out, a, not_1_out);
  not not_1 (not_1_out, c);
  and and_2 (and_2_out, c, b);
  or or_1 (out_4, and_1_out, and_2_out);
endmodule

module MUX4 (
  input  c1,
  input  c0,
  input  a,
  input  b,
  input  c,
  input  d,
  output out_7
);

  wire mux2_1_out_4, mux2_2_out_4;

  MUX2 mux2_1 (.a(a), .b(b), .out_4(mux2_1_out_4), .c(c0));
  MUX2 mux2_2 (.a(c), .b(d), .out_4(mux2_2_out_4), .c(c0));
  MUX2 mux2_3 (.a(mux2_1_out_4), .b(mux2_2_out_4), .out_4(out_7), .c(c1));
endmodule

module Schaltfunktion_mit_MUX (
  input  x,
  input  y,
  input  in_3,
  input  in_4,
  output out_5
);

  MUX4 mux4_1 (.a(in_3), .b(in_4), .c(in_4), .d(in_3), .out_7(out_5), .c1(x), .c0(y));

  // Notes on the sheet:
  //   XOR:
  //   Funktionsergebnisse:
endmodule

module _4_2_Encoder (
  input  x0,
  input  x1,
  input  x2,
  input  x3,
  output z0,
  output z1
);

  wire not_1_out, not_2_out, not_3_out;

  not not_1 (not_1_out, x2);
  not not_2 (not_2_out, x0);
  not not_3 (not_3_out, x1);
  and and_1 (z0, not_1_out, not_2_out);
  and and_2 (z1, not_2_out, not_3_out);
endmodule

module Halbaddierer (
  input  x,
  input  y,
  output s,
  output c_out
);

  wire and_1_out, and_2_out, not_1_out, not_2_out;

  not not_1 (not_1_out, y);
  not not_2 (not_2_out, x);
  and and_1 (and_1_out, x, not_1_out);
  and and_2 (and_2_out, not_2_out, y);
  and and_3 (c_out, x, y);
  or or_1 (s, and_1_out, and_2_out);
endmodule

module Halbaddierer1 (
  input  x,
  input  y,
  output s,
  output c_out
);

  xor xor_1 (s, x, y);
  and and_1 (c_out, x, y);
endmodule

module Full_Adder (
  input  x,
  input  y,
  input  cin,
  output s,
  output cout
);

  wire halbaddierer1_1_c_out, halbaddierer1_1_s, halbaddierer1_2_c_out;

  Halbaddierer1 halbaddierer1_1 (.x(x), .y(y), .s(halbaddierer1_1_s), .c_out(halbaddierer1_1_c_out));
  or or_1 (cout, halbaddierer1_1_c_out, halbaddierer1_2_c_out);
  Halbaddierer1 halbaddierer1_2 (.x(halbaddierer1_1_s), .y(cin), .s(s), .c_out(halbaddierer1_2_c_out));
endmodule

module FA_Kaskade (
  input  [3:0] in_1,
  input  [3:0] in_2,
  input  neg,
  output cout_Flag,
  output [3:0] out_5
);

  wire full_adder_2_cout, full_adder_3_cout, full_adder_4_cout, xor_1_out, xor_2_out, xor_3_out, xor_4_out;

  Hex_Digit_Display hex_digit_display_1 (.value(in_1));  // open: dp
  xor xor_1 (xor_1_out, in_2[3], neg);
  Full_Adder full_adder_1 (.s(out_5[3]), .cout(cout_Flag), .x(xor_1_out), .y(in_1[3]), .cin(full_adder_2_cout));
  xor xor_2 (xor_2_out, in_2[2], neg);
  Full_Adder full_adder_2 (.s(out_5[2]), .cout(full_adder_2_cout), .x(xor_2_out), .y(in_1[2]), .cin(full_adder_3_cout));
  xor xor_3 (xor_3_out, in_2[1], neg);
  Full_Adder full_adder_3 (.s(out_5[1]), .cout(full_adder_3_cout), .x(xor_3_out), .y(in_1[1]), .cin(full_adder_4_cout));
  Hex_Digit_Display hex_digit_display_2 (.value(in_2));  // open: dp
  xor xor_4 (xor_4_out, in_2[0], neg);
  Full_Adder full_adder_4 (.s(out_5[0]), .cout(full_adder_4_cout), .x(xor_4_out), .y(in_1[0]), .cin(neg));
  Hex_Digit_Display hex_digit_display_3 (.value(out_5));  // open: dp
endmodule

module SRAM (
  input  select,
  input  data,
  input  write_read,
  output out_4
);

  wire and_1_out, and_2_out, not_1_out, rs_latch_1_out_3;

  and and_1 (and_1_out, select, data, write_read);
  and and_2 (and_2_out, select, not_1_out, write_read);
  not not_1 (not_1_out, data);
  RS_Latch rs_latch_1 (.S(and_1_out), .R(and_2_out), .out_3(rs_latch_1_out_3));
  and and_3 (out_4, select, rs_latch_1_out_3);
endmodule

module _4BitRegister (
  input  [3:0] in_1,
  input  select,
  input  write,
  output [3:0] out_4
);

  SRAM sram_1 (.select(select), .data(in_1[3]), .write_read(write), .out_4(out_4[3]));
  Hex_Digit_Display hex_digit_display_1 (.value(in_1));  // open: dp
  SRAM sram_2 (.select(select), .data(in_1[2]), .write_read(write), .out_4(out_4[2]));
  SRAM sram_3 (.select(select), .data(in_1[1]), .write_read(write), .out_4(out_4[1]));
  Hex_Digit_Display hex_digit_display_2 (.value(out_4));  // open: dp
  SRAM sram_4 (.select(select), .data(in_1[0]), .write_read(write), .out_4(out_4[0]));
endmodule

module Dec2_4 (
  input  [1:0] in_1,
  input  enable,
  output [3:0] out_3
);

  wire not_1_out, not_2_out, not_3_out, not_4_out;

  not not_1 (not_1_out, in_1[1]);
  and and_1 (out_3[0], not_1_out, enable, not_2_out);
  not not_2 (not_2_out, in_1[0]);
  not not_3 (not_3_out, in_1[1]);
  and and_2 (out_3[1], not_3_out, enable, in_1[0]);
  and and_3 (out_3[2], in_1[1], enable, not_4_out);
  not not_4 (not_4_out, in_1[0]);
  and and_4 (out_3[3], in_1[1], enable, in_1[0]);
endmodule

module multiRegister (
  input  [3:0] Input,
  input  [1:0] Adresse,
  input  write,
  output [3:0] out_4,
  output [3:0] out_5
);

  wire [3:0] dec2_4_1_out_3, n4bitregister_1_out_4, n4bitregister_2_out_4, n4bitregister_3_out_4;

  Dec2_4 dec2_4_1 (.out_3(dec2_4_1_out_3), .in_1(Adresse), .enable(1'b1));
  _4BitRegister u_4bitregister_1 (
    .select(dec2_4_1_out_3[3]), .write(write), .in_1(Input), .out_4(n4bitregister_1_out_4));
  _4BitRegister u_4bitregister_2 (
    .select(dec2_4_1_out_3[2]), .write(write), .in_1(Input), .out_4(n4bitregister_2_out_4));
  _4bit_MUX4 u_4bit_mux4_1 (
    .a(out_4), .b(n4bitregister_3_out_4), .c(n4bitregister_2_out_4), .d(n4bitregister_1_out_4),
    .out_6(out_5), .Adress(Adresse));
  _4BitRegister u_4bitregister_3 (
    .select(dec2_4_1_out_3[1]), .write(write), .in_1(Input), .out_4(n4bitregister_3_out_4));
  _4BitRegister u_4bitregister_4 (.select(dec2_4_1_out_3[0]), .write(write), .in_1(Input), .out_4(out_4));
  Hex_Digit_Display hex_digit_display_1 (.value(out_5));  // open: dp
endmodule

module _4bit_MUX4 (
  input  [1:0] Adress,
  input  [3:0] a,
  input  [3:0] b,
  input  [3:0] c,
  input  [3:0] d,
  output [3:0] out_6
);

  wire [3:0] n4bit_mux2_1_out, n4bit_mux2_2_out;

  _4bit_MUX2 u_4bit_mux2_1 (.out(n4bit_mux2_1_out), .b(b), .a(a), .Adress(Adress[0]));
  _4bit_MUX2 u_4bit_mux2_2 (.out(n4bit_mux2_2_out), .b(d), .a(c), .Adress(Adress[0]));
  _4bit_MUX2 u_4bit_mux2_3 (.out(out_6), .b(n4bit_mux2_2_out), .a(n4bit_mux2_1_out), .Adress(Adress[1]));
endmodule

module _4bit_MUX2 (
  input  [3:0] b,
  input  [3:0] a,
  input  Adress,
  output [3:0] out
);

  MUX2 mux2_1 (.a(a[0]), .b(b[0]), .out_4(out[0]), .c(Adress));
  MUX2 mux2_2 (.a(a[1]), .b(b[1]), .out_4(out[1]), .c(Adress));
  MUX2 mux2_3 (.a(a[2]), .b(b[2]), .out_4(out[2]), .c(Adress));
  MUX2 mux2_4 (.a(a[3]), .b(b[3]), .out_4(out[3]), .c(Adress));
endmodule

module Dec3_8 (
  input  [2:0] in_1,
  output [7:0] out_2
);

  wire not_1_out;

  not not_1 (not_1_out, in_1[2]);
  Dec2_4 dec2_4_1 (.out_3(out_2[3:0]), .in_1(in_1[1:0]), .enable(not_1_out));
  Dec2_4 dec2_4_2 (.out_3(out_2[7:4]), .in_1(in_1[1:0]), .enable(in_1[2]));
endmodule
